// Logisim project RAM.circ as structural Verilog: 1 circuit, main circuit RAM
module RAM (
  input  [9:0] ADDR,
  input  [9:0] ADDR_2,
  input  [9:0] ADDR_3,
  input  [9:0] ADDR_4,
  input  [31:0] in_5,
  input  [9:0] ADDR_5,
  input  in_7,
  input  in_8,
  input  [31:0] in_9,
  input  in_10,
  input  in_11,
  input  in_12,
  input  in_13,
  input  [31:0] in_14,
  input  in_15,
  input  [31:0] in_16,
  input  [31:0] in_17,
  input  [9:0] ADDR_6,
  input  [9:0] ADDR_7,
  input  [9:0] ADDR_8,
  input  [9:0] ADDR_9,
  input  [9:0] ADDR_10,
  input  [31:0] in_23,
  input  in_24,
  input  in_25,
  input  in_26,
  input  [31:0] in_27,
  input  in_28,
  input  in_29,
  input  [31:0] in_30,
  input  [31:0] in_31,
  input  [31:0] in_32,
  input  [9:0] ADDR_11,
  input  [9:0] ADDR_12,
  input  [9:0] ADDR_13,
  input  [9:0] ADDR_14,
  input  [31:0] in_37,
  input  [9:0] ADDR_15,
  input  in_39,
  input  in_40,
  input  [31:0] in_41,
  input  in_42,
  input  in_43,
  input  in_44,
  input  [31:0] in_45,
  input  [31:0] in_46,
  input  [9:0] ADDR_16,
  input  [9:0] ADDR_17,
  input  [9:0] ADDR_18,
  input  [9:0] ADDR_19,
  input  [31:0] in_51,
  input  [9:0] ADDR_20,
  input  [31:0] in_53,
  input  in_54,
  input  in_55,
  input  in_56,
  input  in_57,
  input  in_58,
  input  [31:0] in_59,
  input  [31:0] in_60,
  input  [31:0] in_61,
  input  [31:0] in_62,
  output [31:0] out_63,
  output [31:0] out_64,
  output [31:0] out_65,
  output [31:0] out_66,
  output [31:0] out_67,
  output [31:0] out_68,
  output [31:0] out_69,
  output [31:0] out_70,
  output [31:0] out_71,
  output [31:0] out_72,
  output [31:0] out_73,
  output [31:0] out_74,
  output [31:0] out_75,
  output [31:0] out_76,
  output [31:0] out_77,
  output [31:0] out_78,
  output [31:0] out_79,
  output [31:0] out_80,
  output [31:0] out_81,
  output [31:0] out_82
);

  RAM_part #(.addrWidth(10), .dataWidth(32), .bus("separate"), .Select("high")) _0 (
    .addr(ADDR_5), .din(in_5), .data(out_63), .str(in_8), .clk(in_7), .clr(in_15));  // open: sel, ld
  RAM_part #(.addrWidth(10), .dataWidth(32), .bus("separate"), .Select("high")) _5 (
    .addr(ADDR_10), .din(in_23), .data(out_68), .str(in_24), .clk(in_7), .clr(in_15));  // open: sel, ld
  RAM_part #(.addrWidth(10), .dataWidth(32), .bus("separate"), .Select("high")) _10 (
    .addr(ADDR_15), .din(in_37), .data(out_73), .str(in_39), .clk(in_7), .clr(in_15));  // open: sel, ld
  RAM_part #(.addrWidth(10), .dataWidth(32), .bus("separate"), .Select("high")) _15 (
    .addr(ADDR_20), .din(in_53), .data(out_78), .str(in_54), .clk(in_7), .clr(in_15));  // open: sel, ld
  RAM_part #(.addrWidth(10), .dataWidth(32), .bus("separate"), .Select("high")) _1 (
    .addr(ADDR_4), .din(in_9), .data(out_64), .str(in_10), .clk(in_7), .clr(in_15));  // open: sel, ld
  RAM_part #(.addrWidth(10), .dataWidth(32), .bus("separate"), .Select("high")) _6 (
    .addr(ADDR_9), .din(in_27), .data(out_69), .str(in_25), .clk(in_7), .clr(in_15));  // open: sel, ld
  RAM_part #(.addrWidth(10), .dataWidth(32), .bus("separate"), .Select("high")) _11 (
    .addr(ADDR_14), .din(in_41), .data(out_74), .str(in_40), .clk(in_7), .clr(in_15));  // open: sel, ld
  RAM_part #(.addrWidth(10), .dataWidth(32), .bus("separate"), .Select("high")) _16 (
    .addr(ADDR_19), .din(in_59), .data(out_79), .str(in_55), .clk(in_7), .clr(in_15));  // open: sel, ld
  RAM_part #(.addrWidth(10), .dataWidth(32), .bus("separate"), .Select("high")) _2 (
    .addr(ADDR_3), .din(in_14), .data(out_65), .str(in_11), .clk(in_7), .clr(in_15));  // open: sel, ld
  RAM_part #(.addrWidth(10), .dataWidth(32), .bus("separate"), .Select("high")) _7 (
    .addr(ADDR_8), .din(in_30), .data(out_70), .str(in_26), .clk(in_7), .clr(in_15));  // open: sel, ld
  RAM_part #(.addrWidth(10), .dataWidth(32), .bus("separate"), .Select("high")) _12 (
    .addr(ADDR_13), .din(in_45), .data(out_75), .str(in_42), .clk(in_7), .clr(in_15));  // open: sel, ld
  RAM_part #(.addrWidth(10), .dataWidth(32), .bus("separate"), .Select("high")) _17 (
    .addr(ADDR_18), .din(in_60), .data(out_80), .str(in_56), .clk(in_7), .clr(in_15));  // open: sel, ld
  RAM_part #(.addrWidth(10), .dataWidth(32), .bus("separate"), .Select("high")) _3 (
    .addr(ADDR_2), .din(in_16), .data(out_66), .str(in_12), .clk(in_7), .clr(in_15));  // open: sel, ld
  RAM_part #(.addrWidth(10), .dataWidth(32), .bus("separate"), .Select("high")) _8 (
    .addr(ADDR_7), .din(in_31), .data(out_71), .str(in_28), .clk(in_7), .clr(in_15));  // open: sel, ld
  RAM_part #(.addrWidth(10), .dataWidth(32), .bus("separate"), .Select("high")) _13 (
    .addr(ADDR_12), .din(in_46), .data(out_76), .str(in_43), .clk(in_7), .clr(in_15));  // open: sel, ld
  RAM_part #(.addrWidth(10), .dataWidth(32), .bus("separate"), .Select("high")) _18 (
    .addr(ADDR_17), .din(in_61), .data(out_81), .str(in_57), .clk(in_7), .clr(in_15));  // open: sel, ld
  RAM_part #(.addrWidth(10), .dataWidth(32), .bus("separate"), .Select("high")) _4 (
    .addr(ADDR), .din(in_17), .data(out_67), .str(in_13), .clk(in_7), .clr(in_15));  // open: sel, ld
  RAM_part #(.addrWidth(10), .dataWidth(32), .bus("separate"), .Select("high")) _9 (
    .addr(ADDR_6), .din(in_32), .data(out_72), .str(in_29), .clk(in_7), .clr(in_15));  // open: sel, ld
  RAM_part #(.addrWidth(10), .dataWidth(32), .bus("separate"), .Select("high")) _14 (
    .addr(ADDR_11), .din(in_51), .data(out_77), .str(in_44), .clk(in_7), .clr(in_15));  // open: sel, ld
  RAM_part #(.addrWidth(10), .dataWidth(32), .bus("separate"), .Select("high")) _19 (
    .addr(ADDR_16), .din(in_62), .data(out_82), .str(in_58), .clk(in_7), .clr(in_15));  // open: sel, ld
endmodule
