// Logisim project main.circ as structural Verilog: 28 circuits, main circuit ◇单周期MIPS
module \单周期MIPS  (
  input  IR1,
  input  IR2,
  input  IR3,
  output RegWrite,
  output MemWrite,
  output [31:0] PC,
  output [31:0] IR,
  output [31:0] RDin,
  output [31:0] MDin,
  output [31:0] LedData
);

  wire and_1_out, and_2_out, and_3_out, and_4_out, CLK, clock_2_out, comparator_1_eq, comparator_1_lt,
       comparator_2_eq, comparator_3_eq, d_ff_1_q, en, Go, IR1_t, IR2_t, IR3_t, IRA, IRB, IRC,
       mips_alu_1_equal, nand_1_out, or_4_out, SB, SignedExt, sys, W1, W2, W3, \单周期硬布线控制器_1_alu_src ,
       \单周期硬布线控制器_1_beq , \单周期硬布线控制器_1_bltz , \单周期硬布线控制器_1_bne , \单周期硬布线控制器_1_jal , \单周期硬布线控制器_1_jmp ,
       \单周期硬布线控制器_1_jr , \单周期硬布线控制器_1_memtoreg , \单周期硬布线控制器_1_regdst ;
  wire [3:0] \单周期硬布线控制器_1_alu_op ;
  wire [4:0] multiplexer_4_out, multiplexer_5_out, multiplexer_6_out, multiplexer_8_out;
  wire [12:0] CNT_num;
  wire [15:0] \总周期数 ;
  wire [31:0] a0, adder_1_out, adder_2_out, AIN, bit_extender_1_out, bit_extender_2_out, DIN, DIN1, DOUT,
       multiplexer_1_out, multiplexer_2_out, multiplexer_3_out, multiplexer_7_out, multiplexer_11_out,
       multiplexer_12_out, multiplexer_15_out, shifter_1_out;

  Clock #(.highDuration(1), .lowDuration(1)) clock_1 ();  // open: out
  Button _1 (.out(IRA));
  Button _2 (.out(IRB));
  Button _3 (.out(IRC));
  Button \u_继续运行  (.out(Go));
  LED #(.active("true")) led_1 (.in(W1));
  LED #(.active("true")) led_2 (.in(W2));
  LED #(.active("true")) led_3 (.in(W3));
  D_Flip_Flop #(.trigger("high"), .Pre_Clr_Positions("LEGACY"), .NegatePresetClear("false"), .enable("true"), .NewFFLayout("false")) d_ff_1 (.Q(d_ff_1_q));  // open: clk, D, Qn, preset, en, reset
  Hex_Digit_Display hex_digit_display_1 (.value(LedData[31:28]));  // open: dp
  // Probe on 13'ha
  Clock #(.highDuration(1), .lowDuration(1)) clock_2 (.out(clock_2_out));
  Multiplexer #(.select(1), .width(32), .disabled("Z"), .enable("false")) multiplexer_1 (
    .in0(adder_1_out), .in1(adder_2_out), .out(multiplexer_1_out), .sel(or_4_out));
  Multiplexer #(.select(1), .width(32), .disabled("Z"), .enable("false")) multiplexer_2 (
    .in0({adder_1_out[31:28], IR[25:0], 2'b00}), .in1(a0), .out(multiplexer_2_out), .sel(\单周期硬布线控制器_1_jr ));
  Hex_Digit_Display hex_digit_display_2 (.value(LedData[23:20]));  // open: dp
  Hex_Digit_Display hex_digit_display_3 (.value(LedData[27:24]));  // open: dp
  Comparator #(.width(13), .mode("twosComplement")) comparator_1 (
    .a(CNT_num), .b(13'ha), .eq(comparator_1_eq), .lt(comparator_1_lt));  // open: gt
  Multiplexer #(.select(1), .width(32), .disabled("Z"), .enable("false")) multiplexer_3 (
    .in0(multiplexer_1_out), .in1(multiplexer_2_out), .out(multiplexer_3_out), .sel(\单周期硬布线控制器_1_jmp ));
  Hex_Digit_Display hex_digit_display_4 (.value(LedData[15:12]));  // open: dp
  Hex_Digit_Display hex_digit_display_5 (.value(LedData[19:16]));  // open: dp
  nand nand_1 (nand_1_out, d_ff_1_q, comparator_1_eq);
  Counter #(.width(13), .max('h1fff), .ongoal("stay"), .trigger("rising"), .behavior("old")) counter_1 (
    .count(comparator_1_lt), .Q(CNT_num), .clk(clock_2_out));  // open: load, D, carry, clr, preset
  Register #(.width(32), .trigger("rising"), .Select("low")) u_PC (
    .D(multiplexer_3_out), .en(en), .Q(PC), .clk(CLK));  // open: clr
  Hex_Digit_Display hex_digit_display_6 (.value(LedData[7:4]));  // open: dp
  Hex_Digit_Display hex_digit_display_7 (.value(LedData[11:8]));  // open: dp
  // Probe on \总周期数 
  assign CLK = nand_1_out ? clock_2_out : 1'bz;  // Controlled_Buffer controlled_buffer_1
  Pull_Resistor #(.pull(1)) pull_resistor_1 (.node(CLK));
  Hex_Digit_Display hex_digit_display_8 (.value(LedData[3:0]));  // open: dp
  Adder #(.width(32)) adder_1 (.a(PC), .b(32'h4), .out(adder_1_out));  // open: cin, cout
  // Probe on PC
  // Probe on IR
  // Probe on RDin
  // Probe on MemWrite
  // Probe on MDin
  // Probe on LedData
  ROM #(.addrWidth(10), .dataWidth(32), .Select("high")) rom_1 (.addr(PC[11:2]), .data(IR));
  or or_1 (IR1_t, IR1, IRA);
  // Probe on RegWrite
  // Mips_Probe mips_probe_1: pin names not known; wires that end beside it: IR
  or or_2 (IR2_t, IR2, IRB);
  Counter #(.width(16), .max('hffff), .ongoal("stay"), .trigger("rising"), .behavior("old")) counter_2 (
    .count(en), .Q(\总周期数 ), .clk(CLK));  // open: load, D, carry, clr, preset
  \单周期硬布线控制器  \u_单周期硬布线控制器_1  (
    .Func(IR[5:0]), .OP(IR[31:26]), .ALU_OP(\单周期硬布线控制器_1_alu_op ), .MemToReg(\单周期硬布线控制器_1_memtoreg ),
    .MemWrite(MemWrite), .ALU_SRC(\单周期硬布线控制器_1_alu_src ), .RegWrite(RegWrite), .SysCALL(sys),
    .SignedExt(SignedExt), .RegDst(\单周期硬布线控制器_1_regdst ), .JR(\单周期硬布线控制器_1_jr ), .JMP(\单周期硬布线控制器_1_jmp ),
    .Beq(\单周期硬布线控制器_1_beq ), .JAL(\单周期硬布线控制器_1_jal ), .Bne(\单周期硬布线控制器_1_bne ), .SB(SB),
    .BLTZ(\单周期硬布线控制器_1_bltz ));
  Multiplexer #(.select(1), .width(5), .disabled("Z"), .enable("false")) multiplexer_4 (
    .in0(IR[25:21]), .in1(5'b00100), .out(multiplexer_4_out), .sel(sys));
  Multiplexer #(.select(1), .width(5), .disabled("Z"), .enable("false")) multiplexer_5 (
    .in0(IR[20:16]), .in1(5'b00010), .out(multiplexer_5_out), .sel(sys));
  assign bit_extender_1_out = {{16{1'b0}}, IR[15:0]};  // Bit_Extender bit_extender_1
  assign bit_extender_2_out = {{16{IR[15]}}, IR[15:0]};  // Bit_Extender bit_extender_2
  or or_3 (IR3_t, IR3, IRC);
  Multiplexer #(.select(1), .width(5), .disabled("Z"), .enable("false")) multiplexer_6 (
    .in0(IR[20:16]), .in1(IR[15:11]), .out(multiplexer_6_out), .sel(\单周期硬布线控制器_1_regdst ));
  Multiplexer #(.select(1), .width(32), .disabled("Z"), .enable("false")) multiplexer_7 (
    .in0(bit_extender_1_out), .in1(bit_extender_2_out), .out(multiplexer_7_out), .sel(SignedExt));
  Multiplexer #(.select(1), .width(5), .disabled("Z"), .enable("false")) multiplexer_8 (
    .in0(multiplexer_6_out), .in1({5{1'b1}}), .out(multiplexer_8_out), .sel(\单周期硬布线控制器_1_jal ));
  Multiplexer #(.select(1), .width(32), .disabled("Z"), .enable("false")) multiplexer_9 (
    .in0(multiplexer_15_out), .in1(adder_1_out), .out(RDin), .sel(\单周期硬布线控制器_1_jal ));
  MIPS_Regifile mips_regifile_1 (
    .Din(RDin), .Clk(CLK), .R1(a0), .R2(DIN), .WE(RegWrite), .W_num(multiplexer_8_out),
    .R1_num(multiplexer_4_out), .R2_num(multiplexer_5_out));
  Multiplexer #(.select(2), .width(32), .disabled("Z"), .enable("false")) multiplexer_10 (
    .in0({DOUT[31:8], DIN[7:0]}), .in1({DOUT[31:16], DIN[7:0], DOUT[7:0]}),
    .in2({DOUT[31:24], DIN[7:0], DOUT[15:0]}), .in3({DIN[7:0], DOUT[23:0]}), .out(DIN1), .sel(AIN[1:0]));
  Multiplexer #(.select(1), .width(32), .disabled("Z"), .enable("false")) multiplexer_11 (
    .in0(DIN), .in1(multiplexer_7_out), .out(multiplexer_11_out), .sel(\单周期硬布线控制器_1_alu_src ));
  Multiplexer #(.select(1), .width(32), .disabled("Z"), .enable("false")) multiplexer_12 (
    .in0(multiplexer_11_out), .in1({32{1'b0}}), .out(multiplexer_12_out), .sel(\单周期硬布线控制器_1_bltz ));
  Shifter #(.width(32), .shift("ll")) shifter_1 (.in(bit_extender_2_out), .\dist (5'b00010), .out(shifter_1_out));
  MIPS_ALU mips_alu_1 (
    .X(a0), .Y(multiplexer_12_out), .AluOP(\单周期硬布线控制器_1_alu_op ), .Equal(mips_alu_1_equal), .Result(AIN),
    .shamt(IR[10:6]));  // open: Result_2
  Comparator #(.width(32), .mode("unsigned")) comparator_2 (.a(DIN), .b(32'h32), .eq(comparator_2_eq));  // open: gt, lt
  Comparator #(.width(32), .mode("twosComplement")) comparator_3 (
    .a(32'h1), .b(AIN), .eq(comparator_3_eq));  // open: gt, lt
  Multiplexer #(.select(1), .width(32), .disabled("Z"), .enable("false")) multiplexer_13 (
    .in0(DIN), .in1(DIN1), .out(MDin), .sel(SB));
  Adder #(.width(32)) adder_2 (.a(shifter_1_out), .b(adder_1_out), .out(adder_2_out));  // open: cin, cout
  and and_1 (and_1_out, comparator_2_eq, sys);
  Register #(.width(32), .trigger("rising"), .Select("low")) register_1 (
    .D(a0), .en(sys), .Q(LedData), .clk(CLK));  // open: clr
  Multiplexer #(.select(1), .width(1), .disabled("Z"), .enable("false")) multiplexer_14 (
    .in0(1'b1), .in1(Go), .out(en), .sel(and_1_out));
  and and_2 (and_2_out, \单周期硬布线控制器_1_beq , mips_alu_1_equal);
  and and_3 (and_3_out, \单周期硬布线控制器_1_bne , ~mips_alu_1_equal);  // AND_Gate
  and and_4 (and_4_out, \单周期硬布线控制器_1_bltz , comparator_3_eq);
  or or_4 (or_4_out, and_2_out, and_3_out, and_4_out);
  RAM #(.addrWidth(10), .dataWidth(32), .bus("separate"), .Select("high")) ram_1 (
    .addr(AIN[11:2]), .din(MDin), .data(DOUT), .str(MemWrite), .clk(CLK));  // open: sel, ld, clr
  Multiplexer #(.select(1), .width(32), .disabled("Z"), .enable("false")) multiplexer_15 (
    .in0(AIN), .in1(DOUT), .out(multiplexer_15_out), .sel(\单周期硬布线控制器_1_memtoreg ));

  // Other names for the same wires on the sheet: v0[31:0] = DIN

  // Notes on the sheet:
  //   中断源
  //   中断等待指示
  //   总复位信号应将除ROM以外所有存储组件全部清零
  //   控制位
  //   暂停节拍，不能为0
  //   用这个时钟源需要去掉电路中的其他时钟源
  //   戳工具置1进入计数暂停模式，ctrl+k时钟自动运行到对应节拍暂停
  //   ctrl+k关闭时钟连续运行，将控制位置零，进入单步调试模式调试
  //   数码管输出
  //   数码管输出应该用寄存器锁存，否则显示数据只能一闪而过
  //   可计数暂停的时钟源
  //   指令存储器
  //   contents of rom_1 (hex, n*v repeats v):
  //   20110001 8000c05 20110001 20120002 20130003 8000c09 20110001 20120002 20130003 8000c0d 20110001
  //   20120002 20130003 8000c11 20110001 20120002 20130003 c000cf1 20100001 20110001 118fc0 112020
  //   20020022 c 118882 12200001 8000c15 112020 20020022 c 20110001 118880 112020 20020022 c 12200001
  //   8000c1f 20110001 118fc0 112020 20020022 c 1188c3 112020 20020022 c 118903 112020 20020022 c 118903
  //   112020 20020022 c 118903 112020 20020022 c 118903 112020 20020022 c 118903 112020 20020022 c 118903
  //   112020 20020022 c 118903 112020 20020022 c 20100001 109fc0 139fc3 8021 2012000c 24160003 26100001
  //   3210000f 20080008 20090001 139900 2709825 132020 20020022 c 1094022 1500fff9 22100001 2018000f
  //   2188024 108700 20080008 20090001 139902 2709825 132021 20020022 c 1094022 1500fff9 108702 2c9b022
  //   12c00001 8000c50 4020 1084027 84400 3508ffff 82021 20020022 c 2010ffff 20110000 ae300000 22100001
  //   22310004 ae300000 22100001 22310004 ae300000 22100001 22310004 ae300000 22100001 22310004 ae300000
  //   22100001 22310004 ae300000 22100001 22310004 ae300000 22100001 22310004 ae300000 22100001 22310004
  //   ae300000 22100001 22310004 ae300000 22100001 22310004 ae300000 22100001 22310004 ae300000 22100001
  //   22310004 ae300000 22100001 22310004 ae300000 22100001 22310004 ae300000 22100001 22310004 ae300000
  //   22100001 22310004 22100001 8020 2011003c 8e130000 8e340000 274402a 11000002 ae330000 ae140000
  //   2231fffc 1611fff8 102020 20020022 c 22100004 2011003c 1611fff2 20020032 c 2008ffff 20117777 112020
  //   20020022 c 200b0010 2288826 112020 20020022 c 216bffff 1560fffa 20020032 c 2008ffff 20090000
  //   20111997 112020 20020022 c 2288820 2e291949 1120fffa 20020032 c 20090000 200b0020 20110000 20120001
  //   a1310000 112020 20020022 c 2328820 21290001 216bffff 1560fff8 200b0008 20090000 8d310000 112020
  //   20020022 c 21290004 216bffff 1560fff9 20020032 c 2011fff1 112020 20020022 c 22310001 620fffb
  //   20020032 c 8000c00 20100000 22100001 102020 20020022 c 22100002 102020 20020022 c 22100003 102020
  //   20020022 c 22100004 102020 20020022 c 22100005 102020 20020022 c 22100006 102020 20020022 c 22100007
  //   102020 20020022 c 22100008 102020 20020022 20020022 c 3e00008
  //   指令字
  //   JMP
  //   JR
  //   OP
  //   OP
  //   Func
  //   Func
  //   rs
  //   rt
  //   rd
  //   SB
  //   BLTZ
  //   Beq
  //   Bne
  //   MemToReg
  //   MemWrite
  //   AluOP
  //   AluSrcB
  //   RegWrite
  //   JAL
  //   RegDst
  //   Syscall
  //   为方便自动评测，需要输出PC，IR，寄存器堆写如数据RDin
  //   RAM写使能MemWrite、RAM写入数据MDin等信号
endmodule

// 单周期硬布线控制器
module \单周期硬布线控制器  (
  input  [5:0] OP,
  input  [5:0] Func,
  output [3:0] ALU_OP,
  output MemToReg,
  output MemWrite,
  output ALU_SRC,
  output RegWrite,
  output SysCALL,
  output SignedExt,
  output RegDst,
  output Beq,
  output Bne,
  output JR,
  output JMP,
  output JAL,
  output SB,
  output BLTZ
);

  \运算控制器自动生成  \u_运算控制器自动生成_1  (
    .OP0(OP[0]), .OP1(OP[1]), .OP2(OP[2]), .OP3(OP[3]), .OP4(OP[4]), .OP5(OP[5]), .F0(Func[0]), .F1(Func[1]),
    .F2(Func[2]), .F3(Func[3]), .F4(Func[4]), .F5(Func[5]), .S0(ALU_OP[0]), .S1(ALU_OP[1]), .S2(ALU_OP[2]),
    .S3(ALU_OP[3]));
  \控制信号自动生成  \u_控制信号自动生成_1  (
    .OP0(OP[0]), .OP1(OP[1]), .OP2(OP[2]), .OP3(OP[3]), .OP4(OP[4]), .OP5(OP[5]), .F0(Func[0]), .F1(Func[1]),
    .F2(Func[2]), .F3(Func[3]), .F4(Func[4]), .F5(Func[5]), .MemToReg(MemToReg), .MemWrite(MemWrite),
    .ALU_SRC(ALU_SRC), .RegWrite(RegWrite), .SysCALL(SysCALL), .SignedExt(SignedExt), .RegDst(RegDst),
    .BEQ(Beq), .BNE(Bne), .JR(JR), .JUMP(JMP), .JAL(JAL), .SB(SB), .BLTZ(BLTZ));

  // Other names for the same wires on the sheet: OP_CODE[5:0] = OP

  // Notes on the sheet:
  //   运算器控制器，根据指令生成运算器功能选择信号
  //   控制信号生成，产生数据通路需要的其他控制信号
endmodule

// 运算器控制器
module \运算控制器自动生成  (
  input  OP0,
  input  OP1,
  input  OP2,
  input  OP3,
  input  OP4,
  input  OP5,
  input  F0,
  input  F1,
  input  F2,
  input  F3,
  input  F4,
  input  F5,
  output S0,
  output S1,
  output S2,
  output S3
);

  wire and_1_out, and_2_out, and_3_out, and_4_out, and_5_out, and_6_out, and_7_out, and_8_out, and_9_out,
       and_10_out, and_11_out, and_12_out, and_13_out, and_14_out, and_15_out, and_16_out, and_17_out,
       and_18_out, and_19_out, and_20_out, and_21_out, and_22_out, and_23_out, and_24_out, and_25_out,
       and_26_out, and_27_out, and_28_out, and_29_out, and_30_out, and_31_out, and_32_out, and_33_out,
       and_34_out, and_35_out, and_36_out, and_37_out, and_38_out, and_39_out, and_40_out, and_41_out,
       and_42_out, and_43_out, not_1_out, not_2_out, not_3_out, not_4_out, not_5_out, not_6_out, not_7_out,
       not_8_out, not_9_out, not_10_out, not_11_out, not_12_out, not_13_out, not_14_out, not_15_out,
       not_16_out, not_17_out, not_18_out, not_19_out, not_20_out, not_21_out, not_22_out, not_23_out,
       not_24_out, not_25_out, not_26_out, not_27_out, not_28_out, not_29_out, not_30_out, not_31_out,
       not_32_out, not_33_out, not_34_out, not_35_out, not_36_out, not_37_out, not_38_out, not_39_out,
       not_40_out, not_41_out, not_42_out, not_43_out, not_44_out, not_45_out, not_46_out, not_47_out,
       not_48_out, not_49_out, not_50_out, not_51_out, not_52_out, not_53_out, not_54_out, not_55_out,
       not_56_out, not_57_out, not_58_out, not_59_out, not_60_out, not_61_out, not_62_out, not_63_out,
       not_64_out, not_65_out, not_66_out, not_67_out, not_68_out, not_69_out, not_70_out, not_71_out,
       not_72_out, not_73_out, not_74_out, not_75_out, not_76_out, not_77_out, not_78_out, not_79_out,
       not_80_out, not_81_out, not_82_out, not_83_out, not_84_out, not_85_out, not_86_out, not_87_out,
       not_88_out, not_89_out, not_90_out, not_91_out, not_92_out, not_93_out, not_94_out, not_95_out,
       not_96_out, not_97_out, not_98_out, not_99_out, not_100_out, not_101_out, not_102_out, not_103_out,
       not_104_out, not_105_out, not_106_out, not_107_out, not_108_out, not_109_out, not_110_out,
       not_111_out, not_112_out, not_113_out, not_114_out, not_115_out, not_116_out, not_117_out,
       not_118_out, not_119_out, not_120_out, not_121_out, not_122_out, not_123_out, not_124_out,
       not_125_out, not_126_out, not_127_out, not_128_out, not_129_out, not_130_out, not_131_out,
       not_132_out, not_133_out, not_134_out, not_135_out, not_136_out, not_137_out, not_138_out,
       not_139_out, not_140_out, not_141_out, not_142_out, not_143_out, not_144_out, not_145_out,
       not_146_out, not_147_out, not_148_out, not_149_out, not_150_out, not_151_out, not_152_out,
       not_153_out, not_154_out, not_155_out, not_156_out, not_157_out, not_158_out, not_159_out,
       not_160_out, not_161_out, not_162_out, not_163_out, not_164_out, not_165_out, not_166_out,
       not_167_out, not_168_out, not_169_out, not_170_out, not_171_out, not_172_out, not_173_out,
       not_174_out, not_175_out, not_176_out, not_177_out, not_178_out, not_179_out, not_180_out,
       not_181_out, not_182_out, not_183_out, not_184_out, not_185_out, not_186_out, not_187_out,
       not_188_out, not_189_out, not_190_out, not_191_out, not_192_out, not_193_out, not_194_out,
       not_195_out, not_196_out, not_197_out, not_198_out, not_199_out, not_200_out, not_201_out,
       not_202_out, not_203_out, not_204_out, not_205_out, not_206_out, not_207_out, not_208_out,
       not_209_out, not_210_out, not_211_out, not_212_out, not_213_out, not_214_out, not_215_out,
       not_216_out, not_217_out, not_218_out, not_219_out, not_220_out, not_221_out, not_222_out,
       not_223_out, not_224_out, not_225_out, not_226_out, not_227_out, not_228_out, not_229_out,
       not_230_out, not_231_out, not_232_out, not_233_out, not_234_out, not_235_out, not_236_out,
       not_237_out, not_238_out, not_239_out, not_240_out, not_241_out, not_242_out, not_243_out,
       not_244_out, not_245_out, not_246_out, not_247_out, not_248_out, not_249_out, not_250_out,
       not_251_out, not_252_out, not_253_out, not_254_out, not_255_out, not_256_out, not_257_out,
       not_258_out, not_259_out, not_260_out, not_261_out, not_262_out, not_263_out, not_264_out,
       not_265_out, not_266_out, not_267_out, not_268_out, not_269_out, not_270_out, not_271_out,
       not_272_out, not_273_out, not_274_out, not_275_out, not_276_out, not_277_out, not_278_out,
       not_279_out, not_280_out, not_281_out, not_282_out, not_283_out;

  not not_1 (not_1_out, OP5);
  not not_2 (not_2_out, OP4);
  not not_3 (not_3_out, OP3);
  not not_4 (not_4_out, OP2);
  not not_5 (not_5_out, OP1);
  not not_6 (not_6_out, OP0);
  not not_7 (not_7_out, F5);
  not not_8 (not_8_out, F4);
  not not_9 (not_9_out, F3);
  not not_10 (not_10_out, F2);
  not not_11 (not_11_out, OP5);
  not not_12 (not_12_out, OP4);
  not not_13 (not_13_out, OP3);
  not not_14 (not_14_out, OP2);
  not not_15 (not_15_out, OP1);
  not not_16 (not_16_out, OP0);
  not not_17 (not_17_out, F4);
  not not_18 (not_18_out, F3);
  not not_19 (not_19_out, F2);
  not not_20 (not_20_out, F1);
  not not_21 (not_21_out, F0);
  not not_22 (not_22_out, OP5);
  not not_23 (not_23_out, OP4);
  not not_24 (not_24_out, OP3);
  not not_25 (not_25_out, OP2);
  not not_26 (not_26_out, OP1);
  not not_27 (not_27_out, OP0);
  not not_28 (not_28_out, F4);
  not not_29 (not_29_out, F3);
  not not_30 (not_30_out, F2);
  not not_31 (not_31_out, F1);
  not not_32 (not_32_out, OP5);
  not not_33 (not_33_out, OP4);
  not not_34 (not_34_out, OP3);
  not not_35 (not_35_out, OP2);
  not not_36 (not_36_out, OP1);
  not not_37 (not_37_out, OP0);
  not not_38 (not_38_out, F4);
  not not_39 (not_39_out, F3);
  not not_40 (not_40_out, F1);
  not not_41 (not_41_out, F0);
  not not_42 (not_42_out, OP5);
  not not_43 (not_43_out, OP4);
  not not_44 (not_44_out, OP3);
  not not_45 (not_45_out, OP2);
  not not_46 (not_46_out, OP1);
  not not_47 (not_47_out, OP0);
  not not_48 (not_48_out, F4);
  not not_49 (not_49_out, F2);
  not not_50 (not_50_out, F0);
  not not_51 (not_51_out, OP5);
  not not_52 (not_52_out, OP4);
  not not_53 (not_53_out, OP2);
  not not_54 (not_54_out, OP1);
  not not_55 (not_55_out, OP0);
  not not_56 (not_56_out, OP5);
  not not_57 (not_57_out, OP4);
  not not_58 (not_58_out, OP1);
  not not_59 (not_59_out, OP0);
  not not_60 (not_60_out, OP5);
  not not_61 (not_61_out, OP4);
  not not_62 (not_62_out, OP2);
  not not_63 (not_63_out, OP1);
  not not_64 (not_64_out, OP5);
  not not_65 (not_65_out, OP4);
  not not_66 (not_66_out, OP2);
  not not_67 (not_67_out, OP0);
  not not_68 (not_68_out, OP4);
  not not_69 (not_69_out, OP3);
  not not_70 (not_70_out, OP2);
  not not_71 (not_71_out, OP4);
  not not_72 (not_72_out, OP2);
  not not_73 (not_73_out, OP5);
  not not_74 (not_74_out, OP4);
  not not_75 (not_75_out, OP3);
  not not_76 (not_76_out, OP2);
  not not_77 (not_77_out, OP1);
  not not_78 (not_78_out, OP0);
  not not_79 (not_79_out, F4);
  not not_80 (not_80_out, F3);
  not not_81 (not_81_out, F0);
  not not_82 (not_82_out, OP4);
  not not_83 (not_83_out, OP2);
  not not_84 (not_84_out, OP1);
  not not_85 (not_85_out, OP0);
  not not_86 (not_86_out, OP5);
  not not_87 (not_87_out, OP4);
  not not_88 (not_88_out, OP3);
  not not_89 (not_89_out, OP2);
  not not_90 (not_90_out, OP1);
  not not_91 (not_91_out, OP5);
  not not_92 (not_92_out, OP4);
  not not_93 (not_93_out, OP3);
  not not_94 (not_94_out, OP2);
  not not_95 (not_95_out, OP1);
  not not_96 (not_96_out, OP0);
  not not_97 (not_97_out, F5);
  not not_98 (not_98_out, F4);
  not not_99 (not_99_out, F3);
  not not_100 (not_100_out, F2);
  not not_101 (not_101_out, F0);
  not not_102 (not_102_out, OP5);
  not not_103 (not_103_out, OP4);
  not not_104 (not_104_out, OP3);
  not not_105 (not_105_out, OP2);
  not not_106 (not_106_out, OP1);
  not not_107 (not_107_out, OP0);
  not not_108 (not_108_out, F4);
  not not_109 (not_109_out, F3);
  not not_110 (not_110_out, F2);
  not not_111 (not_111_out, F0);
  not not_112 (not_112_out, OP5);
  not not_113 (not_113_out, OP4);
  not not_114 (not_114_out, OP3);
  not not_115 (not_115_out, OP2);
  not not_116 (not_116_out, OP1);
  not not_117 (not_117_out, OP0);
  not not_118 (not_118_out, F4);
  not not_119 (not_119_out, F3);
  not not_120 (not_120_out, F1);
  not not_121 (not_121_out, F0);
  not not_122 (not_122_out, OP5);
  not not_123 (not_123_out, OP4);
  not not_124 (not_124_out, OP3);
  not not_125 (not_125_out, OP2);
  not not_126 (not_126_out, OP1);
  not not_127 (not_127_out, OP0);
  not not_128 (not_128_out, F4);
  not not_129 (not_129_out, F3);
  not not_130 (not_130_out, OP5);
  not not_131 (not_131_out, OP4);
  not not_132 (not_132_out, OP3);
  not not_133 (not_133_out, OP2);
  not not_134 (not_134_out, OP1);
  not not_135 (not_135_out, OP0);
  not not_136 (not_136_out, F4);
  not not_137 (not_137_out, F2);
  not not_138 (not_138_out, F0);
  not not_139 (not_139_out, OP5);
  not not_140 (not_140_out, OP4);
  not not_141 (not_141_out, OP1);
  not not_142 (not_142_out, OP0);
  not not_143 (not_143_out, OP5);
  not not_144 (not_144_out, OP4);
  not not_145 (not_145_out, OP2);
  not not_146 (not_146_out, OP0);
  not not_147 (not_147_out, OP5);
  not not_148 (not_148_out, OP4);
  not not_149 (not_149_out, OP3);
  not not_150 (not_150_out, OP2);
  not not_151 (not_151_out, OP1);
  not not_152 (not_152_out, OP5);
  not not_153 (not_153_out, OP4);
  not not_154 (not_154_out, OP3);
  not not_155 (not_155_out, OP2);
  not not_156 (not_156_out, OP1);
  not not_157 (not_157_out, OP0);
  not not_158 (not_158_out, F4);
  not not_159 (not_159_out, F3);
  not not_160 (not_160_out, F2);
  not not_161 (not_161_out, F1);
  not not_162 (not_162_out, F0);
  not not_163 (not_163_out, OP5);
  not not_164 (not_164_out, OP4);
  not not_165 (not_165_out, OP3);
  not not_166 (not_166_out, OP2);
  not not_167 (not_167_out, OP1);
  not not_168 (not_168_out, OP0);
  not not_169 (not_169_out, F4);
  not not_170 (not_170_out, F3);
  not not_171 (not_171_out, F2);
  not not_172 (not_172_out, F1);
  not not_173 (not_173_out, OP5);
  not not_174 (not_174_out, OP4);
  not not_175 (not_175_out, OP3);
  not not_176 (not_176_out, OP2);
  not not_177 (not_177_out, OP1);
  not not_178 (not_178_out, OP0);
  not not_179 (not_179_out, F4);
  not not_180 (not_180_out, F3);
  not not_181 (not_181_out, F2);
  not not_182 (not_182_out, F0);
  not not_183 (not_183_out, OP5);
  not not_184 (not_184_out, OP4);
  not not_185 (not_185_out, OP3);
  not not_186 (not_186_out, OP2);
  not not_187 (not_187_out, OP1);
  not not_188 (not_188_out, OP0);
  not not_189 (not_189_out, F4);
  not not_190 (not_190_out, F3);
  not not_191 (not_191_out, F1);
  not not_192 (not_192_out, F0);
  not not_193 (not_193_out, OP5);
  not not_194 (not_194_out, OP4);
  not not_195 (not_195_out, OP3);
  not not_196 (not_196_out, OP2);
  not not_197 (not_197_out, OP1);
  not not_198 (not_198_out, OP0);
  not not_199 (not_199_out, F4);
  not not_200 (not_200_out, F2);
  not not_201 (not_201_out, OP5);
  not not_202 (not_202_out, OP4);
  not not_203 (not_203_out, OP2);
  not not_204 (not_204_out, OP1);
  not not_205 (not_205_out, OP0);
  not not_206 (not_206_out, OP5);
  not not_207 (not_207_out, OP4);
  not not_208 (not_208_out, OP1);
  not not_209 (not_209_out, OP0);
  not not_210 (not_210_out, OP5);
  not not_211 (not_211_out, OP4);
  not not_212 (not_212_out, OP2);
  not not_213 (not_213_out, OP1);
  not not_214 (not_214_out, OP4);
  not not_215 (not_215_out, OP3);
  not not_216 (not_216_out, OP2);
  not not_217 (not_217_out, OP4);
  not not_218 (not_218_out, OP2);
  not not_219 (not_219_out, OP5);
  not not_220 (not_220_out, OP4);
  not not_221 (not_221_out, OP2);
  not not_222 (not_222_out, OP4);
  not not_223 (not_223_out, OP2);
  not not_224 (not_224_out, OP1);
  not not_225 (not_225_out, OP0);
  not not_226 (not_226_out, OP5);
  not not_227 (not_227_out, OP4);
  not not_228 (not_228_out, OP3);
  not not_229 (not_229_out, OP2);
  not not_230 (not_230_out, OP1);
  not not_231 (not_231_out, OP0);
  not not_232 (not_232_out, F4);
  not not_233 (not_233_out, F3);
  not not_234 (not_234_out, F1);
  not not_235 (not_235_out, OP5);
  not not_236 (not_236_out, OP4);
  not not_237 (not_237_out, OP3);
  not not_238 (not_238_out, OP2);
  not not_239 (not_239_out, OP1);
  not not_240 (not_240_out, OP0);
  not not_241 (not_241_out, F4);
  not not_242 (not_242_out, F3);
  not not_243 (not_243_out, OP5);
  not not_244 (not_244_out, OP4);
  not not_245 (not_245_out, OP3);
  not not_246 (not_246_out, OP2);
  not not_247 (not_247_out, OP1);
  not not_248 (not_248_out, OP0);
  not not_249 (not_249_out, F4);
  not not_250 (not_250_out, F2);
  not not_251 (not_251_out, F0);
  not not_252 (not_252_out, OP5);
  not not_253 (not_253_out, OP4);
  not not_254 (not_254_out, OP3);
  not not_255 (not_255_out, OP2);
  not not_256 (not_256_out, OP1);
  not not_257 (not_257_out, OP0);
  not not_258 (not_258_out, F4);
  not not_259 (not_259_out, F2);
  not not_260 (not_260_out, OP5);
  not not_261 (not_261_out, OP4);
  not not_262 (not_262_out, OP2);
  not not_263 (not_263_out, OP0);
  not not_264 (not_264_out, OP5);
  not not_265 (not_265_out, OP4);
  not not_266 (not_266_out, OP1);
  not not_267 (not_267_out, OP5);
  not not_268 (not_268_out, OP4);
  not not_269 (not_269_out, OP3);
  not not_270 (not_270_out, OP2);
  not not_271 (not_271_out, OP1);
  not not_272 (not_272_out, OP0);
  not not_273 (not_273_out, F4);
  not not_274 (not_274_out, F3);
  not not_275 (not_275_out, F0);
  not not_276 (not_276_out, OP5);
  not not_277 (not_277_out, OP4);
  not not_278 (not_278_out, OP2);
  not not_279 (not_279_out, OP5);
  not not_280 (not_280_out, OP4);
  not not_281 (not_281_out, OP3);
  not not_282 (not_282_out, OP2);
  not not_283 (not_283_out, OP1);
  and and_1 (and_1_out, not_1_out, not_2_out, not_3_out, not_4_out, not_5_out, not_6_out, not_7_out, not_8_out, not_9_out, not_10_out, F1, F0);
  and and_2 (and_2_out, not_11_out, not_12_out, not_13_out, not_14_out, not_15_out, not_16_out, F5, not_17_out, not_18_out, not_19_out, not_20_out, not_21_out);
  and and_3 (and_3_out, not_22_out, not_23_out, not_24_out, not_25_out, not_26_out, not_27_out, F5, not_28_out, not_29_out, not_30_out, not_31_out, F0);
  and and_4 (and_4_out, not_32_out, not_33_out, not_34_out, not_35_out, not_36_out, not_37_out, F5, not_38_out, not_39_out, F2, not_40_out, not_41_out);
  and and_5 (and_5_out, not_42_out, not_43_out, not_44_out, not_45_out, not_46_out, not_47_out, F5, not_48_out, F3, not_49_out, F1, not_50_out);
  and and_6 (and_6_out, not_51_out, not_52_out, OP3, not_53_out, not_54_out, not_55_out);
  and and_7 (and_7_out, not_56_out, not_57_out, OP3, OP2, not_58_out, not_59_out);
  and and_8 (and_8_out, not_60_out, not_61_out, OP3, not_62_out, not_63_out, OP0);
  and and_9 (and_9_out, not_64_out, not_65_out, OP3, not_66_out, OP1, not_67_out);
  and and_10 (and_10_out, OP5, not_68_out, not_69_out, not_70_out, OP1, OP0);
  and and_11 (and_11_out, OP5, not_71_out, OP3, not_72_out, OP1, OP0);
  and and_12 (and_12_out, not_73_out, not_74_out, not_75_out, not_76_out, not_77_out, not_78_out, F5, not_79_out, not_80_out, F2, F1, not_81_out);
  and and_13 (and_13_out, OP5, not_82_out, OP3, not_83_out, not_84_out, not_85_out);
  and and_14 (and_14_out, not_86_out, not_87_out, not_88_out, not_89_out, not_90_out, OP0);
  and and_15 (and_15_out, not_91_out, not_92_out, not_93_out, not_94_out, not_95_out, not_96_out, not_97_out, not_98_out, not_99_out, not_100_out, F1, not_101_out);
  and and_16 (and_16_out, not_102_out, not_103_out, not_104_out, not_105_out, not_106_out, not_107_out, F5, not_108_out, not_109_out, not_110_out, F1, not_111_out);
  and and_17 (and_17_out, not_112_out, not_113_out, not_114_out, not_115_out, not_116_out, not_117_out, F5, not_118_out, not_119_out, F2, not_120_out, not_121_out);
  and and_18 (and_18_out, not_122_out, not_123_out, not_124_out, not_125_out, not_126_out, not_127_out, F5, not_128_out, not_129_out, F2, F1, F0);
  and and_19 (and_19_out, not_130_out, not_131_out, not_132_out, not_133_out, not_134_out, not_135_out, F5, not_136_out, F3, not_137_out, F1, not_138_out);
  and and_20 (and_20_out, not_139_out, not_140_out, OP3, OP2, not_141_out, not_142_out);
  and and_21 (and_21_out, not_143_out, not_144_out, OP3, not_145_out, OP1, not_146_out);
  and and_22 (and_22_out, not_147_out, not_148_out, not_149_out, not_150_out, not_151_out, OP0);
  and and_23 (and_23_out, not_152_out, not_153_out, not_154_out, not_155_out, not_156_out, not_157_out, F5, not_158_out, not_159_out, not_160_out, not_161_out, not_162_out);
  and and_24 (and_24_out, not_163_out, not_164_out, not_165_out, not_166_out, not_167_out, not_168_out, F5, not_169_out, not_170_out, not_171_out, not_172_out, F0);
  and and_25 (and_25_out, not_173_out, not_174_out, not_175_out, not_176_out, not_177_out, not_178_out, F5, not_179_out, not_180_out, not_181_out, F1, not_182_out);
  and and_26 (and_26_out, not_183_out, not_184_out, not_185_out, not_186_out, not_187_out, not_188_out, F5, not_189_out, not_190_out, F2, not_191_out, not_192_out);
  and and_27 (and_27_out, not_193_out, not_194_out, not_195_out, not_196_out, not_197_out, not_198_out, F5, not_199_out, F3, not_200_out, F1, F0);
  and and_28 (and_28_out, not_201_out, not_202_out, OP3, not_203_out, not_204_out, not_205_out);
  and and_29 (and_29_out, not_206_out, not_207_out, OP3, OP2, not_208_out, not_209_out);
  and and_30 (and_30_out, not_210_out, not_211_out, OP3, not_212_out, not_213_out, OP0);
  and and_31 (and_31_out, OP5, not_214_out, not_215_out, not_216_out, OP1, OP0);
  and and_32 (and_32_out, OP5, not_217_out, OP3, not_218_out, OP1, OP0);
  and and_33 (and_33_out, not_219_out, not_220_out, OP3, not_221_out, OP1, OP0);
  and and_34 (and_34_out, OP5, not_222_out, OP3, not_223_out, not_224_out, not_225_out);
  and and_35 (and_35_out, not_226_out, not_227_out, not_228_out, not_229_out, not_230_out, not_231_out, F5, not_232_out, not_233_out, F2, not_234_out, F0);
  and and_36 (and_36_out, not_235_out, not_236_out, not_237_out, not_238_out, not_239_out, not_240_out, F5, not_241_out, not_242_out, F2, F1, F0);
  and and_37 (and_37_out, not_243_out, not_244_out, not_245_out, not_246_out, not_247_out, not_248_out, F5, not_249_out, F3, not_250_out, F1, not_251_out);
  and and_38 (and_38_out, not_252_out, not_253_out, not_254_out, not_255_out, not_256_out, not_257_out, F5, not_258_out, F3, not_259_out, F1, F0);
  and and_39 (and_39_out, not_260_out, not_261_out, OP3, not_262_out, OP1, not_263_out);
  and and_40 (and_40_out, not_264_out, not_265_out, OP3, OP2, not_266_out, OP0);
  and and_41 (and_41_out, not_267_out, not_268_out, not_269_out, not_270_out, not_271_out, not_272_out, F5, not_273_out, not_274_out, F2, F1, not_275_out);
  and and_42 (and_42_out, not_276_out, not_277_out, OP3, not_278_out, OP1, OP0);
  and and_43 (and_43_out, not_279_out, not_280_out, not_281_out, not_282_out, not_283_out, OP0);
  or or_1 (S1, and_15_out, and_16_out, and_17_out, and_18_out, and_19_out, and_20_out, and_21_out, and_22_out);
  or or_2 (S3, and_35_out, and_36_out, and_37_out, and_38_out, and_39_out, and_40_out, and_41_out, and_42_out, and_43_out);
  or or_3 (S0, and_1_out, and_2_out, and_3_out, and_4_out, and_5_out, and_6_out, and_7_out, and_8_out, and_9_out, and_10_out, and_11_out, and_12_out, and_13_out, and_14_out);
  or or_4 (S2, and_23_out, and_24_out, and_25_out, and_26_out, and_27_out, and_28_out, and_29_out, and_30_out, and_31_out, and_32_out, and_33_out, and_34_out);
endmodule

// 控制信号生成
module \控制信号自动生成  (
  input  OP0,
  input  OP1,
  input  OP2,
  input  OP3,
  input  OP4,
  input  OP5,
  input  F0,
  input  F1,
  input  F2,
  input  F3,
  input  F4,
  input  F5,
  output MemToReg,
  output MemWrite,
  output ALU_SRC,
  output RegWrite,
  output SysCALL,
  output SignedExt,
  output RegDst,
  output BEQ,
  output BNE,
  output JR,
  output JUMP,
  output JAL,
  output SB,
  output BLTZ
);

  wire and_2_out, and_3_out, and_4_out, and_5_out, and_6_out, and_7_out, and_8_out, and_9_out, and_10_out,
       and_11_out, and_12_out, and_13_out, and_14_out, and_15_out, and_16_out, and_17_out, and_18_out,
       and_19_out, and_20_out, and_21_out, and_22_out, and_23_out, and_24_out, and_25_out, and_26_out,
       and_27_out, and_28_out, and_29_out, and_30_out, and_31_out, and_32_out, and_34_out, and_35_out,
       and_36_out, and_37_out, and_38_out, and_39_out, and_40_out, and_41_out, and_42_out, and_43_out,
       and_44_out, and_45_out, and_46_out, and_47_out, and_48_out, and_49_out, and_50_out, and_51_out,
       and_52_out, and_56_out, and_57_out, and_58_out, not_1_out, not_2_out, not_3_out, not_4_out, not_5_out,
       not_6_out, not_7_out, not_8_out, not_9_out, not_10_out, not_11_out, not_12_out, not_13_out,
       not_14_out, not_15_out, not_16_out, not_17_out, not_18_out, not_19_out, not_20_out, not_21_out,
       not_22_out, not_23_out, not_24_out, not_25_out, not_26_out, not_27_out, not_28_out, not_29_out,
       not_30_out, not_31_out, not_32_out, not_33_out, not_34_out, not_35_out, not_36_out, not_37_out,
       not_38_out, not_39_out, not_40_out, not_41_out, not_42_out, not_43_out, not_44_out, not_45_out,
       not_46_out, not_47_out, not_48_out, not_49_out, not_50_out, not_51_out, not_52_out, not_53_out,
       not_54_out, not_55_out, not_56_out, not_57_out, not_58_out, not_59_out, not_60_out, not_61_out,
       not_62_out, not_63_out, not_64_out, not_65_out, not_66_out, not_67_out, not_68_out, not_69_out,
       not_70_out, not_71_out, not_72_out, not_73_out, not_74_out, not_75_out, not_76_out, not_77_out,
       not_78_out, not_79_out, not_80_out, not_81_out, not_82_out, not_83_out, not_84_out, not_85_out,
       not_86_out, not_87_out, not_88_out, not_89_out, not_90_out, not_91_out, not_92_out, not_93_out,
       not_94_out, not_95_out, not_96_out, not_97_out, not_98_out, not_99_out, not_100_out, not_101_out,
       not_102_out, not_103_out, not_104_out, not_105_out, not_106_out, not_107_out, not_108_out,
       not_109_out, not_110_out, not_111_out, not_112_out, not_113_out, not_114_out, not_115_out,
       not_116_out, not_117_out, not_118_out, not_119_out, not_120_out, not_121_out, not_122_out,
       not_123_out, not_124_out, not_125_out, not_126_out, not_127_out, not_128_out, not_129_out,
       not_130_out, not_131_out, not_132_out, not_133_out, not_134_out, not_135_out, not_136_out,
       not_137_out, not_138_out, not_139_out, not_140_out, not_141_out, not_142_out, not_143_out,
       not_144_out, not_145_out, not_146_out, not_147_out, not_148_out, not_149_out, not_150_out,
       not_151_out, not_152_out, not_153_out, not_154_out, not_155_out, not_156_out, not_157_out,
       not_158_out, not_159_out, not_160_out, not_161_out, not_162_out, not_163_out, not_164_out,
       not_165_out, not_166_out, not_167_out, not_168_out, not_169_out, not_170_out, not_171_out,
       not_172_out, not_173_out, not_174_out, not_175_out, not_176_out, not_177_out, not_178_out,
       not_179_out, not_180_out, not_181_out, not_182_out, not_183_out, not_184_out, not_185_out,
       not_186_out, not_187_out, not_188_out, not_189_out, not_190_out, not_191_out, not_192_out,
       not_193_out, not_194_out, not_195_out, not_196_out, not_197_out, not_198_out, not_199_out,
       not_200_out, not_201_out, not_202_out, not_203_out, not_204_out, not_205_out, not_206_out,
       not_207_out, not_208_out, not_209_out, not_210_out, not_211_out, not_212_out, not_213_out,
       not_214_out, not_215_out, not_216_out, not_217_out, not_218_out, not_219_out, not_220_out,
       not_221_out, not_222_out, not_223_out, not_224_out, not_225_out, not_226_out, not_227_out,
       not_228_out, not_229_out, not_230_out, not_231_out, not_232_out, not_233_out, not_234_out,
       not_235_out, not_236_out, not_237_out, not_238_out, not_239_out, not_240_out, not_241_out,
       not_242_out, not_243_out, not_244_out, not_245_out, not_246_out, not_247_out, not_248_out,
       not_249_out, not_250_out, not_251_out, not_252_out, not_253_out, not_254_out, not_255_out,
       not_256_out, not_257_out, not_258_out, not_259_out, not_260_out, not_261_out, not_262_out,
       not_263_out, not_264_out, not_265_out, not_266_out, not_267_out, not_268_out, not_269_out,
       not_270_out, not_271_out, not_272_out, not_273_out, not_274_out, not_275_out, not_276_out,
       not_277_out, not_278_out, not_279_out, not_280_out, not_281_out, not_282_out, not_283_out,
       not_284_out, not_285_out, not_286_out, not_287_out, not_288_out, not_289_out, not_290_out,
       not_291_out, not_292_out, not_293_out, not_294_out, not_295_out, not_296_out, not_297_out,
       not_298_out, not_299_out, not_300_out, not_301_out, not_302_out, not_303_out, not_304_out,
       not_305_out, not_306_out, not_307_out, not_308_out, not_309_out, not_310_out, not_311_out,
       not_312_out, not_313_out, not_314_out, not_315_out, not_316_out, not_317_out, not_318_out,
       not_319_out, not_320_out, not_321_out, not_322_out, not_323_out, not_324_out, not_325_out,
       not_326_out, not_327_out, not_328_out, not_329_out, not_330_out, not_331_out, not_332_out,
       not_333_out, not_334_out, not_335_out, not_336_out, not_337_out, not_338_out, not_339_out,
       not_340_out, not_341_out, not_342_out, not_343_out, not_344_out, not_345_out, not_346_out,
       not_347_out, not_348_out, not_349_out, not_350_out, not_351_out, not_352_out, not_353_out,
       not_354_out, not_355_out, not_356_out, not_357_out, not_358_out, not_359_out, not_360_out,
       not_361_out, not_362_out, not_363_out, not_364_out, not_365_out, not_366_out, not_367_out,
       not_368_out, not_369_out, not_370_out, not_371_out, not_372_out, not_373_out, not_374_out,
       not_375_out, not_376_out, not_377_out, not_378_out, not_379_out, not_380_out, not_381_out,
       not_382_out, not_383_out, not_384_out, not_385_out, not_386_out, not_387_out, not_388_out,
       not_389_out, not_390_out, not_391_out, not_392_out, not_393_out;

  not not_1 (not_1_out, OP4);
  not not_2 (not_2_out, OP3);
  not not_3 (not_3_out, OP2);
  not not_4 (not_4_out, OP4);
  not not_5 (not_5_out, OP2);
  not not_6 (not_6_out, OP4);
  not not_7 (not_7_out, OP2);
  not not_8 (not_8_out, OP1);
  not not_9 (not_9_out, OP0);
  not not_10 (not_10_out, OP5);
  not not_11 (not_11_out, OP4);
  not not_12 (not_12_out, OP2);
  not not_13 (not_13_out, OP1);
  not not_14 (not_14_out, OP0);
  not not_15 (not_15_out, OP5);
  not not_16 (not_16_out, OP4);
  not not_17 (not_17_out, OP1);
  not not_18 (not_18_out, OP0);
  not not_19 (not_19_out, OP5);
  not not_20 (not_20_out, OP4);
  not not_21 (not_21_out, OP2);
  not not_22 (not_22_out, OP1);
  not not_23 (not_23_out, OP5);
  not not_24 (not_24_out, OP4);
  not not_25 (not_25_out, OP2);
  not not_26 (not_26_out, OP0);
  not not_27 (not_27_out, OP5);
  not not_28 (not_28_out, OP4);
  not not_29 (not_29_out, OP1);
  not not_30 (not_30_out, OP4);
  not not_31 (not_31_out, OP3);
  not not_32 (not_32_out, OP2);
  not not_33 (not_33_out, OP4);
  not not_34 (not_34_out, OP2);
  not not_35 (not_35_out, OP5);
  not not_36 (not_36_out, OP4);
  not not_37 (not_37_out, OP2);
  not not_38 (not_38_out, OP4);
  not not_39 (not_39_out, OP2);
  not not_40 (not_40_out, OP1);
  not not_41 (not_41_out, OP0);
  not not_42 (not_42_out, OP5);
  not not_43 (not_43_out, OP4);
  not not_44 (not_44_out, OP3);
  not not_45 (not_45_out, OP2);
  not not_46 (not_46_out, OP1);
  not not_47 (not_47_out, OP0);
  not not_48 (not_48_out, F5);
  not not_49 (not_49_out, F4);
  not not_50 (not_50_out, F3);
  not not_51 (not_51_out, F2);
  not not_52 (not_52_out, F1);
  not not_53 (not_53_out, F0);
  not not_54 (not_54_out, OP5);
  not not_55 (not_55_out, OP4);
  not not_56 (not_56_out, OP3);
  not not_57 (not_57_out, OP2);
  not not_58 (not_58_out, OP1);
  not not_59 (not_59_out, OP0);
  not not_60 (not_60_out, F5);
  not not_61 (not_61_out, F4);
  not not_62 (not_62_out, F3);
  not not_63 (not_63_out, F2);
  not not_64 (not_64_out, OP5);
  not not_65 (not_65_out, OP4);
  not not_66 (not_66_out, OP3);
  not not_67 (not_67_out, OP2);
  not not_68 (not_68_out, OP1);
  not not_69 (not_69_out, OP0);
  not not_70 (not_70_out, F5);
  not not_71 (not_71_out, F4);
  not not_72 (not_72_out, F3);
  not not_73 (not_73_out, F2);
  not not_74 (not_74_out, F0);
  not not_75 (not_75_out, OP5);
  not not_76 (not_76_out, OP4);
  not not_77 (not_77_out, OP3);
  not not_78 (not_78_out, OP2);
  not not_79 (not_79_out, OP1);
  not not_80 (not_80_out, OP0);
  not not_81 (not_81_out, F4);
  not not_82 (not_82_out, F3);
  not not_83 (not_83_out, F2);
  not not_84 (not_84_out, F1);
  not not_85 (not_85_out, F0);
  not not_86 (not_86_out, OP5);
  not not_87 (not_87_out, OP4);
  not not_88 (not_88_out, OP3);
  not not_89 (not_89_out, OP2);
  not not_90 (not_90_out, OP1);
  not not_91 (not_91_out, OP0);
  not not_92 (not_92_out, F4);
  not not_93 (not_93_out, F3);
  not not_94 (not_94_out, F2);
  not not_95 (not_95_out, F1);
  not not_96 (not_96_out, OP5);
  not not_97 (not_97_out, OP4);
  not not_98 (not_98_out, OP3);
  not not_99 (not_99_out, OP2);
  not not_100 (not_100_out, OP1);
  not not_101 (not_101_out, OP0);
  not not_102 (not_102_out, F4);
  not not_103 (not_103_out, F3);
  not not_104 (not_104_out, F2);
  not not_105 (not_105_out, F0);
  not not_106 (not_106_out, OP5);
  not not_107 (not_107_out, OP4);
  not not_108 (not_108_out, OP3);
  not not_109 (not_109_out, OP2);
  not not_110 (not_110_out, OP1);
  not not_111 (not_111_out, OP0);
  not not_112 (not_112_out, F4);
  not not_113 (not_113_out, F3);
  not not_114 (not_114_out, F1);
  not not_115 (not_115_out, F0);
  not not_116 (not_116_out, OP5);
  not not_117 (not_117_out, OP4);
  not not_118 (not_118_out, OP3);
  not not_119 (not_119_out, OP2);
  not not_120 (not_120_out, OP1);
  not not_121 (not_121_out, OP0);
  not not_122 (not_122_out, F4);
  not not_123 (not_123_out, F3);
  not not_124 (not_124_out, F1);
  not not_125 (not_125_out, OP5);
  not not_126 (not_126_out, OP4);
  not not_127 (not_127_out, OP3);
  not not_128 (not_128_out, OP2);
  not not_129 (not_129_out, OP1);
  not not_130 (not_130_out, OP0);
  not not_131 (not_131_out, F4);
  not not_132 (not_132_out, F3);
  not not_133 (not_133_out, OP5);
  not not_134 (not_134_out, OP4);
  not not_135 (not_135_out, OP3);
  not not_136 (not_136_out, OP2);
  not not_137 (not_137_out, OP1);
  not not_138 (not_138_out, OP0);
  not not_139 (not_139_out, F4);
  not not_140 (not_140_out, F2);
  not not_141 (not_141_out, F0);
  not not_142 (not_142_out, OP5);
  not not_143 (not_143_out, OP4);
  not not_144 (not_144_out, OP3);
  not not_145 (not_145_out, OP2);
  not not_146 (not_146_out, OP1);
  not not_147 (not_147_out, OP0);
  not not_148 (not_148_out, F4);
  not not_149 (not_149_out, F2);
  not not_150 (not_150_out, OP5);
  not not_151 (not_151_out, OP4);
  not not_152 (not_152_out, OP3);
  not not_153 (not_153_out, OP2);
  not not_154 (not_154_out, OP5);
  not not_155 (not_155_out, OP4);
  not not_156 (not_156_out, OP2);
  not not_157 (not_157_out, OP1);
  not not_158 (not_158_out, OP0);
  not not_159 (not_159_out, OP5);
  not not_160 (not_160_out, OP4);
  not not_161 (not_161_out, OP1);
  not not_162 (not_162_out, OP0);
  not not_163 (not_163_out, OP5);
  not not_164 (not_164_out, OP4);
  not not_165 (not_165_out, OP2);
  not not_166 (not_166_out, OP1);
  not not_167 (not_167_out, OP5);
  not not_168 (not_168_out, OP4);
  not not_169 (not_169_out, OP2);
  not not_170 (not_170_out, OP0);
  not not_171 (not_171_out, OP5);
  not not_172 (not_172_out, OP4);
  not not_173 (not_173_out, OP1);
  not not_174 (not_174_out, OP4);
  not not_175 (not_175_out, OP3);
  not not_176 (not_176_out, OP2);
  not not_177 (not_177_out, OP5);
  not not_178 (not_178_out, OP4);
  not not_179 (not_179_out, OP3);
  not not_180 (not_180_out, OP2);
  not not_181 (not_181_out, OP1);
  not not_182 (not_182_out, OP0);
  not not_183 (not_183_out, F4);
  not not_184 (not_184_out, F3);
  not not_185 (not_185_out, F0);
  not not_186 (not_186_out, OP5);
  not not_187 (not_187_out, OP4);
  not not_188 (not_188_out, OP2);
  not not_189 (not_189_out, OP5);
  not not_190 (not_190_out, OP4);
  not not_191 (not_191_out, OP3);
  not not_192 (not_192_out, OP2);
  not not_193 (not_193_out, OP1);
  not not_194 (not_194_out, OP0);
  not not_195 (not_195_out, F5);
  not not_196 (not_196_out, F4);
  not not_197 (not_197_out, F1);
  not not_198 (not_198_out, F0);
  not not_199 (not_199_out, OP5);
  not not_200 (not_200_out, OP4);
  not not_201 (not_201_out, OP2);
  not not_202 (not_202_out, OP1);
  not not_203 (not_203_out, OP0);
  not not_204 (not_204_out, OP5);
  not not_205 (not_205_out, OP4);
  not not_206 (not_206_out, OP2);
  not not_207 (not_207_out, OP1);
  not not_208 (not_208_out, OP5);
  not not_209 (not_209_out, OP4);
  not not_210 (not_210_out, OP2);
  not not_211 (not_211_out, OP0);
  not not_212 (not_212_out, OP4);
  not not_213 (not_213_out, OP3);
  not not_214 (not_214_out, OP2);
  not not_215 (not_215_out, OP4);
  not not_216 (not_216_out, OP2);
  not not_217 (not_217_out, OP5);
  not not_218 (not_218_out, OP4);
  not not_219 (not_219_out, OP2);
  not not_220 (not_220_out, OP4);
  not not_221 (not_221_out, OP2);
  not not_222 (not_222_out, OP1);
  not not_223 (not_223_out, OP0);
  not not_224 (not_224_out, OP5);
  not not_225 (not_225_out, OP4);
  not not_226 (not_226_out, OP3);
  not not_227 (not_227_out, OP2);
  not not_228 (not_228_out, OP1);
  not not_229 (not_229_out, OP0);
  not not_230 (not_230_out, F5);
  not not_231 (not_231_out, F4);
  not not_232 (not_232_out, F3);
  not not_233 (not_233_out, F2);
  not not_234 (not_234_out, F1);
  not not_235 (not_235_out, F0);
  not not_236 (not_236_out, OP5);
  not not_237 (not_237_out, OP4);
  not not_238 (not_238_out, OP3);
  not not_239 (not_239_out, OP2);
  not not_240 (not_240_out, OP1);
  not not_241 (not_241_out, OP0);
  not not_242 (not_242_out, F5);
  not not_243 (not_243_out, F4);
  not not_244 (not_244_out, F3);
  not not_245 (not_245_out, F2);
  not not_246 (not_246_out, OP5);
  not not_247 (not_247_out, OP4);
  not not_248 (not_248_out, OP3);
  not not_249 (not_249_out, OP2);
  not not_250 (not_250_out, OP1);
  not not_251 (not_251_out, OP0);
  not not_252 (not_252_out, F5);
  not not_253 (not_253_out, F4);
  not not_254 (not_254_out, F3);
  not not_255 (not_255_out, F2);
  not not_256 (not_256_out, F0);
  not not_257 (not_257_out, OP5);
  not not_258 (not_258_out, OP4);
  not not_259 (not_259_out, OP3);
  not not_260 (not_260_out, OP2);
  not not_261 (not_261_out, OP1);
  not not_262 (not_262_out, OP0);
  not not_263 (not_263_out, F4);
  not not_264 (not_264_out, F3);
  not not_265 (not_265_out, F2);
  not not_266 (not_266_out, F1);
  not not_267 (not_267_out, F0);
  not not_268 (not_268_out, OP5);
  not not_269 (not_269_out, OP4);
  not not_270 (not_270_out, OP3);
  not not_271 (not_271_out, OP2);
  not not_272 (not_272_out, OP1);
  not not_273 (not_273_out, OP0);
  not not_274 (not_274_out, F4);
  not not_275 (not_275_out, F3);
  not not_276 (not_276_out, F2);
  not not_277 (not_277_out, F1);
  not not_278 (not_278_out, OP5);
  not not_279 (not_279_out, OP4);
  not not_280 (not_280_out, OP3);
  not not_281 (not_281_out, OP2);
  not not_282 (not_282_out, OP1);
  not not_283 (not_283_out, OP0);
  not not_284 (not_284_out, F4);
  not not_285 (not_285_out, F3);
  not not_286 (not_286_out, F2);
  not not_287 (not_287_out, F0);
  not not_288 (not_288_out, OP5);
  not not_289 (not_289_out, OP4);
  not not_290 (not_290_out, OP3);
  not not_291 (not_291_out, OP2);
  not not_292 (not_292_out, OP1);
  not not_293 (not_293_out, OP0);
  not not_294 (not_294_out, F4);
  not not_295 (not_295_out, F3);
  not not_296 (not_296_out, F1);
  not not_297 (not_297_out, F0);
  not not_298 (not_298_out, OP5);
  not not_299 (not_299_out, OP4);
  not not_300 (not_300_out, OP3);
  not not_301 (not_301_out, OP2);
  not not_302 (not_302_out, OP1);
  not not_303 (not_303_out, OP0);
  not not_304 (not_304_out, F4);
  not not_305 (not_305_out, F3);
  not not_306 (not_306_out, F1);
  not not_307 (not_307_out, OP5);
  not not_308 (not_308_out, OP4);
  not not_309 (not_309_out, OP3);
  not not_310 (not_310_out, OP2);
  not not_311 (not_311_out, OP1);
  not not_312 (not_312_out, OP0);
  not not_313 (not_313_out, F4);
  not not_314 (not_314_out, F3);
  not not_315 (not_315_out, OP5);
  not not_316 (not_316_out, OP4);
  not not_317 (not_317_out, OP3);
  not not_318 (not_318_out, OP2);
  not not_319 (not_319_out, OP1);
  not not_320 (not_320_out, OP0);
  not not_321 (not_321_out, F4);
  not not_322 (not_322_out, F2);
  not not_323 (not_323_out, F0);
  not not_324 (not_324_out, OP5);
  not not_325 (not_325_out, OP4);
  not not_326 (not_326_out, OP3);
  not not_327 (not_327_out, OP2);
  not not_328 (not_328_out, OP1);
  not not_329 (not_329_out, OP0);
  not not_330 (not_330_out, F4);
  not not_331 (not_331_out, F2);
  not not_332 (not_332_out, OP5);
  not not_333 (not_333_out, OP4);
  not not_334 (not_334_out, OP3);
  not not_335 (not_335_out, OP2);
  not not_336 (not_336_out, OP1);
  not not_337 (not_337_out, OP0);
  not not_338 (not_338_out, F4);
  not not_339 (not_339_out, F3);
  not not_340 (not_340_out, F0);
  not not_341 (not_341_out, OP5);
  not not_342 (not_342_out, OP4);
  not not_343 (not_343_out, OP3);
  not not_344 (not_344_out, OP1);
  not not_345 (not_345_out, OP0);
  not not_346 (not_346_out, OP5);
  not not_347 (not_347_out, OP4);
  not not_348 (not_348_out, OP3);
  not not_349 (not_349_out, OP1);
  not not_350 (not_350_out, OP5);
  not not_351 (not_351_out, OP4);
  not not_352 (not_352_out, OP3);
  not not_353 (not_353_out, OP2);
  not not_354 (not_354_out, OP1);
  not not_355 (not_355_out, OP0);
  not not_356 (not_356_out, F5);
  not not_357 (not_357_out, F4);
  not not_358 (not_358_out, F2);
  not not_359 (not_359_out, F1);
  not not_360 (not_360_out, F0);
  not not_361 (not_361_out, OP5);
  not not_362 (not_362_out, OP4);
  not not_363 (not_363_out, OP3);
  not not_364 (not_364_out, OP2);
  not not_365 (not_365_out, OP1);
  not not_366 (not_366_out, OP0);
  not not_367 (not_367_out, F5);
  not not_368 (not_368_out, F4);
  not not_369 (not_369_out, F2);
  not not_370 (not_370_out, F1);
  not not_371 (not_371_out, F0);
  not not_372 (not_372_out, OP5);
  not not_373 (not_373_out, OP4);
  not not_374 (not_374_out, OP3);
  not not_375 (not_375_out, OP2);
  not not_376 (not_376_out, OP0);
  not not_377 (not_377_out, OP5);
  not not_378 (not_378_out, OP4);
  not not_379 (not_379_out, OP3);
  not not_380 (not_380_out, OP2);
  not not_381 (not_381_out, OP5);
  not not_382 (not_382_out, OP4);
  not not_383 (not_383_out, OP3);
  not not_384 (not_384_out, OP2);
  not not_385 (not_385_out, OP4);
  not not_386 (not_386_out, OP2);
  not not_387 (not_387_out, OP1);
  not not_388 (not_388_out, OP0);
  not not_389 (not_389_out, OP5);
  not not_390 (not_390_out, OP4);
  not not_391 (not_391_out, OP3);
  not not_392 (not_392_out, OP2);
  not not_393 (not_393_out, OP1);
  and and_1 (MemToReg, OP5, not_1_out, not_2_out, not_3_out, OP1, OP0);
  and and_2 (and_2_out, OP5, not_4_out, OP3, not_5_out, OP1, OP0);
  and and_3 (and_3_out, OP5, not_6_out, OP3, not_7_out, not_8_out, not_9_out);
  and and_4 (and_4_out, not_10_out, not_11_out, OP3, not_12_out, not_13_out, not_14_out);
  and and_5 (and_5_out, not_15_out, not_16_out, OP3, OP2, not_17_out, not_18_out);
  and and_6 (and_6_out, not_19_out, not_20_out, OP3, not_21_out, not_22_out, OP0);
  and and_7 (and_7_out, not_23_out, not_24_out, OP3, not_25_out, OP1, not_26_out);
  and and_8 (and_8_out, not_27_out, not_28_out, OP3, OP2, not_29_out, OP0);
  and and_9 (and_9_out, OP5, not_30_out, not_31_out, not_32_out, OP1, OP0);
  and and_10 (and_10_out, OP5, not_33_out, OP3, not_34_out, OP1, OP0);
  and and_11 (and_11_out, not_35_out, not_36_out, OP3, not_37_out, OP1, OP0);
  and and_12 (and_12_out, OP5, not_38_out, OP3, not_39_out, not_40_out, not_41_out);
  and and_13 (and_13_out, not_42_out, not_43_out, not_44_out, not_45_out, not_46_out, not_47_out, not_48_out, not_49_out, not_50_out, not_51_out, not_52_out, not_53_out);
  and and_14 (and_14_out, not_54_out, not_55_out, not_56_out, not_57_out, not_58_out, not_59_out, not_60_out, not_61_out, not_62_out, not_63_out, F1, F0);
  and and_15 (and_15_out, not_64_out, not_65_out, not_66_out, not_67_out, not_68_out, not_69_out, not_70_out, not_71_out, not_72_out, not_73_out, F1, not_74_out);
  and and_16 (and_16_out, not_75_out, not_76_out, not_77_out, not_78_out, not_79_out, not_80_out, F5, not_81_out, not_82_out, not_83_out, not_84_out, not_85_out);
  and and_17 (and_17_out, not_86_out, not_87_out, not_88_out, not_89_out, not_90_out, not_91_out, F5, not_92_out, not_93_out, not_94_out, not_95_out, F0);
  and and_18 (and_18_out, not_96_out, not_97_out, not_98_out, not_99_out, not_100_out, not_101_out, F5, not_102_out, not_103_out, not_104_out, F1, not_105_out);
  and and_19 (and_19_out, not_106_out, not_107_out, not_108_out, not_109_out, not_110_out, not_111_out, F5, not_112_out, not_113_out, F2, not_114_out, not_115_out);
  and and_20 (and_20_out, not_116_out, not_117_out, not_118_out, not_119_out, not_120_out, not_121_out, F5, not_122_out, not_123_out, F2, not_124_out, F0);
  and and_21 (and_21_out, not_125_out, not_126_out, not_127_out, not_128_out, not_129_out, not_130_out, F5, not_131_out, not_132_out, F2, F1, F0);
  and and_22 (and_22_out, not_133_out, not_134_out, not_135_out, not_136_out, not_137_out, not_138_out, F5, not_139_out, F3, not_140_out, F1, not_141_out);
  and and_23 (and_23_out, not_142_out, not_143_out, not_144_out, not_145_out, not_146_out, not_147_out, F5, not_148_out, F3, not_149_out, F1, F0);
  and and_24 (and_24_out, not_150_out, not_151_out, not_152_out, not_153_out, OP1, OP0);
  and and_25 (and_25_out, not_154_out, not_155_out, OP3, not_156_out, not_157_out, not_158_out);
  and and_26 (and_26_out, not_159_out, not_160_out, OP3, OP2, not_161_out, not_162_out);
  and and_27 (and_27_out, not_163_out, not_164_out, OP3, not_165_out, not_166_out, OP0);
  and and_28 (and_28_out, not_167_out, not_168_out, OP3, not_169_out, OP1, not_170_out);
  and and_29 (and_29_out, not_171_out, not_172_out, OP3, OP2, not_173_out, OP0);
  and and_30 (and_30_out, OP5, not_174_out, not_175_out, not_176_out, OP1, OP0);
  and and_31 (and_31_out, not_177_out, not_178_out, not_179_out, not_180_out, not_181_out, not_182_out, F5, not_183_out, not_184_out, F2, F1, not_185_out);
  and and_32 (and_32_out, not_186_out, not_187_out, OP3, not_188_out, OP1, OP0);
  and and_33 (SysCALL, not_189_out, not_190_out, not_191_out, not_192_out, not_193_out, not_194_out, not_195_out, not_196_out, F3, F2, not_197_out, not_198_out);
  and and_34 (and_34_out, not_199_out, not_200_out, OP3, not_201_out, not_202_out, not_203_out);
  and and_35 (and_35_out, not_204_out, not_205_out, OP3, not_206_out, not_207_out, OP0);
  and and_36 (and_36_out, not_208_out, not_209_out, OP3, not_210_out, OP1, not_211_out);
  and and_37 (and_37_out, OP5, not_212_out, not_213_out, not_214_out, OP1, OP0);
  and and_38 (and_38_out, OP5, not_215_out, OP3, not_216_out, OP1, OP0);
  and and_39 (and_39_out, not_217_out, not_218_out, OP3, not_219_out, OP1, OP0);
  and and_40 (and_40_out, OP5, not_220_out, OP3, not_221_out, not_222_out, not_223_out);
  and and_41 (and_41_out, not_224_out, not_225_out, not_226_out, not_227_out, not_228_out, not_229_out, not_230_out, not_231_out, not_232_out, not_233_out, not_234_out, not_235_out);
  and and_42 (and_42_out, not_236_out, not_237_out, not_238_out, not_239_out, not_240_out, not_241_out, not_242_out, not_243_out, not_244_out, not_245_out, F1, F0);
  and and_43 (and_43_out, not_246_out, not_247_out, not_248_out, not_249_out, not_250_out, not_251_out, not_252_out, not_253_out, not_254_out, not_255_out, F1, not_256_out);
  and and_44 (and_44_out, not_257_out, not_258_out, not_259_out, not_260_out, not_261_out, not_262_out, F5, not_263_out, not_264_out, not_265_out, not_266_out, not_267_out);
  and and_45 (and_45_out, not_268_out, not_269_out, not_270_out, not_271_out, not_272_out, not_273_out, F5, not_274_out, not_275_out, not_276_out, not_277_out, F0);
  and and_46 (and_46_out, not_278_out, not_279_out, not_280_out, not_281_out, not_282_out, not_283_out, F5, not_284_out, not_285_out, not_286_out, F1, not_287_out);
  and and_47 (and_47_out, not_288_out, not_289_out, not_290_out, not_291_out, not_292_out, not_293_out, F5, not_294_out, not_295_out, F2, not_296_out, not_297_out);
  and and_48 (and_48_out, not_298_out, not_299_out, not_300_out, not_301_out, not_302_out, not_303_out, F5, not_304_out, not_305_out, F2, not_306_out, F0);
  and and_49 (and_49_out, not_307_out, not_308_out, not_309_out, not_310_out, not_311_out, not_312_out, F5, not_313_out, not_314_out, F2, F1, F0);
  and and_50 (and_50_out, not_315_out, not_316_out, not_317_out, not_318_out, not_319_out, not_320_out, F5, not_321_out, F3, not_322_out, F1, not_323_out);
  and and_51 (and_51_out, not_324_out, not_325_out, not_326_out, not_327_out, not_328_out, not_329_out, F5, not_330_out, F3, not_331_out, F1, F0);
  and and_52 (and_52_out, not_332_out, not_333_out, not_334_out, not_335_out, not_336_out, not_337_out, F5, not_338_out, not_339_out, F2, F1, not_340_out);
  and and_53 (BEQ, not_341_out, not_342_out, not_343_out, OP2, not_344_out, not_345_out);
  and and_54 (BNE, not_346_out, not_347_out, not_348_out, OP2, not_349_out, OP0);
  and and_55 (JR, not_350_out, not_351_out, not_352_out, not_353_out, not_354_out, not_355_out, not_356_out, not_357_out, F3, not_358_out, not_359_out, not_360_out);
  and and_56 (and_56_out, not_361_out, not_362_out, not_363_out, not_364_out, not_365_out, not_366_out, not_367_out, not_368_out, F3, not_369_out, not_370_out, not_371_out);
  and and_57 (and_57_out, not_372_out, not_373_out, not_374_out, not_375_out, OP1, not_376_out);
  and and_58 (and_58_out, not_377_out, not_378_out, not_379_out, not_380_out, OP1, OP0);
  and and_59 (JAL, not_381_out, not_382_out, not_383_out, not_384_out, OP1, OP0);
  and and_60 (SB, OP5, not_385_out, OP3, not_386_out, not_387_out, not_388_out);
  and and_61 (BLTZ, not_389_out, not_390_out, not_391_out, not_392_out, not_393_out, OP0);
  or or_1 (MemWrite, and_2_out, and_3_out);
  or or_2 (ALU_SRC, and_4_out, and_5_out, and_6_out, and_7_out, and_8_out, and_9_out, and_10_out, and_11_out, and_12_out);
  or or_3 (SignedExt, and_34_out, and_35_out, and_36_out, and_37_out, and_38_out, and_39_out, and_40_out);
  or or_4 (JUMP, and_56_out, and_57_out, and_58_out);
  or or_5 (RegWrite, and_13_out, and_14_out, and_15_out, and_16_out, and_17_out, and_18_out, and_19_out, and_20_out, and_21_out, and_22_out, and_23_out, and_24_out, and_25_out, and_26_out, and_27_out, and_28_out, and_29_out, and_30_out, and_31_out, and_32_out);
  or or_6 (RegDst, and_41_out, and_42_out, and_43_out, and_44_out, and_45_out, and_46_out, and_47_out, and_48_out, and_49_out, and_50_out, and_51_out, and_52_out);
endmodule

// ALU
module MIPS_ALU (
  input  [4:0] shamt,
  input  [31:0] X,
  input  [31:0] Y,
  input  [3:0] AluOP,
  output Equal,
  output [31:0] Result,
  output [31:0] Result_2
);

  wire [0:0] comparator_1_lt, comparator_2_lt;
  wire [31:0] adder_1_out, AND_out, divider_1_out, divider_1_rem, multiplier_1_cout, multiplier_1_out,
       NOR_out, OR_out, shifter_1_out, shifter_2_out, shifter_3_out, subtractor_1_out, XOR_out;

  assign AND_out = X & Y;  // AND_Gate AND, 32 bits wide
  assign OR_out = X | Y;  // OR_Gate OR, 32 bits wide
  Shifter #(.width(32), .shift("ll")) shifter_1 (.in(Y), .\dist (shamt), .out(shifter_1_out));
  Shifter #(.width(32), .shift("ar")) shifter_2 (.in(Y), .\dist (shamt), .out(shifter_2_out));
  Shifter #(.width(32), .shift("lr")) shifter_3 (.in(Y), .\dist (shamt), .out(shifter_3_out));
  Multiplier #(.width(32)) multiplier_1 (.a(X), .b(Y), .out(multiplier_1_out), .cout(multiplier_1_cout));  // open: cin
  Divider #(.width(32)) divider_1 (.a(X), .b(Y), .out(divider_1_out), .rem(divider_1_rem));  // open: upper
  Adder #(.width(32)) adder_1 (.a(X), .b(Y), .out(adder_1_out));  // open: cin, cout
  Subtractor #(.width(32)) subtractor_1 (.a(X), .b(Y), .out(subtractor_1_out));  // open: bin, bout
  assign XOR_out = X ^ Y;  // XOR_Gate XOR, 32 bits wide
  assign NOR_out = ~(X | Y);  // NOR_Gate NOR, 32 bits wide
  Comparator #(.width(32), .mode("twosComplement")) comparator_1 (
    .a(X), .b(Y), .eq(Equal), .lt(comparator_1_lt[0]));  // open: gt
  Comparator #(.width(32), .mode("unsigned")) comparator_2 (.a(X), .b(Y), .lt(comparator_2_lt[0]));  // open: gt, eq
  Multiplexer #(.select(4), .width(32), .disabled("Z"), .enable("false")) multiplexer_1 (
    .in0(shifter_1_out), .in1(shifter_2_out), .in2(shifter_3_out), .in3(multiplier_1_out),
    .in4(divider_1_out), .in5(adder_1_out), .in6(subtractor_1_out), .in7(AND_out), .in8(OR_out),
    .in9(XOR_out), .in10(NOR_out), .in11({{31{1'b0}}, comparator_1_lt[0]}),
    .in12({{31{1'b0}}, comparator_2_lt[0]}), .in13({32{1'b0}}), .in14({32{1'b0}}), .in15({32{1'b0}}),
    .out(Result), .sel(AluOP));
  Multiplexer #(.select(4), .width(32), .disabled("Z"), .enable("false")) multiplexer_2 (
    .in0({32{1'b0}}), .in1({32{1'b0}}), .in2({32{1'b0}}), .in3(multiplier_1_cout), .in4(divider_1_rem),
    .in5({32{1'b0}}), .in6({32{1'b0}}), .in7({32{1'b0}}), .in8({32{1'b0}}), .in9({32{1'b0}}),
    .in10({32{1'b0}}), .in11({32{1'b0}}), .in12({32{1'b0}}), .in13({32{1'b0}}), .in14({32{1'b0}}),
    .in15({32{1'b0}}), .out(Result_2), .sel(AluOP));

  // Other names for the same wires on the sheet: Result2[31:0] = Result_2; S[3:0] = AluOP

  // Notes on the sheet:
  //   不要改变此引脚区域内容，也不要改变ALU封装形式
  //   输入引脚
  //   输出引脚
endmodule

module MIPS_Regifile (
  input  [31:0] Din,
  input  Clk,
  input  WE,
  input  [4:0] R1_num,
  input  [4:0] W_num,
  input  [4:0] R2_num,
  output [31:0] R1,
  output [31:0] R2
);

  // RegisterFile registerfile_1: pin names not known; wires that end beside it: Din, Clk, WE, W_num, R1_num, R2_num, R1, R2
endmodule

module \理想流水线  (
  output RegWrite,
  output MemWrite,
  output [31:0] IF_PC,
  output [31:0] ID_PC,
  output [31:0] EX_PC,
  output [31:0] M_PC,
  output [31:0] WB_PC,
  output [31:0] RDin,
  output [31:0] MDin,
  output [31:0] LedData
);

  wire and_1_out, and_2_out, and_3_out, and_4_out, CLK, clock_1_out, clock_2_out, comparator_1_eq,
       comparator_1_lt, comparator_2_eq, comparator_3_eq, d_ff_1_q, en, ex_mem_1_jal_2, ex_mem_1_memtoreg_2,
       ex_mem_1_regwrite_2, ex_mem_1_sb_2, ex_mem_1_syscall_2, Go, id_ex_1_alusrcb_2, id_ex_1_beq_2,
       id_ex_1_bltz_2, id_ex_1_bne_2, id_ex_1_jal_2, id_ex_1_jmp_2, id_ex_1_jr_2, id_ex_1_memtoreg_2,
       id_ex_1_memwrite_2, id_ex_1_regwrite_2, id_ex_1_sb_2, id_ex_1_syscall_2, IR1, IR2, IR3,
       mem_wb_1_jal_2, mem_wb_1_memtoreg_2, mips_alu_1_equal, nand_1_out, not_1_out, not_2_out, not_3_out,
       not_4_out, or_1_out, or_2_out, RST, SignedExt, sys, W1, W2, W3, \单周期硬布线控制器_1_alu_src ,
       \单周期硬布线控制器_1_beq , \单周期硬布线控制器_1_bltz , \单周期硬布线控制器_1_bne , \单周期硬布线控制器_1_jal , \单周期硬布线控制器_1_jmp ,
       \单周期硬布线控制器_1_jr , \单周期硬布线控制器_1_memtoreg , \单周期硬布线控制器_1_memwrite , \单周期硬布线控制器_1_regdst ,
       \单周期硬布线控制器_1_regwrite , \单周期硬布线控制器_1_sb , \单周期硬布线控制器_1_syscall ;
  wire [3:0] id_ex_1_aluop, \单周期硬布线控制器_1_alu_op ;
  wire [4:0] ex_mem_1_wr_2, id_ex_1_shamt_2, id_ex_1_wr_2, mem_wb_1_wr_2, multiplexer_4_out,
       multiplexer_5_out, multiplexer_6_out, multiplexer_7_out;
  wire [12:0] CNT_num;
  wire [15:0] \LoadUse次数 , \总周期数 , \插入气泡数 , \无条件分支数 , \条件分支成功数 ;
  wire [31:0] a0, adder_1_out, adder_2_out, AIN, bit_extender_1_out, bit_extender_2_out, DIN, DIN1, DOUT,
       EX_IR, ex_mem_1_pc_2, ex_mem_1_rs_2, ex_mem_1_rt_2, id_ex_1_e1_2, id_ex_1_e2_2, id_ex_1_pc_2,
       id_ex_1_rs_2, id_ex_1_rt_2, ID_IR, if_id_1_pc_2, IF_IR, MEM_IR, mem_wb_1_aluresult_2, mem_wb_1_dout_2,
       mem_wb_1_pc_2, mips_alu_1_result, mips_regifile_1_r1, mips_regifile_1_r2, multiplexer_1_out,
       multiplexer_2_out, multiplexer_3_out, multiplexer_8_out, multiplexer_11_out, multiplexer_12_out,
       multiplexer_14_out, shifter_1_out, v0, WB_IR;

  Button \u_总复位  (.out(RST));
  Button _1 (.out(IR1));
  Button _2 (.out(IR2));
  Button _3 (.out(IR3));
  // Probe on \总周期数 
  // Probe on \总周期数 
  Button \u_继续运行  (.out(Go));
  LED #(.active("true")) led_1 (.in(W1));
  LED #(.active("true")) led_2 (.in(W2));
  LED #(.active("true")) led_3 (.in(W3));
  Hex_Digit_Display hex_digit_display_1 (.value(LedData[31:28]));  // open: dp
  // Probe on IF_PC[19:0]
  // Mips_Probe mips_probe_1: pin names not known; wires that end beside it: IF_IR
  Multiplexer #(.select(1), .width(32), .disabled("Z"), .enable("false")) multiplexer_1 (
    .in0(adder_1_out), .in1(adder_2_out), .out(multiplexer_1_out), .sel(or_1_out));
  Hex_Digit_Display hex_digit_display_2 (.value(LedData[23:20]));  // open: dp
  Hex_Digit_Display hex_digit_display_3 (.value(LedData[27:24]));  // open: dp
  // Probe on ID_PC[19:0]
  // Mips_Probe mips_probe_2: pin names not known; wires that end beside it: ID_IR
  Multiplexer #(.select(1), .width(32), .disabled("Z"), .enable("false")) multiplexer_2 (
    .in0({id_ex_1_pc_2[31:28], EX_IR[25:0], 2'b00}), .in1(id_ex_1_rs_2), .out(multiplexer_2_out),
    .sel(id_ex_1_jr_2));
  Hex_Digit_Display hex_digit_display_4 (.value(LedData[15:12]));  // open: dp
  Hex_Digit_Display hex_digit_display_5 (.value(LedData[19:16]));  // open: dp
  Multiplexer #(.select(1), .width(32), .disabled("Z"), .enable("false")) multiplexer_3 (
    .in0(multiplexer_1_out), .in1(multiplexer_2_out), .out(multiplexer_3_out), .sel(id_ex_1_jmp_2));
  Hex_Digit_Display hex_digit_display_6 (.value(LedData[7:4]));  // open: dp
  Hex_Digit_Display hex_digit_display_7 (.value(LedData[11:8]));  // open: dp
  Clock #(.highDuration(1), .lowDuration(1)) clock_1 (.out(clock_1_out));
  // Probe on EX_PC[19:0]
  // Mips_Probe mips_probe_3: pin names not known; wires that end beside it: clock_1_out, EX_IR, CLK
  Register #(.width(32), .trigger("rising"), .Select("low")) PC (
    .D(multiplexer_3_out), .en(en), .Q(IF_PC), .clk(CLK));  // open: clr
  Hex_Digit_Display hex_digit_display_8 (.value(LedData[3:0]));  // open: dp
  Adder #(.width(32)) adder_1 (.a(IF_PC), .b(32'h4), .out(adder_1_out));  // open: cin, cout
  // Probe on \总周期数 
  // Probe on M_PC[19:0]
  // Mips_Probe mips_probe_4: pin names not known; wires that end beside it: MEM_IR
  // Probe on \总周期数 
  // Probe on \无条件分支数 
  // Probe on \条件分支成功数 
  // Probe on \插入气泡数 
  // Probe on \LoadUse次数 
  // Mips_Probe mips_probe_5: pin names not known; wires that end beside it: IF_IR
  ROM #(.addrWidth(10), .dataWidth(32), .Select("high")) rom_1 (.addr(IF_PC[11:2]), .data(IF_IR));
  // Probe on IF_PC[11:0]
  // Probe on WB_PC[19:0]
  // Mips_Probe mips_probe_6: pin names not known; wires that end beside it: WB_IR
  IF_ID if_id_1 (
    .CLK(CLK), .PC_2(if_id_1_pc_2), .IR_2(ID_IR), .PCN_2(ID_PC), .EN(not_1_out), .PCN(IF_PC), .CLR(1'b0),
    .PC(adder_1_out), .IR(IF_IR));  // open: RST
  not not_1 (not_1_out, en);
  // Probe on EX_PC[11:0]
  // Probe on ID_PC[11:0]
  // Probe on M_PC[11:0]
  D_Flip_Flop #(.trigger("high"), .Pre_Clr_Positions("LEGACY"), .NegatePresetClear("false"), .enable("true"), .NewFFLayout("false")) d_ff_1 (.Q(d_ff_1_q));  // open: clk, D, Qn, preset, en, reset
  // Probe on 13'h4
  Multiplexer #(.select(1), .width(5), .disabled("Z"), .enable("false")) multiplexer_4 (
    .in0(ID_IR[25:21]), .in1(5'b00100), .out(multiplexer_4_out), .sel(\单周期硬布线控制器_1_syscall ));
  Multiplexer #(.select(1), .width(5), .disabled("Z"), .enable("false")) multiplexer_5 (
    .in0(ID_IR[20:16]), .in1(5'b00010), .out(multiplexer_5_out), .sel(\单周期硬布线控制器_1_syscall ));
  // Probe on WB_PC[11:0]
  Comparator #(.width(13), .mode("twosComplement")) comparator_1 (
    .a(CNT_num), .b(13'h4), .eq(comparator_1_eq), .lt(comparator_1_lt));  // open: gt
  Clock #(.highDuration(1), .lowDuration(1)) clock_2 (.out(clock_2_out));
  \单周期硬布线控制器  \u_单周期硬布线控制器_1  (
    .Func(ID_IR[5:0]), .OP(ID_IR[31:26]), .ALU_OP(\单周期硬布线控制器_1_alu_op ), .MemToReg(\单周期硬布线控制器_1_memtoreg ),
    .MemWrite(\单周期硬布线控制器_1_memwrite ), .ALU_SRC(\单周期硬布线控制器_1_alu_src ), .RegWrite(\单周期硬布线控制器_1_regwrite ),
    .SysCALL(\单周期硬布线控制器_1_syscall ), .SignedExt(SignedExt), .RegDst(\单周期硬布线控制器_1_regdst ),
    .JR(\单周期硬布线控制器_1_jr ), .JMP(\单周期硬布线控制器_1_jmp ), .Beq(\单周期硬布线控制器_1_beq ), .JAL(\单周期硬布线控制器_1_jal ),
    .Bne(\单周期硬布线控制器_1_bne ), .SB(\单周期硬布线控制器_1_sb ), .BLTZ(\单周期硬布线控制器_1_bltz ));
  assign bit_extender_1_out = {{16{1'b0}}, ID_IR[15:0]};  // Bit_Extender bit_extender_1
  assign bit_extender_2_out = {{16{ID_IR[15]}}, ID_IR[15:0]};  // Bit_Extender bit_extender_2
  nand nand_1 (nand_1_out, d_ff_1_q, comparator_1_eq);
  Counter #(.width(13), .max('h1fff), .ongoal("stay"), .trigger("rising"), .behavior("old")) counter_1 (
    .count(comparator_1_lt), .Q(CNT_num), .clk(clock_2_out));  // open: load, D, carry, clr, preset
  Multiplexer #(.select(1), .width(5), .disabled("Z"), .enable("false")) multiplexer_6 (
    .in0(ID_IR[20:16]), .in1(ID_IR[15:11]), .out(multiplexer_6_out), .sel(\单周期硬布线控制器_1_regdst ));
  Multiplexer #(.select(1), .width(5), .disabled("Z"), .enable("false")) multiplexer_7 (
    .in0(multiplexer_6_out), .in1({5{1'b1}}), .out(multiplexer_7_out), .sel(\单周期硬布线控制器_1_jal ));
  Multiplexer #(.select(1), .width(32), .disabled("Z"), .enable("false")) multiplexer_8 (
    .in0(bit_extender_1_out), .in1(bit_extender_2_out), .out(multiplexer_8_out), .sel(SignedExt));
  assign CLK = nand_1_out ? clock_2_out : 1'bz;  // Controlled_Buffer controlled_buffer_1
  Pull_Resistor #(.pull(1)) pull_resistor_1 (.node(CLK));
  Multiplexer #(.select(1), .width(32), .disabled("Z"), .enable("false")) multiplexer_9 (
    .in0(multiplexer_14_out), .in1(mem_wb_1_pc_2), .out(RDin), .sel(mem_wb_1_jal_2));
  Counter #(.width(16), .max('hffff), .ongoal("stay"), .trigger("rising"), .behavior("old")) counter_2 (
    .count(en), .Q(\总周期数 ), .clk(CLK));  // open: load, D, carry, clr, preset
  MIPS_Regifile mips_regifile_1 (
    .Din(RDin), .Clk(CLK), .R1(mips_regifile_1_r1), .R2(mips_regifile_1_r2), .WE(RegWrite),
    .W_num(mem_wb_1_wr_2), .R1_num(multiplexer_4_out), .R2_num(multiplexer_5_out));
  not not_2 (not_2_out, en);
  ID_EX id_ex_1 (
    .CLK(CLK), .JMP_2(id_ex_1_jmp_2), .JR_2(id_ex_1_jr_2), .SB_2(id_ex_1_sb_2), .BLTZ_2(id_ex_1_bltz_2),
    .Beq_2(id_ex_1_beq_2), .RegWrite_2(id_ex_1_regwrite_2), .Bne_2(id_ex_1_bne_2),
    .MemToReg_2(id_ex_1_memtoreg_2), .MemWrite_2(id_ex_1_memwrite_2), .AluSrcB_2(id_ex_1_alusrcb_2),
    .JAL_2(id_ex_1_jal_2), .AluOP(id_ex_1_aluop), .RS_2(id_ex_1_rs_2), .E1_2(id_ex_1_e1_2),
    .RT_2(id_ex_1_rt_2), .E2_2(id_ex_1_e2_2), .PC_2(id_ex_1_pc_2), .WR_2(id_ex_1_wr_2),
    .shamt_2(id_ex_1_shamt_2), .PCN_2(EX_PC), .IR_2(EX_IR), .EN(not_2_out), .CLR(1'b0),
    .JMP(\单周期硬布线控制器_1_jmp ), .JR(\单周期硬布线控制器_1_jr ), .SB(\单周期硬布线控制器_1_sb ), .BLTZ(\单周期硬布线控制器_1_bltz ),
    .Beq(\单周期硬布线控制器_1_beq ), .RegWrite(\单周期硬布线控制器_1_regwrite ), .Bne(\单周期硬布线控制器_1_bne ),
    .MemToReg(\单周期硬布线控制器_1_memtoreg ), .MemWrite(\单周期硬布线控制器_1_memwrite ), .AluSrcB(\单周期硬布线控制器_1_alu_src ),
    .JAL(\单周期硬布线控制器_1_jal ), .in_16(\单周期硬布线控制器_1_alu_op ), .WR(multiplexer_7_out), .shamt(ID_IR[10:6]),
    .RS(mips_regifile_1_r1), .E1(multiplexer_8_out), .PCN(ID_PC), .RT(mips_regifile_1_r2),
    .E2(bit_extender_2_out), .IR(ID_IR), .PC(if_id_1_pc_2), .SysCall(\单周期硬布线控制器_1_syscall ),
    .SysCall_2(id_ex_1_syscall_2));  // open: RsForward, RsForward_2, RtForward, RtForward_2, RST
  Multiplexer #(.select(2), .width(32), .disabled("Z"), .enable("false")) multiplexer_10 (
    .in0({DOUT[31:8], DIN[7:0]}), .in1({DOUT[31:16], DIN[7:0], DOUT[7:0]}),
    .in2({DOUT[31:24], DIN[7:0], DOUT[15:0]}), .in3({DIN[7:0], DOUT[23:0]}), .out(DIN1), .sel(AIN[1:0]));
  Multiplexer #(.select(1), .width(32), .disabled("Z"), .enable("false")) multiplexer_11 (
    .in0(id_ex_1_rt_2), .in1(id_ex_1_e1_2), .out(multiplexer_11_out), .sel(id_ex_1_alusrcb_2));
  Multiplexer #(.select(1), .width(32), .disabled("Z"), .enable("false")) multiplexer_12 (
    .in0(multiplexer_11_out), .in1({32{1'b0}}), .out(multiplexer_12_out), .sel(id_ex_1_bltz_2));
  Shifter #(.width(32), .shift("ll")) shifter_1 (.in(id_ex_1_e2_2), .\dist (5'b00010), .out(shifter_1_out));
  MIPS_ALU mips_alu_1 (
    .X(id_ex_1_rs_2), .Y(multiplexer_12_out), .AluOP(id_ex_1_aluop), .Equal(mips_alu_1_equal),
    .Result(mips_alu_1_result), .shamt(id_ex_1_shamt_2));  // open: Result_2
  Adder #(.width(32)) adder_2 (.a(shifter_1_out), .b(id_ex_1_pc_2), .out(adder_2_out), .cin(1'b0));  // open: cout
  and and_1 (and_1_out, id_ex_1_beq_2, mips_alu_1_equal);
  Comparator #(.width(32), .mode("twosComplement")) comparator_2 (
    .a(32'h1), .b(mips_alu_1_result), .eq(comparator_2_eq));  // open: gt, lt
  Comparator #(.width(32), .mode("unsigned")) comparator_3 (.a(v0), .b(32'h32), .eq(comparator_3_eq));  // open: gt, lt
  or or_1 (or_1_out, and_1_out, and_2_out, and_3_out);
  and and_2 (and_2_out, id_ex_1_bne_2, ~mips_alu_1_equal);  // AND_Gate
  Register #(.width(32), .trigger("rising"), .Select("low")) register_1 (
    .D(a0), .en(sys), .Q(LedData), .clk(CLK));  // open: clr
  or or_2 (or_2_out, comparator_3_eq, Go);
  and and_3 (and_3_out, id_ex_1_bltz_2, comparator_2_eq);
  and and_4 (and_4_out, or_2_out, sys);
  not not_3 (not_3_out, en);
  T_Flip_Flop #(.trigger("rising"), .Pre_Clr_Positions("ABOVE_BELOW"), .NegatePresetClear("false"), .enable("false"), .NewFFLayout("true")) t_ff_1 (
    .clk(and_4_out), .T(1'b1), .Qn(en));  // open: Q, preset, reset
  EX_MEM ex_mem_1 (
    .CLK(CLK), .WR(id_ex_1_wr_2), .SB_2(ex_mem_1_sb_2), .MemToReg_2(ex_mem_1_memtoreg_2),
    .MemWrite_2(MemWrite), .RegWrite_2(ex_mem_1_regwrite_2), .JAL_2(ex_mem_1_jal_2), .WR_2(ex_mem_1_wr_2),
    .AluResult_2(AIN), .WriteData_2(DIN), .PC_2(ex_mem_1_pc_2), .IR_2(MEM_IR), .PCN_2(M_PC), .EN(not_3_out),
    .CLR(1'b0), .SB(id_ex_1_sb_2), .MemToReg(id_ex_1_memtoreg_2), .MemWrite(id_ex_1_memwrite_2),
    .RegWrite(id_ex_1_regwrite_2), .JAL(id_ex_1_jal_2), .AluResult(mips_alu_1_result),
    .WriteData(id_ex_1_rt_2), .PC(id_ex_1_pc_2), .IR(EX_IR), .PCN(EX_PC), .RS(id_ex_1_rs_2),
    .RS_2(ex_mem_1_rs_2), .RT(id_ex_1_rt_2), .RT_2(ex_mem_1_rt_2), .SysCall(id_ex_1_syscall_2),
    .SysCall_2(ex_mem_1_syscall_2));  // open: RST
  Multiplexer #(.select(1), .width(32), .disabled("Z"), .enable("false")) multiplexer_13 (
    .in0(DIN), .in1(DIN1), .out(MDin), .sel(ex_mem_1_sb_2));
  RAM #(.addrWidth(10), .dataWidth(32), .bus("separate"), .Select("high")) ram_1 (
    .addr(AIN[11:2]), .din(MDin), .data(DOUT), .str(MemWrite), .clk(CLK));  // open: sel, ld, clr
  not not_4 (not_4_out, en);
  MEM_WB mem_wb_1 (
    .RegWrite_2(RegWrite), .JAL_2(mem_wb_1_jal_2), .AluResult_2(mem_wb_1_aluresult_2),
    .Dout_2(mem_wb_1_dout_2), .WR(ex_mem_1_wr_2), .WR_2(mem_wb_1_wr_2), .CLK(CLK), .PC_2(mem_wb_1_pc_2),
    .MemToReg_2(mem_wb_1_memtoreg_2), .IR_2(WB_IR), .PCN_2(WB_PC), .EN(not_4_out), .CLR(1'b0),
    .RegWrite(ex_mem_1_regwrite_2), .MemToReg(ex_mem_1_memtoreg_2), .JAL(ex_mem_1_jal_2), .AluResult(AIN),
    .Dout(DOUT), .PC(ex_mem_1_pc_2), .IR(MEM_IR), .PCN(M_PC), .RS(ex_mem_1_rs_2), .RS_2(a0),
    .RT(ex_mem_1_rt_2), .RT_2(v0), .SysCall(ex_mem_1_syscall_2), .SysCall_2(sys));  // open: in_8
  Multiplexer #(.select(1), .width(32), .disabled("Z"), .enable("false")) multiplexer_14 (
    .in0(mem_wb_1_aluresult_2), .in1(mem_wb_1_dout_2), .out(multiplexer_14_out), .sel(mem_wb_1_memtoreg_2));

  // Other names for the same wires on the sheet: MEM_PC[31:0] = M_PC

  // Notes on the sheet:
  //   中断源
  //   时空图监测，可删除
  //   中断等待指示
  //   数码管输出
  //   指令存储器
  //   指令字
  //   contents of rom_1 (hex, n*v repeats v):
  //   20100000 20110000 20120000 20130000 36100000 36310001 36520002 36730003 ae100000 ae110004 ae120008
  //   ae13000c 2002000a 20110000 20120000 20130000 c
  //   控制位
  //   OP
  //   Func
  //   rs
  //   rt
  //   rd
  //   流水调试日志用
  //   暂停节拍，不能为0
  //   JMP
  //   JR
  //   OP
  //   Func
  //   戳工具置1进入计数暂停模式，ctrl+k时钟自动运行到对应节拍暂停
  //   ctrl+k关闭时钟连续运行，将控制位置零，进入单步调试模式调试
  //   用这个时钟源需要去掉电路中的其他时钟源
  //   SB
  //   BLTZ
  //   Beq
  //   Bne
  //   MemToReg
  //   MemWrite
  //   AluOP
  //   AluSrcB
  //   RegWrite
  //   JAL
  //   RegDst
  //   Syscall
  //   可计数暂停的时钟源
  //   为方便自动评测，需要输出流水线各段保存的PC值，注意是PC不是PC+4，另外ID段寄存器写入信息，Mem段内存写入信息也要输出
endmodule

module \气泡流水线  (
  output RegWrite,
  output MemWrite,
  output [31:0] IF_PC,
  output [31:0] ID_PC,
  output [31:0] EX_PC,
  output [31:0] M_PC,
  output [31:0] WB_PC,
  output [31:0] RDin,
  output [31:0] MDin,
  output [31:0] LedData
);

  wire and_1_out, and_2_out, and_3_out, and_4_out, and_5_out, CLK, clock_1_out, clock_2_out, comparator_1_eq,
       comparator_1_lt, comparator_2_eq, comparator_3_eq, d_ff_1_q, en, ex_mem_1_jal_2, ex_mem_1_memtoreg_2,
       ex_mem_1_regwrite_2, ex_mem_1_sb_2, ex_mem_1_syscall_2, Go, id_ex_1_alusrcb_2, id_ex_1_beq_2,
       id_ex_1_bltz_2, id_ex_1_bne_2, id_ex_1_jal_2, id_ex_1_jmp_2, id_ex_1_jr_2, id_ex_1_memtoreg_2,
       id_ex_1_memwrite_2, id_ex_1_regwrite_2, id_ex_1_sb_2, id_ex_1_syscall_2, IR1, IR2, IR3,
       mem_wb_1_jal_2, mem_wb_1_memtoreg_2, mips_alu_1_equal, nand_1_out, not_1_out, not_2_out, not_3_out,
       not_4_out, or_1_out, or_2_out, or_3_out, or_4_out, RST, SignedExt, sys, W1, W2, W3,
       \单周期硬布线控制器_1_alu_src , \单周期硬布线控制器_1_beq , \单周期硬布线控制器_1_bltz , \单周期硬布线控制器_1_bne , \单周期硬布线控制器_1_jal ,
       \单周期硬布线控制器_1_jmp , \单周期硬布线控制器_1_jr , \单周期硬布线控制器_1_memtoreg , \单周期硬布线控制器_1_memwrite ,
       \单周期硬布线控制器_1_regdst , \单周期硬布线控制器_1_regwrite , \单周期硬布线控制器_1_sb , \单周期硬布线控制器_1_syscall ,
       \气泡流水线处理逻辑_1_flush , \气泡流水线处理逻辑_1_stall ;
  wire [3:0] id_ex_1_aluop, \单周期硬布线控制器_1_alu_op ;
  wire [4:0] ex_mem_1_wr_2, id_ex_1_shamt_2, id_ex_1_wr_2, mem_wb_1_wr_2, multiplexer_4_out,
       multiplexer_5_out, multiplexer_6_out, multiplexer_7_out;
  wire [12:0] CNT_num;
  wire [15:0] \LoadUse次数 , \总周期数 , \插入气泡数 , \无条件分支数 , \条件分支成功数 ;
  wire [31:0] a0, adder_1_out, adder_2_out, AIN, bit_extender_1_out, bit_extender_2_out, DIN, DIN1, DOUT,
       EX_IR, ex_mem_1_pc_2, ex_mem_1_rs_2, ex_mem_1_rt_2, id_ex_1_e1_2, id_ex_1_e2_2, id_ex_1_pc_2,
       id_ex_1_rs_2, id_ex_1_rt_2, ID_IR, if_id_1_pc_2, IF_IR, MEM_IR, mem_wb_1_aluresult_2, mem_wb_1_dout_2,
       mem_wb_1_pc_2, mips_alu_1_result, mips_regifile_1_r1, mips_regifile_1_r2, multiplexer_1_out,
       multiplexer_2_out, multiplexer_3_out, multiplexer_8_out, multiplexer_10_out, multiplexer_11_out,
       multiplexer_14_out, shifter_1_out, v0, WB_IR;

  Button \u_总复位  (.out(RST));
  Button _1 (.out(IR1));
  Button _2 (.out(IR2));
  Button _3 (.out(IR3));
  // Probe on \总周期数 
  // Probe on \总周期数 
  Button \u_继续运行  (.out(Go));
  LED #(.active("true")) led_1 (.in(W1));
  LED #(.active("true")) led_2 (.in(W2));
  LED #(.active("true")) led_3 (.in(W3));
  Hex_Digit_Display hex_digit_display_1 (.value(LedData[31:28]));  // open: dp
  // Probe on IF_PC[19:0]
  // Mips_Probe mips_probe_1: pin names not known; wires that end beside it: IF_IR
  Hex_Digit_Display hex_digit_display_2 (.value(LedData[27:24]));  // open: dp
  Hex_Digit_Display hex_digit_display_3 (.value(LedData[23:20]));  // open: dp
  // Probe on ID_PC[19:0]
  // Mips_Probe mips_probe_2: pin names not known; wires that end beside it: ID_IR
  Hex_Digit_Display hex_digit_display_4 (.value(LedData[19:16]));  // open: dp
  Hex_Digit_Display hex_digit_display_5 (.value(LedData[15:12]));  // open: dp
  Hex_Digit_Display hex_digit_display_6 (.value(LedData[11:8]));  // open: dp
  Hex_Digit_Display hex_digit_display_7 (.value(LedData[7:4]));  // open: dp
  Clock #(.highDuration(1), .lowDuration(1)) clock_1 (.out(clock_1_out));
  // Probe on EX_PC[19:0]
  // Mips_Probe mips_probe_3: pin names not known; wires that end beside it: clock_1_out, EX_IR, CLK
  Multiplexer #(.select(1), .width(32), .disabled("Z"), .enable("false")) multiplexer_1 (
    .in0(adder_1_out), .in1(adder_2_out), .out(multiplexer_1_out), .sel(or_3_out));
  Hex_Digit_Display hex_digit_display_8 (.value(LedData[3:0]));  // open: dp
  \气泡流水线处理逻辑  \u_气泡流水线处理逻辑_1  (
    .rt(multiplexer_5_out), .rs(multiplexer_4_out), .MEM_RegWrite(ex_mem_1_regwrite_2),
    .EX_RegWrite(id_ex_1_regwrite_2), .MEM_WR(ex_mem_1_wr_2), .EX_WR(id_ex_1_wr_2), .Instr(ID_IR),
    .BranchTaken(or_2_out), .Flush(\气泡流水线处理逻辑_1_flush ), .Stall(\气泡流水线处理逻辑_1_stall ));
  Multiplexer #(.select(1), .width(32), .disabled("Z"), .enable("false")) multiplexer_2 (
    .in0({id_ex_1_pc_2[31:28], EX_IR[25:0], 2'b00}), .in1(id_ex_1_rs_2), .out(multiplexer_2_out),
    .sel(id_ex_1_jr_2));
  // Probe on \总周期数 
  // Probe on M_PC[19:0]
  // Mips_Probe mips_probe_4: pin names not known; wires that end beside it: MEM_IR
  and and_1 (and_1_out, en, ~\气泡流水线处理逻辑_1_stall );  // AND_Gate
  Multiplexer #(.select(1), .width(32), .disabled("Z"), .enable("false")) multiplexer_3 (
    .in0(multiplexer_1_out), .in1(multiplexer_2_out), .out(multiplexer_3_out), .sel(id_ex_1_jmp_2));
  // Probe on \总周期数 
  // Probe on \无条件分支数 
  // Probe on \条件分支成功数 
  // Probe on \插入气泡数 
  // Probe on \LoadUse次数 
  Register #(.width(32), .trigger("rising"), .Select("low")) register_1 (
    .D(multiplexer_3_out), .en(and_1_out), .Q(IF_PC), .clk(CLK));  // open: clr
  // Probe on IF_PC[11:0]
  // Probe on WB_PC[19:0]
  // Mips_Probe mips_probe_5: pin names not known; wires that end beside it: WB_IR
  Adder #(.width(32)) adder_1 (.a(IF_PC), .b(32'h4), .out(adder_1_out));  // open: cin, cout
  // Probe on EX_PC[11:0]
  // Probe on ID_PC[11:0]
  // Probe on M_PC[11:0]
  D_Flip_Flop #(.trigger("high"), .Pre_Clr_Positions("LEGACY"), .NegatePresetClear("false"), .enable("true"), .NewFFLayout("false")) d_ff_1 (.Q(d_ff_1_q));  // open: clk, D, Qn, preset, en, reset
  // Probe on 13'he25
  // Mips_Probe mips_probe_6: pin names not known; wires that end beside it: IF_IR
  ROM #(.addrWidth(10), .dataWidth(32), .Select("high")) rom_1 (.addr(IF_PC[11:2]), .data(IF_IR));
  // Probe on WB_PC[11:0]
  Comparator #(.width(13), .mode("twosComplement")) comparator_1 (
    .a(CNT_num), .b(13'he25), .eq(comparator_1_eq), .lt(comparator_1_lt));  // open: gt
  Clock #(.highDuration(1), .lowDuration(1)) clock_2 (.out(clock_2_out));
  or or_1 (or_1_out, ~en, \气泡流水线处理逻辑_1_stall );  // OR_Gate
  IF_ID if_id_1 (
    .CLK(CLK), .PC_2(if_id_1_pc_2), .IR_2(ID_IR), .PCN_2(ID_PC), .EN(or_1_out), .PCN(IF_PC), .CLR(or_2_out),
    .PC(adder_1_out), .IR(IF_IR));  // open: RST
  nand nand_1 (nand_1_out, d_ff_1_q, comparator_1_eq);
  Counter #(.width(13), .max('h1fff), .ongoal("stay"), .trigger("rising"), .behavior("old")) counter_1 (
    .count(comparator_1_lt), .Q(CNT_num), .clk(clock_2_out));  // open: load, D, carry, clr, preset
  assign CLK = nand_1_out ? clock_2_out : 1'bz;  // Controlled_Buffer controlled_buffer_1
  Multiplexer #(.select(1), .width(5), .disabled("Z"), .enable("false")) multiplexer_4 (
    .in0(ID_IR[25:21]), .in1(5'b00100), .out(multiplexer_4_out), .sel(\单周期硬布线控制器_1_syscall ));
  Multiplexer #(.select(1), .width(5), .disabled("Z"), .enable("false")) multiplexer_5 (
    .in0(ID_IR[20:16]), .in1(5'b00010), .out(multiplexer_5_out), .sel(\单周期硬布线控制器_1_syscall ));
  Pull_Resistor #(.pull(1)) pull_resistor_1 (.node(CLK));
  \单周期硬布线控制器  \u_单周期硬布线控制器_1  (
    .Func(ID_IR[5:0]), .OP(ID_IR[31:26]), .ALU_OP(\单周期硬布线控制器_1_alu_op ), .MemToReg(\单周期硬布线控制器_1_memtoreg ),
    .MemWrite(\单周期硬布线控制器_1_memwrite ), .ALU_SRC(\单周期硬布线控制器_1_alu_src ), .RegWrite(\单周期硬布线控制器_1_regwrite ),
    .SysCALL(\单周期硬布线控制器_1_syscall ), .SignedExt(SignedExt), .RegDst(\单周期硬布线控制器_1_regdst ),
    .JR(\单周期硬布线控制器_1_jr ), .JMP(\单周期硬布线控制器_1_jmp ), .Beq(\单周期硬布线控制器_1_beq ), .JAL(\单周期硬布线控制器_1_jal ),
    .Bne(\单周期硬布线控制器_1_bne ), .SB(\单周期硬布线控制器_1_sb ), .BLTZ(\单周期硬布线控制器_1_bltz ));
  Multiplexer #(.select(1), .width(5), .disabled("Z"), .enable("false")) multiplexer_6 (
    .in0(ID_IR[20:16]), .in1(ID_IR[15:11]), .out(multiplexer_6_out), .sel(\单周期硬布线控制器_1_regdst ));
  assign bit_extender_1_out = {{16{1'b0}}, ID_IR[15:0]};  // Bit_Extender bit_extender_1
  assign bit_extender_2_out = {{16{ID_IR[15]}}, ID_IR[15:0]};  // Bit_Extender bit_extender_2
  Multiplexer #(.select(1), .width(5), .disabled("Z"), .enable("false")) multiplexer_7 (
    .in0(multiplexer_6_out), .in1({5{1'b1}}), .out(multiplexer_7_out), .sel(\单周期硬布线控制器_1_jal ));
  Multiplexer #(.select(1), .width(32), .disabled("Z"), .enable("false")) multiplexer_8 (
    .in0(bit_extender_1_out), .in1(bit_extender_2_out), .out(multiplexer_8_out), .sel(SignedExt));
  Multiplexer #(.select(1), .width(32), .disabled("Z"), .enable("false")) multiplexer_9 (
    .in0(multiplexer_14_out), .in1(mem_wb_1_pc_2), .out(RDin), .sel(mem_wb_1_jal_2));
  not not_1 (not_1_out, CLK);
  MIPS_Regifile mips_regifile_1 (
    .Din(RDin), .Clk(not_1_out), .R1(mips_regifile_1_r1), .R2(mips_regifile_1_r2), .WE(RegWrite),
    .W_num(mem_wb_1_wr_2), .R1_num(multiplexer_4_out), .R2_num(multiplexer_5_out));
  not not_2 (not_2_out, en);
  ID_EX id_ex_1 (
    .CLK(CLK), .JMP_2(id_ex_1_jmp_2), .JR_2(id_ex_1_jr_2), .SB_2(id_ex_1_sb_2), .BLTZ_2(id_ex_1_bltz_2),
    .Beq_2(id_ex_1_beq_2), .RegWrite_2(id_ex_1_regwrite_2), .Bne_2(id_ex_1_bne_2),
    .MemToReg_2(id_ex_1_memtoreg_2), .MemWrite_2(id_ex_1_memwrite_2), .AluSrcB_2(id_ex_1_alusrcb_2),
    .JAL_2(id_ex_1_jal_2), .AluOP(id_ex_1_aluop), .RS_2(id_ex_1_rs_2), .E1_2(id_ex_1_e1_2),
    .RT_2(id_ex_1_rt_2), .E2_2(id_ex_1_e2_2), .PC_2(id_ex_1_pc_2), .WR_2(id_ex_1_wr_2),
    .shamt_2(id_ex_1_shamt_2), .PCN_2(EX_PC), .IR_2(EX_IR), .EN(not_2_out), .CLR(\气泡流水线处理逻辑_1_flush ),
    .JMP(\单周期硬布线控制器_1_jmp ), .JR(\单周期硬布线控制器_1_jr ), .SB(\单周期硬布线控制器_1_sb ), .BLTZ(\单周期硬布线控制器_1_bltz ),
    .Beq(\单周期硬布线控制器_1_beq ), .RegWrite(\单周期硬布线控制器_1_regwrite ), .Bne(\单周期硬布线控制器_1_bne ),
    .MemToReg(\单周期硬布线控制器_1_memtoreg ), .MemWrite(\单周期硬布线控制器_1_memwrite ), .AluSrcB(\单周期硬布线控制器_1_alu_src ),
    .JAL(\单周期硬布线控制器_1_jal ), .in_16(\单周期硬布线控制器_1_alu_op ), .WR(multiplexer_7_out), .shamt(ID_IR[10:6]),
    .RS(mips_regifile_1_r1), .E1(multiplexer_8_out), .PCN(ID_PC), .RT(mips_regifile_1_r2),
    .E2(bit_extender_2_out), .IR(ID_IR), .PC(if_id_1_pc_2), .SysCall(\单周期硬布线控制器_1_syscall ),
    .SysCall_2(id_ex_1_syscall_2));  // open: RsForward, RsForward_2, RtForward, RtForward_2, RST
  or or_2 (or_2_out, id_ex_1_jmp_2, id_ex_1_jr_2, or_3_out);
  Multiplexer #(.select(1), .width(32), .disabled("Z"), .enable("false")) multiplexer_10 (
    .in0(id_ex_1_rt_2), .in1(id_ex_1_e1_2), .out(multiplexer_10_out), .sel(id_ex_1_alusrcb_2));
  Multiplexer #(.select(1), .width(32), .disabled("Z"), .enable("false")) multiplexer_11 (
    .in0(multiplexer_10_out), .in1({32{1'b0}}), .out(multiplexer_11_out), .sel(id_ex_1_bltz_2));
  Shifter #(.width(32), .shift("ll")) shifter_1 (.in(id_ex_1_e2_2), .\dist (5'b00010), .out(shifter_1_out));
  MIPS_ALU mips_alu_1 (
    .X(id_ex_1_rs_2), .Y(multiplexer_11_out), .AluOP(id_ex_1_aluop), .Equal(mips_alu_1_equal),
    .Result(mips_alu_1_result), .shamt(id_ex_1_shamt_2));  // open: Result_2
  Adder #(.width(32)) adder_2 (.a(shifter_1_out), .b(id_ex_1_pc_2), .out(adder_2_out), .cin(1'b0));  // open: cout
  Counter #(.width(16), .max('hffff), .ongoal("stay"), .trigger("rising"), .behavior("old")) counter_2 (
    .count(en), .Q(\总周期数 ), .clk(CLK));  // open: load, D, carry, clr, preset
  and and_2 (and_2_out, id_ex_1_beq_2, mips_alu_1_equal);
  Comparator #(.width(32), .mode("twosComplement")) comparator_2 (
    .a(32'h1), .b(mips_alu_1_result), .eq(comparator_2_eq));  // open: gt, lt
  or or_3 (or_3_out, and_2_out, and_3_out, and_4_out);
  and and_3 (and_3_out, id_ex_1_bne_2, ~mips_alu_1_equal);  // AND_Gate
  and and_4 (and_4_out, id_ex_1_bltz_2, comparator_2_eq);
  not not_3 (not_3_out, en);
  EX_MEM ex_mem_1 (
    .CLK(CLK), .WR(id_ex_1_wr_2), .SB_2(ex_mem_1_sb_2), .MemToReg_2(ex_mem_1_memtoreg_2),
    .MemWrite_2(MemWrite), .RegWrite_2(ex_mem_1_regwrite_2), .JAL_2(ex_mem_1_jal_2), .WR_2(ex_mem_1_wr_2),
    .AluResult_2(AIN), .WriteData_2(DIN), .PC_2(ex_mem_1_pc_2), .IR_2(MEM_IR), .PCN_2(M_PC), .EN(not_3_out),
    .CLR(1'b0), .SB(id_ex_1_sb_2), .MemToReg(id_ex_1_memtoreg_2), .MemWrite(id_ex_1_memwrite_2),
    .RegWrite(id_ex_1_regwrite_2), .JAL(id_ex_1_jal_2), .AluResult(mips_alu_1_result),
    .WriteData(id_ex_1_rt_2), .PC(id_ex_1_pc_2), .IR(EX_IR), .PCN(EX_PC), .RS(id_ex_1_rs_2),
    .RS_2(ex_mem_1_rs_2), .RT(id_ex_1_rt_2), .RT_2(ex_mem_1_rt_2), .SysCall(id_ex_1_syscall_2),
    .SysCall_2(ex_mem_1_syscall_2));  // open: RST
  Multiplexer #(.select(1), .width(32), .disabled("Z"), .enable("false")) multiplexer_12 (
    .in0(DIN), .in1(DIN1), .out(MDin), .sel(ex_mem_1_sb_2));
  Multiplexer #(.select(2), .width(32), .disabled("Z"), .enable("false")) multiplexer_13 (
    .in0({DOUT[31:8], DIN[7:0]}), .in1({DOUT[31:16], DIN[7:0], DOUT[7:0]}),
    .in2({DOUT[31:24], DIN[7:0], DOUT[15:0]}), .in3({DIN[7:0], DOUT[23:0]}), .out(DIN1), .sel(AIN[1:0]));
  RAM #(.addrWidth(10), .dataWidth(32), .bus("separate"), .Select("high")) ram_1 (
    .addr(AIN[11:2]), .din(MDin), .data(DOUT), .str(MemWrite), .clk(CLK));  // open: sel, ld, clr
  Comparator #(.width(32), .mode("unsigned")) comparator_3 (.a(v0), .b(32'h32), .eq(comparator_3_eq));  // open: gt, lt
  not not_4 (not_4_out, en);
  MEM_WB mem_wb_1 (
    .RegWrite_2(RegWrite), .JAL_2(mem_wb_1_jal_2), .AluResult_2(mem_wb_1_aluresult_2),
    .Dout_2(mem_wb_1_dout_2), .WR(ex_mem_1_wr_2), .WR_2(mem_wb_1_wr_2), .CLK(CLK), .PC_2(mem_wb_1_pc_2),
    .MemToReg_2(mem_wb_1_memtoreg_2), .IR_2(WB_IR), .PCN_2(WB_PC), .EN(not_4_out), .CLR(1'b0),
    .RegWrite(ex_mem_1_regwrite_2), .MemToReg(ex_mem_1_memtoreg_2), .JAL(ex_mem_1_jal_2), .AluResult(AIN),
    .Dout(DOUT), .PC(ex_mem_1_pc_2), .IR(MEM_IR), .PCN(M_PC), .RS(ex_mem_1_rs_2), .RS_2(a0),
    .RT(ex_mem_1_rt_2), .RT_2(v0), .SysCall(ex_mem_1_syscall_2), .SysCall_2(sys));  // open: in_8
  Register #(.width(32), .trigger("rising"), .Select("low")) register_2 (
    .D(a0), .en(sys), .Q(LedData), .clk(CLK));  // open: clr
  or or_4 (or_4_out, comparator_3_eq, Go);
  and and_5 (and_5_out, or_4_out, sys);
  Multiplexer #(.select(1), .width(32), .disabled("Z"), .enable("false")) multiplexer_14 (
    .in0(mem_wb_1_aluresult_2), .in1(mem_wb_1_dout_2), .out(multiplexer_14_out), .sel(mem_wb_1_memtoreg_2));
  T_Flip_Flop #(.trigger("rising"), .Pre_Clr_Positions("ABOVE_BELOW"), .NegatePresetClear("false"), .enable("false"), .NewFFLayout("true")) t_ff_1 (
    .clk(and_5_out), .T(1'b1), .Qn(en));  // open: Q, preset, reset

  // Other names for the same wires on the sheet: MEM_PC[31:0] = M_PC

  // Notes on the sheet:
  //   中断源
  //   时空图监测，可删除
  //   中断等待指示
  //   数码管输出
  //   控制位
  //   指令存储器
  //   流水调试日志用
  //   暂停节拍，不能为0
  //   指令字
  //   contents of rom_1 (hex, n*v repeats v):
  //   20110001 8000c05 20110001 20120002 20130003 8000c09 20110001 20120002 20130003 8000c0d 20110001
  //   20120002 20130003 8000c11 20110001 20120002 20130003 c000cb8 20100001 20110001 118fc0 112020
  //   20020022 c 118882 12200001 8000c15 112020 20020022 c 20110001 118880 112020 20020022 c 12200001
  //   8000c1f 20110001 118fc0 112020 20020022 c 1188c3 112020 20020022 c 118903 112020 20020022 c 118903
  //   112020 20020022 c 118903 112020 20020022 c 118903 112020 20020022 c 118903 112020 20020022 c 118903
  //   112020 20020022 c 118903 112020 20020022 c 20100001 109fc0 139fc3 8021 2012000c 24160003 26100001
  //   3210000f 20080008 20090001 139900 2709825 132020 20020022 c 1094022 1500fff9 22100001 2018000f
  //   2188024 108700 20080008 20090001 139902 2709825 132021 20020022 c 1094022 1500fff9 108702 2c9b022
  //   12c00001 8000c50 4020 1084027 84400 3508ffff 82021 20020022 c 2010ffff 20110000 ae300000 22100001
  //   22310004 ae300000 22100001 22310004 ae300000 22100001 22310004 ae300000 22100001 22310004 ae300000
  //   22100001 22310004 ae300000 22100001 22310004 ae300000 22100001 22310004 ae300000 22100001 22310004
  //   ae300000 22100001 22310004 ae300000 22100001 22310004 ae300000 22100001 22310004 ae300000 22100001
  //   22310004 ae300000 22100001 22310004 ae300000 22100001 22310004 ae300000 22100001 22310004 ae300000
  //   22100001 22310004 22100001 8020 2011003c 8e130000 8e340000 274402a 11000002 ae330000 ae140000
  //   2231fffc 1611fff8 102020 20020022 c 22100004 2011003c 1611fff2 20020032 c 20100000 22100001 102020
  //   20020022 c 22100002 102020 20020022 c 22100003 102020 20020022 c 22100004 102020 20020022 c 22100005
  //   102020 20020022 c 22100006 102020 20020022 c 22100007 102020 20020022 c 22100008 102020 20020022
  //   20020022 c 3e00008
  //   戳工具置1进入计数暂停模式，ctrl+k时钟自动运行到对应节拍暂停
  //   ctrl+k关闭时钟连续运行，将控制位置零，进入单步调试模式调试
  //   OP
  //   Func
  //   rs
  //   rt
  //   rd
  //   可计数暂停的时钟源
  //   JMP
  //   JR
  //   OP
  //   Func
  //   SB
  //   BLTZ
  //   Beq
  //   Bne
  //   MemToReg
  //   MemWrite
  //   AluOP
  //   AluSrcB
  //   RegWrite
  //   JAL
  //   RegDst
  //   Syscall
  //   为方便自动评测，需要输出流水线各段保存的PC值，注意是PC不是PC+4，另外ID段寄存器写入信息，Mem段内存写入信息也要输出
endmodule
module \重定向流水线  (
  output RegWrite,
  output MemWrite,
  output [31:0] IF_PC,
  output [31:0] ID_PC,
  output [31:0] EX_PC,
  output [31:0] M_PC,
  output [31:0] WB_PC,
  output [31:0] RDin,
  output [31:0] MDin,
  output [31:0] LedData
);

  wire and_1_out, and_2_out, and_3_out, and_4_out, and_5_out, Branch, CLK, clock_1_out, clock_2_out,
       comparator_1_eq, comparator_1_lt, comparator_2_eq, comparator_3_eq, d_ff_1_q, en, ex_mem_1_jal_2,
       ex_mem_1_memtoreg_2, ex_mem_1_regwrite_2, ex_mem_1_sb_2, ex_mem_1_syscall_2, Go, id_ex_1_alusrcb_2,
       id_ex_1_beq_2, id_ex_1_bltz_2, id_ex_1_bne_2, id_ex_1_jal_2, id_ex_1_jr_2, id_ex_1_memtoreg_2,
       id_ex_1_memwrite_2, id_ex_1_regwrite_2, id_ex_1_sb_2, id_ex_1_syscall_2, IR1, IR2, IR3, JMP, LoadUse,
       mem_wb_1_jal_2, mem_wb_1_memtoreg_2, mips_alu_1_equal, nand_1_out, not_1_out, not_2_out, not_3_out,
       not_4_out, or_1_out, or_2_out, RST, SignedExt, sys, W1, W2, W3, \单周期硬布线控制器_1_alu_src ,
       \单周期硬布线控制器_1_beq , \单周期硬布线控制器_1_bltz , \单周期硬布线控制器_1_bne , \单周期硬布线控制器_1_jal , \单周期硬布线控制器_1_jmp ,
       \单周期硬布线控制器_1_jr , \单周期硬布线控制器_1_memtoreg , \单周期硬布线控制器_1_memwrite , \单周期硬布线控制器_1_regdst ,
       \单周期硬布线控制器_1_regwrite , \单周期硬布线控制器_1_sb , \单周期硬布线控制器_1_syscall , \重定向流水线处理逻辑_1_flush ,
       \重定向流水线处理逻辑_1_stall ;
  wire [1:0] id_ex_1_rsforward_2, id_ex_1_rtforward_2, \重定向流水线处理逻辑_1_rsforward , \重定向流水线处理逻辑_1_rtforward ;
  wire [3:0] id_ex_1_aluop, \单周期硬布线控制器_1_alu_op ;
  wire [4:0] ex_mem_1_wr_2, id_ex_1_shamt_2, id_ex_1_wr_2, mem_wb_1_wr_2, multiplexer_4_out,
       multiplexer_5_out, multiplexer_6_out, multiplexer_7_out;
  wire [12:0] CNT_num;
  wire [15:0] adder_2_out, \LoadUse次数 , multiplier_1_out, \总周期数 , \插入气泡数 , \无条件分支数 , \条件分支成功数 ;
  wire [31:0] a0, adder_1_out, adder_4_out, AIN, bit_extender_1_out, bit_extender_2_out, DIN, DIN1, DOUT,
       EX_IR, ex_mem_1_pc_2, ex_mem_1_rs_2, ex_mem_1_rt_2, id_ex_1_e1_2, id_ex_1_e2_2, id_ex_1_pc_2,
       id_ex_1_rs_2, id_ex_1_rt_2, ID_IR, if_id_1_pc_2, IF_IR, MEM_IR, mem_wb_1_aluresult_2, mem_wb_1_dout_2,
       mem_wb_1_pc_2, mips_alu_1_result, mips_regifile_1_r1, mips_regifile_1_r2, multiplexer_1_out,
       multiplexer_2_out, multiplexer_3_out, multiplexer_8_out, multiplexer_10_out, multiplexer_11_out,
       multiplexer_12_out, multiplexer_13_out, multiplexer_17_out, shifter_1_out, v0, WB_IR;

  Button \u_总复位  (.out(RST));
  Button _1 (.out(IR1));
  Button _2 (.out(IR2));
  Button _3 (.out(IR3));
  // Probe on \总周期数 
  // Probe on \总周期数 
  Button \u_继续运行  (.out(Go));
  LED #(.active("true")) led_1 (.in(W1));
  LED #(.active("true")) led_2 (.in(W2));
  LED #(.active("true")) led_3 (.in(W3));
  Hex_Digit_Display hex_digit_display_1 (.value(LedData[31:28]));  // open: dp
  // Probe on IF_PC[19:0]
  // Mips_Probe mips_probe_1: pin names not known; wires that end beside it: IF_IR
  Hex_Digit_Display hex_digit_display_2 (.value(LedData[23:20]));  // open: dp
  Hex_Digit_Display hex_digit_display_3 (.value(LedData[27:24]));  // open: dp
  // Probe on ID_PC[19:0]
  // Mips_Probe mips_probe_2: pin names not known; wires that end beside it: ID_IR
  Hex_Digit_Display hex_digit_display_4 (.value(LedData[15:12]));  // open: dp
  Hex_Digit_Display hex_digit_display_5 (.value(LedData[19:16]));  // open: dp
  Hex_Digit_Display hex_digit_display_6 (.value(LedData[7:4]));  // open: dp
  Hex_Digit_Display hex_digit_display_7 (.value(LedData[11:8]));  // open: dp
  Clock #(.highDuration(1), .lowDuration(1)) clock_1 (.out(clock_1_out));
  // Probe on EX_PC[19:0]
  // Mips_Probe mips_probe_3: pin names not known; wires that end beside it: clock_1_out, EX_IR, CLK
  Multiplexer #(.select(1), .width(32), .disabled("Z"), .enable("false")) multiplexer_1 (
    .in0(adder_1_out), .in1(adder_4_out), .out(multiplexer_1_out), .sel(Branch));
  Hex_Digit_Display hex_digit_display_8 (.value(LedData[3:0]));  // open: dp
  \重定向流水线处理逻辑  \u_重定向流水线处理逻辑_1  (
    .Instr(ID_IR), .MEM_RegWrite(ex_mem_1_regwrite_2), .EX_RegWrite(id_ex_1_regwrite_2),
    .MEM_WR(ex_mem_1_wr_2), .EX_WR(id_ex_1_wr_2), .rt(multiplexer_5_out), .rs(multiplexer_4_out),
    .EX_MemToReg(id_ex_1_memtoreg_2), .BranchTaken(or_2_out), .Flush(\重定向流水线处理逻辑_1_flush ),
    .Stall(\重定向流水线处理逻辑_1_stall ), .RsForward(\重定向流水线处理逻辑_1_rsforward ), .RtForward(\重定向流水线处理逻辑_1_rtforward ),
    .LoadUse(LoadUse));
  Multiplexer #(.select(1), .width(32), .disabled("Z"), .enable("false")) multiplexer_2 (
    .in0({id_ex_1_pc_2[31:28], EX_IR[25:0], 2'b00}), .in1(multiplexer_10_out), .out(multiplexer_2_out),
    .sel(id_ex_1_jr_2));
  // Probe on \总周期数 
  // Probe on M_PC[19:0]
  // Mips_Probe mips_probe_4: pin names not known; wires that end beside it: MEM_IR
  and and_1 (and_1_out, en, ~\重定向流水线处理逻辑_1_stall );  // AND_Gate
  Multiplexer #(.select(1), .width(32), .disabled("Z"), .enable("false")) multiplexer_3 (
    .in0(multiplexer_1_out), .in1(multiplexer_2_out), .out(multiplexer_3_out), .sel(JMP));
  // Probe on \总周期数 
  // Probe on \无条件分支数 
  // Probe on \条件分支成功数 
  // Probe on \插入气泡数 
  // Probe on \LoadUse次数 
  Register #(.width(32), .trigger("rising"), .Select("low")) register_1 (
    .D(multiplexer_3_out), .en(and_1_out), .Q(IF_PC), .clk(CLK), .clr(RST));
  // Probe on IF_PC[11:0]
  // Probe on WB_PC[19:0]
  // Mips_Probe mips_probe_5: pin names not known; wires that end beside it: WB_IR
  Adder #(.width(32)) adder_1 (.a(IF_PC), .b(32'h4), .out(adder_1_out));  // open: cin, cout
  // Probe on EX_PC[11:0]
  // Probe on ID_PC[11:0]
  // Probe on M_PC[11:0]
  D_Flip_Flop #(.trigger("high"), .Pre_Clr_Positions("LEGACY"), .NegatePresetClear("false"), .enable("true"), .NewFFLayout("false")) d_ff_1 (.Q(d_ff_1_q));  // open: clk, D, Qn, preset, en, reset
  // Probe on 13'h8f9
  // Mips_Probe mips_probe_6: pin names not known; wires that end beside it: IF_IR
  ROM #(.addrWidth(10), .dataWidth(32), .Select("high")) rom_1 (.addr(IF_PC[11:2]), .data(IF_IR));
  // Probe on WB_PC[11:0]
  Comparator #(.width(13), .mode("twosComplement")) comparator_1 (
    .a(CNT_num), .b(13'h8f9), .eq(comparator_1_eq), .lt(comparator_1_lt));  // open: gt
  Clock #(.highDuration(1), .lowDuration(1)) clock_2 (.out(clock_2_out));
  or or_1 (or_1_out, ~en, \重定向流水线处理逻辑_1_stall );  // OR_Gate
  IF_ID if_id_1 (
    .CLK(CLK), .PC_2(if_id_1_pc_2), .IR_2(ID_IR), .PCN_2(ID_PC), .EN(or_1_out), .PCN(IF_PC), .CLR(or_2_out),
    .PC(adder_1_out), .IR(IF_IR), .RST(RST));
  nand nand_1 (nand_1_out, d_ff_1_q, comparator_1_eq);
  Counter #(.width(13), .max('h1fff), .ongoal("stay"), .trigger("rising"), .behavior("old")) counter_1 (
    .count(comparator_1_lt), .Q(CNT_num), .clk(clock_2_out));  // open: load, D, carry, clr, preset
  assign CLK = nand_1_out ? clock_2_out : 1'bz;  // Controlled_Buffer controlled_buffer_1
  Multiplexer #(.select(1), .width(5), .disabled("Z"), .enable("false")) multiplexer_4 (
    .in0(ID_IR[25:21]), .in1(5'b00100), .out(multiplexer_4_out), .sel(\单周期硬布线控制器_1_syscall ));
  Multiplexer #(.select(1), .width(5), .disabled("Z"), .enable("false")) multiplexer_5 (
    .in0(ID_IR[20:16]), .in1(5'b00010), .out(multiplexer_5_out), .sel(\单周期硬布线控制器_1_syscall ));
  Pull_Resistor #(.pull(1)) pull_resistor_1 (.node(CLK));
  \单周期硬布线控制器  \u_单周期硬布线控制器_1  (
    .Func(ID_IR[5:0]), .OP(ID_IR[31:26]), .ALU_OP(\单周期硬布线控制器_1_alu_op ), .MemToReg(\单周期硬布线控制器_1_memtoreg ),
    .MemWrite(\单周期硬布线控制器_1_memwrite ), .ALU_SRC(\单周期硬布线控制器_1_alu_src ), .RegWrite(\单周期硬布线控制器_1_regwrite ),
    .SysCALL(\单周期硬布线控制器_1_syscall ), .SignedExt(SignedExt), .RegDst(\单周期硬布线控制器_1_regdst ),
    .JR(\单周期硬布线控制器_1_jr ), .JMP(\单周期硬布线控制器_1_jmp ), .Beq(\单周期硬布线控制器_1_beq ), .JAL(\单周期硬布线控制器_1_jal ),
    .Bne(\单周期硬布线控制器_1_bne ), .SB(\单周期硬布线控制器_1_sb ), .BLTZ(\单周期硬布线控制器_1_bltz ));
  Multiplexer #(.select(1), .width(5), .disabled("Z"), .enable("false")) multiplexer_6 (
    .in0(ID_IR[20:16]), .in1(ID_IR[15:11]), .out(multiplexer_6_out), .sel(\单周期硬布线控制器_1_regdst ));
  assign bit_extender_1_out = {{16{1'b0}}, ID_IR[15:0]};  // Bit_Extender bit_extender_1
  assign bit_extender_2_out = {{16{ID_IR[15]}}, ID_IR[15:0]};  // Bit_Extender bit_extender_2
  Multiplexer #(.select(1), .width(5), .disabled("Z"), .enable("false")) multiplexer_7 (
    .in0(multiplexer_6_out), .in1({5{1'b1}}), .out(multiplexer_7_out), .sel(\单周期硬布线控制器_1_jal ));
  Multiplexer #(.select(1), .width(32), .disabled("Z"), .enable("false")) multiplexer_8 (
    .in0(bit_extender_1_out), .in1(bit_extender_2_out), .out(multiplexer_8_out), .sel(SignedExt));
  Multiplexer #(.select(1), .width(32), .disabled("Z"), .enable("false")) multiplexer_9 (
    .in0(multiplexer_17_out), .in1(mem_wb_1_pc_2), .out(RDin), .sel(mem_wb_1_jal_2));
  not not_1 (not_1_out, CLK);
  MIPS_Regifile mips_regifile_1 (
    .Din(RDin), .Clk(not_1_out), .R1(mips_regifile_1_r1), .R2(mips_regifile_1_r2), .WE(RegWrite),
    .W_num(mem_wb_1_wr_2), .R1_num(multiplexer_4_out), .R2_num(multiplexer_5_out));
  Counter #(.width(16), .max('hffff), .ongoal("stay"), .trigger("rising"), .behavior("new")) counter_2 (
    .count(JMP), .Q(\无条件分支数 ), .clk(CLK), .clr(RST));  // open: load, D, carry, preset, down
  Counter #(.width(16), .max('hffff), .ongoal("stay"), .trigger("rising"), .behavior("new")) counter_3 (
    .count(LoadUse), .Q(\LoadUse次数 ), .clk(CLK), .clr(RST));  // open: load, D, carry, preset, down
  Counter #(.width(16), .max('hffff), .ongoal("stay"), .trigger("rising"), .behavior("new")) counter_4 (
    .count(Branch), .Q(\条件分支成功数 ), .clk(CLK), .clr(RST));  // open: load, D, carry, preset, down
  not not_2 (not_2_out, en);
  ID_EX id_ex_1 (
    .CLK(CLK), .JMP_2(JMP), .JR_2(id_ex_1_jr_2), .SB_2(id_ex_1_sb_2), .BLTZ_2(id_ex_1_bltz_2),
    .Beq_2(id_ex_1_beq_2), .RegWrite_2(id_ex_1_regwrite_2), .Bne_2(id_ex_1_bne_2),
    .MemToReg_2(id_ex_1_memtoreg_2), .MemWrite_2(id_ex_1_memwrite_2), .AluSrcB_2(id_ex_1_alusrcb_2),
    .JAL_2(id_ex_1_jal_2), .AluOP(id_ex_1_aluop), .RS_2(id_ex_1_rs_2), .E1_2(id_ex_1_e1_2),
    .RT_2(id_ex_1_rt_2), .E2_2(id_ex_1_e2_2), .PC_2(id_ex_1_pc_2), .WR_2(id_ex_1_wr_2),
    .shamt_2(id_ex_1_shamt_2), .PCN_2(EX_PC), .IR_2(EX_IR), .EN(not_2_out), .CLR(\重定向流水线处理逻辑_1_flush ),
    .JMP(\单周期硬布线控制器_1_jmp ), .JR(\单周期硬布线控制器_1_jr ), .SB(\单周期硬布线控制器_1_sb ), .BLTZ(\单周期硬布线控制器_1_bltz ),
    .Beq(\单周期硬布线控制器_1_beq ), .RegWrite(\单周期硬布线控制器_1_regwrite ), .Bne(\单周期硬布线控制器_1_bne ),
    .MemToReg(\单周期硬布线控制器_1_memtoreg ), .MemWrite(\单周期硬布线控制器_1_memwrite ), .AluSrcB(\单周期硬布线控制器_1_alu_src ),
    .JAL(\单周期硬布线控制器_1_jal ), .in_16(\单周期硬布线控制器_1_alu_op ), .WR(multiplexer_7_out), .shamt(ID_IR[10:6]),
    .RS(mips_regifile_1_r1), .E1(multiplexer_8_out), .PCN(ID_PC), .RT(mips_regifile_1_r2),
    .E2(bit_extender_2_out), .IR(ID_IR), .PC(if_id_1_pc_2), .SysCall(\单周期硬布线控制器_1_syscall ),
    .SysCall_2(id_ex_1_syscall_2), .RsForward(\重定向流水线处理逻辑_1_rsforward ), .RsForward_2(id_ex_1_rsforward_2),
    .RtForward(\重定向流水线处理逻辑_1_rtforward ), .RtForward_2(id_ex_1_rtforward_2), .RST(RST));
  Adder #(.width(16)) adder_2 (.a(\无条件分支数 ), .b(\条件分支成功数 ), .out(adder_2_out));  // open: cin, cout
  Multiplexer #(.select(2), .width(32), .disabled("Z"), .enable("false")) multiplexer_10 (
    .in0(id_ex_1_rs_2), .in1(multiplexer_17_out), .in2(AIN), .out(multiplexer_10_out),
    .sel(id_ex_1_rsforward_2));  // open: in3
  Multiplier #(.width(16)) multiplier_1 (.a(adder_2_out), .b(16'h2), .out(multiplier_1_out));  // open: cin, cout
  Multiplexer #(.select(2), .width(32), .disabled("Z"), .enable("false")) multiplexer_11 (
    .in0(id_ex_1_rt_2), .in1(multiplexer_17_out), .in2(AIN), .out(multiplexer_11_out),
    .sel(id_ex_1_rtforward_2));  // open: in3
  Adder #(.width(16)) adder_3 (.a(multiplier_1_out), .b(\LoadUse次数 ), .out(\插入气泡数 ));  // open: cin, cout
  or or_2 (or_2_out, JMP, id_ex_1_jr_2, Branch);
  Multiplexer #(.select(1), .width(32), .disabled("Z"), .enable("false")) multiplexer_12 (
    .in0(multiplexer_11_out), .in1(id_ex_1_e1_2), .out(multiplexer_12_out), .sel(id_ex_1_alusrcb_2));
  Multiplexer #(.select(1), .width(32), .disabled("Z"), .enable("false")) multiplexer_13 (
    .in0(multiplexer_12_out), .in1({32{1'b0}}), .out(multiplexer_13_out), .sel(id_ex_1_bltz_2));
  Shifter #(.width(32), .shift("ll")) shifter_1 (.in(id_ex_1_e2_2), .\dist (5'b00010), .out(shifter_1_out));
  Counter #(.width(16), .max('hffff), .ongoal("stay"), .trigger("rising"), .behavior("old")) \u_周期数  (
    .count(en), .Q(\总周期数 ), .clk(CLK), .clr(RST));  // open: load, D, carry, preset
  MIPS_ALU mips_alu_1 (
    .X(multiplexer_10_out), .Y(multiplexer_13_out), .AluOP(id_ex_1_aluop), .Equal(mips_alu_1_equal),
    .Result(mips_alu_1_result), .shamt(id_ex_1_shamt_2));  // open: Result_2
  Adder #(.width(32)) adder_4 (.a(shifter_1_out), .b(id_ex_1_pc_2), .out(adder_4_out), .cin(1'b0));  // open: cout
  and and_2 (and_2_out, id_ex_1_beq_2, mips_alu_1_equal);
  Comparator #(.width(32), .mode("twosComplement")) comparator_2 (
    .a(32'h1), .b(mips_alu_1_result), .eq(comparator_2_eq));  // open: gt, lt
  or or_3 (Branch, and_2_out, and_3_out, and_4_out);
  and and_3 (and_3_out, id_ex_1_bne_2, ~mips_alu_1_equal);  // AND_Gate
  and and_4 (and_4_out, id_ex_1_bltz_2, comparator_2_eq);
  not not_3 (not_3_out, en);
  EX_MEM ex_mem_1 (
    .CLK(CLK), .WR(id_ex_1_wr_2), .SB_2(ex_mem_1_sb_2), .MemToReg_2(ex_mem_1_memtoreg_2),
    .MemWrite_2(MemWrite), .RegWrite_2(ex_mem_1_regwrite_2), .JAL_2(ex_mem_1_jal_2), .WR_2(ex_mem_1_wr_2),
    .AluResult_2(AIN), .WriteData_2(DIN), .PC_2(ex_mem_1_pc_2), .IR_2(MEM_IR), .PCN_2(M_PC), .EN(not_3_out),
    .CLR(1'b0), .SB(id_ex_1_sb_2), .MemToReg(id_ex_1_memtoreg_2), .MemWrite(id_ex_1_memwrite_2),
    .RegWrite(id_ex_1_regwrite_2), .JAL(id_ex_1_jal_2), .AluResult(mips_alu_1_result),
    .WriteData(multiplexer_11_out), .PC(id_ex_1_pc_2), .IR(EX_IR), .PCN(EX_PC), .RS(multiplexer_10_out),
    .RS_2(ex_mem_1_rs_2), .RT(multiplexer_11_out), .RT_2(ex_mem_1_rt_2), .SysCall(id_ex_1_syscall_2),
    .SysCall_2(ex_mem_1_syscall_2), .RST(RST));
  Multiplexer #(.select(2), .width(32), .disabled("Z"), .enable("false")) multiplexer_14 (
    .in0({DOUT[31:8], DIN[7:0]}), .in1({DOUT[31:16], DIN[7:0], DOUT[7:0]}),
    .in2({DOUT[31:24], DIN[7:0], DOUT[15:0]}), .in3({DIN[7:0], DOUT[23:0]}), .out(DIN1), .sel(AIN[1:0]));
  Multiplexer #(.select(1), .width(32), .disabled("Z"), .enable("false")) multiplexer_15 (
    .in0(DIN), .in1(DIN1), .out(MDin), .sel(ex_mem_1_sb_2));
  RAM #(.addrWidth(10), .dataWidth(32), .bus("separate"), .Select("high")) ram_1 (
    .addr(AIN[11:2]), .din(MDin), .data(DOUT), .str(MemWrite), .clk(CLK), .clr(RST));  // open: sel, ld
  Register #(.width(32), .trigger("rising"), .Select("low")) register_2 (
    .D(a0), .en(sys), .Q(LedData), .clk(CLK), .clr(RST));
  Comparator #(.width(32), .mode("unsigned")) comparator_3 (.a(v0), .b(32'h32), .eq(comparator_3_eq));  // open: gt, lt
  Multiplexer #(.select(1), .width(1), .disabled("Z"), .enable("false")) multiplexer_16 (
    .in0(1'b1), .in1(Go), .out(en), .sel(and_5_out));
  and and_5 (and_5_out, comparator_3_eq, sys);
  not not_4 (not_4_out, en);
  MEM_WB mem_wb_1 (
    .RegWrite_2(RegWrite), .JAL_2(mem_wb_1_jal_2), .AluResult_2(mem_wb_1_aluresult_2),
    .Dout_2(mem_wb_1_dout_2), .WR(ex_mem_1_wr_2), .WR_2(mem_wb_1_wr_2), .CLK(CLK), .PC_2(mem_wb_1_pc_2),
    .MemToReg_2(mem_wb_1_memtoreg_2), .IR_2(WB_IR), .PCN_2(WB_PC), .EN(not_4_out), .CLR(1'b0),
    .RegWrite(ex_mem_1_regwrite_2), .MemToReg(ex_mem_1_memtoreg_2), .JAL(ex_mem_1_jal_2), .AluResult(AIN),
    .Dout(DOUT), .PC(ex_mem_1_pc_2), .IR(MEM_IR), .PCN(M_PC), .RS(ex_mem_1_rs_2), .RS_2(a0),
    .RT(ex_mem_1_rt_2), .RT_2(v0), .SysCall(ex_mem_1_syscall_2), .SysCall_2(sys), .in_8(RST));
  Multiplexer #(.select(1), .width(32), .disabled("Z"), .enable("false")) multiplexer_17 (
    .in0(mem_wb_1_aluresult_2), .in1(mem_wb_1_dout_2), .out(multiplexer_17_out), .sel(mem_wb_1_memtoreg_2));

  // Other names for the same wires on the sheet: MEM_PC[31:0] = M_PC

  // Notes on the sheet:
  //   中断源
  //   时空图监测，可删除
  //   中断等待指示
  //   数码管输出
  //   控制位
  //   指令存储器
  //   流水调试日志用
  //   暂停节拍，不能为0
  //   指令字
  //   contents of rom_1 (hex, n*v repeats v):
  //   20110001 8000c05 20110001 20120002 20130003 8000c09 20110001 20120002 20130003 8000c0d 20110001
  //   20120002 20130003 8000c11 20110001 20120002 20130003 c000cb8 20100001 20110001 118fc0 112020
  //   20020022 c 118882 12200001 8000c15 112020 20020022 c 20110001 118880 112020 20020022 c 12200001
  //   8000c1f 20110001 118fc0 112020 20020022 c 1188c3 112020 20020022 c 118903 112020 20020022 c 118903
  //   112020 20020022 c 118903 112020 20020022 c 118903 112020 20020022 c 118903 112020 20020022 c 118903
  //   112020 20020022 c 118903 112020 20020022 c 20100001 109fc0 139fc3 8021 2012000c 24160003 26100001
  //   3210000f 20080008 20090001 139900 2709825 132020 20020022 c 1094022 1500fff9 22100001 2018000f
  //   2188024 108700 20080008 20090001 139902 2709825 132021 20020022 c 1094022 1500fff9 108702 2c9b022
  //   12c00001 8000c50 4020 1084027 84400 3508ffff 82021 20020022 c 2010ffff 20110000 ae300000 22100001
  //   22310004 ae300000 22100001 22310004 ae300000 22100001 22310004 ae300000 22100001 22310004 ae300000
  //   22100001 22310004 ae300000 22100001 22310004 ae300000 22100001 22310004 ae300000 22100001 22310004
  //   ae300000 22100001 22310004 ae300000 22100001 22310004 ae300000 22100001 22310004 ae300000 22100001
  //   22310004 ae300000 22100001 22310004 ae300000 22100001 22310004 ae300000 22100001 22310004 ae300000
  //   22100001 22310004 22100001 8020 2011003c 8e130000 8e340000 274402a 11000002 ae330000 ae140000
  //   2231fffc 1611fff8 102020 20020022 c 22100004 2011003c 1611fff2 20020032 c 20100000 22100001 102020
  //   20020022 c 22100002 102020 20020022 c 22100003 102020 20020022 c 22100004 102020 20020022 c 22100005
  //   102020 20020022 c 22100006 102020 20020022 c 22100007 102020 20020022 c 22100008 102020 20020022
  //   20020022 c 3e00008
  //   戳工具置1进入计数暂停模式，ctrl+k时钟自动运行到对应节拍暂停
  //   ctrl+k关闭时钟连续运行，将控制位置零，进入单步调试模式调试
  //   OP
  //   Func
  //   rs
  //   rt
  //   rd
  //   可计数暂停的时钟源
  //   JMP
  //   JR
  //   OP
  //   Func
  //   SB
  //   BLTZ
  //   Beq
  //   Bne
  //   MemToReg
  //   MemWrite
  //   AluOP
  //   AluSrcB
  //   RegWrite
  //   JAL
  //   RegDst
  //   Syscall
  //   为方便自动评测，需要输出流水线各段保存的PC值，注意是PC不是PC+4，另外ID段寄存器写入信息，Mem段内存写入信息也要输出
endmodule

module \中断按键参考电路  (
  input  \同步清零信号 ,
  output \与中断屏蔽位与 
);

  wire \_1号中断_out , and_1_out, clock_1_out, d_ff_1_q, or_1_out, or_2_out;

  Clock #(.highDuration(1), .lowDuration(1)) clock_1 (.out(clock_1_out));
  Button \_1号中断  (.out(\_1号中断_out ));
  LED #(.active("true")) \_1号中断等待指示灯  (.in(or_1_out));
  or or_1 (or_1_out, \与中断屏蔽位与 , d_ff_1_q);
  D_Flip_Flop #(.trigger("rising"), .Pre_Clr_Positions("LEGACY"), .NegatePresetClear("false"), .enable("true"), .NewFFLayout("false")) d_ff_1 (
    .clk(\_1号中断_out ), .D(1'b1), .Q(d_ff_1_q), .reset(\与中断屏蔽位与 ));  // open: Qn, preset, en
  or or_2 (or_2_out, d_ff_1_q, \与中断屏蔽位与 );
  and and_1 (and_1_out, or_2_out, ~\同步清零信号 );  // AND_Gate
  D_Flip_Flop #(.trigger("rising"), .Pre_Clr_Positions("LEGACY"), .NegatePresetClear("false"), .enable("true"), .NewFFLayout("false")) IR1 (
    .clk(clock_1_out), .D(and_1_out), .Q(\与中断屏蔽位与 ));  // open: Qn, preset, en, reset

  // Notes on the sheet:
  //   中断信号采样参考电路
  //   Reset 
endmodule

module \单周期MIPS_单级中断  (
  input  IR1,
  input  IR2,
  input  IR3,
  input  IR4,
  output RegWrite,
  output MemWrite,
  output [31:0] PC,
  output [31:0] IR,
  output [31:0] RDin,
  output [31:0] MDin,
  output [31:0] LedData
);

  wire _2048data, and_1_out, and_3_out, and_4_out, and_5_out, and_6_out, and_7_out, and_8_out, and_9_out,
       and_10_out, and_11_out, and_12_out, and_13_out, and_15_out, and_16_out, and_17_out, and_18_out,
       and_19_out, and_20_out, and_21_out, and_22_out, CLK, clock_2_out, comparator_1_eq, comparator_1_lt,
       comparator_3_eq, comparator_4_eq, comparator_5_eq, comparator_6_eq, comparator_7_eq, comparator_8_eq,
       controlled_buffer_1_out, controlled_inverter_1_out, controlled_inverter_2_out,
       controlled_inverter_3_out, d_ff_1_q, en, ERET, Go, IR1_t, IR2_t, IR3_t, IR4_t, IRA, IRB, IRC, IRD,
       mips_alu_1_equal, nand_1_out, or_5_out, or_6_out, or_8_out, random, rW, SB, SignedExt, sys, W1, W2,
       W3, W4, \单周期硬布线控制器_1_alu_src , \单周期硬布线控制器_1_beq , \单周期硬布线控制器_1_bltz , \单周期硬布线控制器_1_bne ,
       \单周期硬布线控制器_1_jal , \单周期硬布线控制器_1_jmp , \单周期硬布线控制器_1_jr , \单周期硬布线控制器_1_memtoreg , \单周期硬布线控制器_1_regdst ;
  wire [1:0] comparator_9_eq;
  wire [3:0] \单周期硬布线控制器_1_alu_op ;
  wire [4:0] multiplexer_4_out, multiplexer_5_out, multiplexer_22_out, w_num, wp;
  wire [6:0] keyboard_1_data, register_18_q;
  wire [7:0] multiplexer_32_out, \n2个随机数_1_out_3 , \n4个随机数_1_out_3 ;
  wire [9:0] multiplexer_6_out, multiplexer_7_out, multiplexer_8_out, multiplexer_9_out, multiplexer_10_out,
       multiplexer_11_out, multiplexer_12_out, multiplexer_13_out, multiplexer_14_out, multiplexer_15_out,
       multiplexer_16_out, multiplexer_17_out, multiplexer_18_out, multiplexer_19_out, multiplexer_20_out,
       multiplexer_21_out;
  wire [12:0] CNT_num;
  wire [15:0] \总周期数 ;
  wire [27:0] adder_1_out;
  wire [31:0] _2048d1, _2048d2, _2048d3, _2048d4, _2048d5, _2048d6, _2048d7, _2048d8, _2048d9, _2048d10,
       _2048d11, _2048d12, _2048d13, _2048d14, _2048d15, _2048d16, a0, adder_2_out, AIN, bit_extender_1_out,
       bit_extender_2_out, data1, data2, data3, data4, data5, data6, data7, data8, data9, data10, data11,
       data12, data13, data14, data15, data16, DIN, DIN1, Din_t, DOUT, multiplexer_1_out, multiplexer_2_out,
       multiplexer_23_out, multiplexer_27_out, multiplexer_28_out, multiplexer_30_out, nextPC, PCin,
       randomNum, shifter_1_out, \显示译码器_1_data1 , \显示译码器_1_data2 , \显示译码器_1_data3 , \显示译码器_1_data4 ,
       \显示译码器_1_data5 , \显示译码器_1_data6 , \显示译码器_1_data7 , \显示译码器_1_data8 , \显示译码器_1_data9 , \显示译码器_1_data10 ,
       \显示译码器_1_data11 , \显示译码器_1_data12 , \显示译码器_1_data13 , \显示译码器_1_data14 , \显示译码器_1_data15 ,
       \显示译码器_1_data16 , \显示译码器_1_data17 , \显示译码器_1_data18 , \显示译码器_1_data19 , \显示译码器_1_data20 ,
       \显示译码器_1_data21 , \显示译码器_1_data22 , \显示译码器_1_data23 , \显示译码器_1_data24 , \显示译码器_1_data25 ,
       \显示译码器_1_data26 , \显示译码器_1_data27 , \显示译码器_1_data28 , \显示译码器_1_data29 , \显示译码器_1_data30 ,
       \显示译码器_1_data31 , \显示译码器_1_data32 , \显示译码器_2_data1 , \显示译码器_2_data2 , \显示译码器_2_data3 ,
       \显示译码器_2_data4 , \显示译码器_2_data5 , \显示译码器_2_data6 , \显示译码器_2_data7 , \显示译码器_2_data8 , \显示译码器_2_data9 ,
       \显示译码器_2_data10 , \显示译码器_2_data11 , \显示译码器_2_data12 , \显示译码器_2_data13 , \显示译码器_2_data14 ,
       \显示译码器_2_data15 , \显示译码器_2_data16 , \显示译码器_2_data17 , \显示译码器_2_data18 , \显示译码器_2_data19 ,
       \显示译码器_2_data20 , \显示译码器_2_data21 , \显示译码器_2_data22 , \显示译码器_2_data23 , \显示译码器_2_data24 ,
       \显示译码器_2_data25 , \显示译码器_2_data26 , \显示译码器_2_data27 , \显示译码器_2_data28 , \显示译码器_2_data29 ,
       \显示译码器_2_data30 , \显示译码器_2_data31 , \显示译码器_2_data32 , \显示译码器_3_data1 , \显示译码器_3_data2 ,
       \显示译码器_3_data3 , \显示译码器_3_data4 , \显示译码器_3_data5 , \显示译码器_3_data6 , \显示译码器_3_data7 , \显示译码器_3_data8 ,
       \显示译码器_3_data9 , \显示译码器_3_data10 , \显示译码器_3_data11 , \显示译码器_3_data12 , \显示译码器_3_data13 ,
       \显示译码器_3_data14 , \显示译码器_3_data15 , \显示译码器_3_data16 , \显示译码器_3_data17 , \显示译码器_3_data18 ,
       \显示译码器_3_data19 , \显示译码器_3_data20 , \显示译码器_3_data21 , \显示译码器_3_data22 , \显示译码器_3_data23 ,
       \显示译码器_3_data24 , \显示译码器_3_data25 , \显示译码器_3_data26 , \显示译码器_3_data27 , \显示译码器_3_data28 ,
       \显示译码器_3_data29 , \显示译码器_3_data30 , \显示译码器_3_data31 , \显示译码器_3_data32 , \显示译码器_4_data1 ,
       \显示译码器_4_data2 , \显示译码器_4_data3 , \显示译码器_4_data4 , \显示译码器_4_data5 , \显示译码器_4_data6 , \显示译码器_4_data7 ,
       \显示译码器_4_data8 , \显示译码器_4_data9 , \显示译码器_4_data10 , \显示译码器_4_data11 , \显示译码器_4_data12 ,
       \显示译码器_4_data13 , \显示译码器_4_data14 , \显示译码器_4_data15 , \显示译码器_4_data16 , \显示译码器_4_data17 ,
       \显示译码器_4_data18 , \显示译码器_4_data19 , \显示译码器_4_data20 , \显示译码器_4_data21 , \显示译码器_4_data22 ,
       \显示译码器_4_data23 , \显示译码器_4_data24 , \显示译码器_4_data25 , \显示译码器_4_data26 , \显示译码器_4_data27 ,
       \显示译码器_4_data28 , \显示译码器_4_data29 , \显示译码器_4_data30 , \显示译码器_4_data31 , \显示译码器_4_data32 ,
       \显示译码器_5_data1 , \显示译码器_5_data2 , \显示译码器_5_data3 , \显示译码器_5_data4 , \显示译码器_5_data5 , \显示译码器_5_data6 ,
       \显示译码器_5_data7 , \显示译码器_5_data8 , \显示译码器_5_data9 , \显示译码器_5_data10 , \显示译码器_5_data11 ,
       \显示译码器_5_data12 , \显示译码器_5_data13 , \显示译码器_5_data14 , \显示译码器_5_data15 , \显示译码器_5_data16 ,
       \显示译码器_5_data17 , \显示译码器_5_data18 , \显示译码器_5_data19 , \显示译码器_5_data20 , \显示译码器_5_data21 ,
       \显示译码器_5_data22 , \显示译码器_5_data23 , \显示译码器_5_data24 , \显示译码器_5_data25 , \显示译码器_5_data26 ,
       \显示译码器_5_data27 , \显示译码器_5_data28 , \显示译码器_5_data29 , \显示译码器_5_data30 , \显示译码器_5_data31 ,
       \显示译码器_5_data32 , \显示译码器_6_data1 , \显示译码器_6_data2 , \显示译码器_6_data3 , \显示译码器_6_data4 , \显示译码器_6_data5 ,
       \显示译码器_6_data6 , \显示译码器_6_data7 , \显示译码器_6_data8 , \显示译码器_6_data9 , \显示译码器_6_data10 ,
       \显示译码器_6_data11 , \显示译码器_6_data12 , \显示译码器_6_data13 , \显示译码器_6_data14 , \显示译码器_6_data15 ,
       \显示译码器_6_data16 , \显示译码器_6_data17 , \显示译码器_6_data18 , \显示译码器_6_data19 , \显示译码器_6_data20 ,
       \显示译码器_6_data21 , \显示译码器_6_data22 , \显示译码器_6_data23 , \显示译码器_6_data24 , \显示译码器_6_data25 ,
       \显示译码器_6_data26 , \显示译码器_6_data27 , \显示译码器_6_data28 , \显示译码器_6_data29 , \显示译码器_6_data30 ,
       \显示译码器_6_data31 , \显示译码器_6_data32 , \显示译码器_7_data1 , \显示译码器_7_data2 , \显示译码器_7_data3 ,
       \显示译码器_7_data4 , \显示译码器_7_data5 , \显示译码器_7_data6 , \显示译码器_7_data7 , \显示译码器_7_data8 , \显示译码器_7_data9 ,
       \显示译码器_7_data10 , \显示译码器_7_data11 , \显示译码器_7_data12 , \显示译码器_7_data13 , \显示译码器_7_data14 ,
       \显示译码器_7_data15 , \显示译码器_7_data16 , \显示译码器_7_data17 , \显示译码器_7_data18 , \显示译码器_7_data19 ,
       \显示译码器_7_data20 , \显示译码器_7_data21 , \显示译码器_7_data22 , \显示译码器_7_data23 , \显示译码器_7_data24 ,
       \显示译码器_7_data25 , \显示译码器_7_data26 , \显示译码器_7_data27 , \显示译码器_7_data28 , \显示译码器_7_data29 ,
       \显示译码器_7_data30 , \显示译码器_7_data31 , \显示译码器_7_data32 , \显示译码器_8_data1 , \显示译码器_8_data2 ,
       \显示译码器_8_data3 , \显示译码器_8_data4 , \显示译码器_8_data5 , \显示译码器_8_data6 , \显示译码器_8_data7 , \显示译码器_8_data8 ,
       \显示译码器_8_data9 , \显示译码器_8_data10 , \显示译码器_8_data11 , \显示译码器_8_data12 , \显示译码器_8_data13 ,
       \显示译码器_8_data14 , \显示译码器_8_data15 , \显示译码器_8_data16 , \显示译码器_8_data17 , \显示译码器_8_data18 ,
       \显示译码器_8_data19 , \显示译码器_8_data20 , \显示译码器_8_data21 , \显示译码器_8_data22 , \显示译码器_8_data23 ,
       \显示译码器_8_data24 , \显示译码器_8_data25 , \显示译码器_8_data26 , \显示译码器_8_data27 , \显示译码器_8_data28 ,
       \显示译码器_8_data29 , \显示译码器_8_data30 , \显示译码器_8_data31 , \显示译码器_8_data32 , \显示译码器_9_data1 ,
       \显示译码器_9_data2 , \显示译码器_9_data3 , \显示译码器_9_data4 , \显示译码器_9_data5 , \显示译码器_9_data6 , \显示译码器_9_data7 ,
       \显示译码器_9_data8 , \显示译码器_9_data9 , \显示译码器_9_data10 , \显示译码器_9_data11 , \显示译码器_9_data12 ,
       \显示译码器_9_data13 , \显示译码器_9_data14 , \显示译码器_9_data15 , \显示译码器_9_data16 , \显示译码器_9_data17 ,
       \显示译码器_9_data18 , \显示译码器_9_data19 , \显示译码器_9_data20 , \显示译码器_9_data21 , \显示译码器_9_data22 ,
       \显示译码器_9_data23 , \显示译码器_9_data24 , \显示译码器_9_data25 , \显示译码器_9_data26 , \显示译码器_9_data27 ,
       \显示译码器_9_data28 , \显示译码器_9_data29 , \显示译码器_9_data30 , \显示译码器_9_data31 , \显示译码器_9_data32 ,
       \显示译码器_10_data1 , \显示译码器_10_data2 , \显示译码器_10_data3 , \显示译码器_10_data4 , \显示译码器_10_data5 ,
       \显示译码器_10_data6 , \显示译码器_10_data7 , \显示译码器_10_data8 , \显示译码器_10_data9 , \显示译码器_10_data10 ,
       \显示译码器_10_data11 , \显示译码器_10_data12 , \显示译码器_10_data13 , \显示译码器_10_data14 , \显示译码器_10_data15 ,
       \显示译码器_10_data16 , \显示译码器_10_data17 , \显示译码器_10_data18 , \显示译码器_10_data19 , \显示译码器_10_data20 ,
       \显示译码器_10_data21 , \显示译码器_10_data22 , \显示译码器_10_data23 , \显示译码器_10_data24 , \显示译码器_10_data25 ,
       \显示译码器_10_data26 , \显示译码器_10_data27 , \显示译码器_10_data28 , \显示译码器_10_data29 , \显示译码器_10_data30 ,
       \显示译码器_10_data31 , \显示译码器_10_data32 , \显示译码器_11_data1 , \显示译码器_11_data2 , \显示译码器_11_data3 ,
       \显示译码器_11_data4 , \显示译码器_11_data5 , \显示译码器_11_data6 , \显示译码器_11_data7 , \显示译码器_11_data8 ,
       \显示译码器_11_data9 , \显示译码器_11_data10 , \显示译码器_11_data11 , \显示译码器_11_data12 , \显示译码器_11_data13 ,
       \显示译码器_11_data14 , \显示译码器_11_data15 , \显示译码器_11_data16 , \显示译码器_11_data17 , \显示译码器_11_data18 ,
       \显示译码器_11_data19 , \显示译码器_11_data20 , \显示译码器_11_data21 , \显示译码器_11_data22 , \显示译码器_11_data23 ,
       \显示译码器_11_data24 , \显示译码器_11_data25 , \显示译码器_11_data26 , \显示译码器_11_data27 , \显示译码器_11_data28 ,
       \显示译码器_11_data29 , \显示译码器_11_data30 , \显示译码器_11_data31 , \显示译码器_11_data32 , \显示译码器_12_data1 ,
       \显示译码器_12_data2 , \显示译码器_12_data3 , \显示译码器_12_data4 , \显示译码器_12_data5 , \显示译码器_12_data6 ,
       \显示译码器_12_data7 , \显示译码器_12_data8 , \显示译码器_12_data9 , \显示译码器_12_data10 , \显示译码器_12_data11 ,
       \显示译码器_12_data12 , \显示译码器_12_data13 , \显示译码器_12_data14 , \显示译码器_12_data15 , \显示译码器_12_data16 ,
       \显示译码器_12_data17 , \显示译码器_12_data18 , \显示译码器_12_data19 , \显示译码器_12_data20 , \显示译码器_12_data21 ,
       \显示译码器_12_data22 , \显示译码器_12_data23 , \显示译码器_12_data24 , \显示译码器_12_data25 , \显示译码器_12_data26 ,
       \显示译码器_12_data27 , \显示译码器_12_data28 , \显示译码器_12_data29 , \显示译码器_12_data30 , \显示译码器_12_data31 ,
       \显示译码器_12_data32 , \显示译码器_13_data1 , \显示译码器_13_data2 , \显示译码器_13_data3 , \显示译码器_13_data4 ,
       \显示译码器_13_data5 , \显示译码器_13_data6 , \显示译码器_13_data7 , \显示译码器_13_data8 , \显示译码器_13_data9 ,
       \显示译码器_13_data10 , \显示译码器_13_data11 , \显示译码器_13_data12 , \显示译码器_13_data13 , \显示译码器_13_data14 ,
       \显示译码器_13_data15 , \显示译码器_13_data16 , \显示译码器_13_data17 , \显示译码器_13_data18 , \显示译码器_13_data19 ,
       \显示译码器_13_data20 , \显示译码器_13_data21 , \显示译码器_13_data22 , \显示译码器_13_data23 , \显示译码器_13_data24 ,
       \显示译码器_13_data25 , \显示译码器_13_data26 , \显示译码器_13_data27 , \显示译码器_13_data28 , \显示译码器_13_data29 ,
       \显示译码器_13_data30 , \显示译码器_13_data31 , \显示译码器_13_data32 , \显示译码器_14_data1 , \显示译码器_14_data2 ,
       \显示译码器_14_data3 , \显示译码器_14_data4 , \显示译码器_14_data5 , \显示译码器_14_data6 , \显示译码器_14_data7 ,
       \显示译码器_14_data8 , \显示译码器_14_data9 , \显示译码器_14_data10 , \显示译码器_14_data11 , \显示译码器_14_data12 ,
       \显示译码器_14_data13 , \显示译码器_14_data14 , \显示译码器_14_data15 , \显示译码器_14_data16 , \显示译码器_14_data17 ,
       \显示译码器_14_data18 , \显示译码器_14_data19 , \显示译码器_14_data20 , \显示译码器_14_data21 , \显示译码器_14_data22 ,
       \显示译码器_14_data23 , \显示译码器_14_data24 , \显示译码器_14_data25 , \显示译码器_14_data26 , \显示译码器_14_data27 ,
       \显示译码器_14_data28 , \显示译码器_14_data29 , \显示译码器_14_data30 , \显示译码器_14_data31 , \显示译码器_14_data32 ,
       \显示译码器_15_data1 , \显示译码器_15_data2 , \显示译码器_15_data3 , \显示译码器_15_data4 , \显示译码器_15_data5 ,
       \显示译码器_15_data6 , \显示译码器_15_data7 , \显示译码器_15_data8 , \显示译码器_15_data9 , \显示译码器_15_data10 ,
       \显示译码器_15_data11 , \显示译码器_15_data12 , \显示译码器_15_data13 , \显示译码器_15_data14 , \显示译码器_15_data15 ,
       \显示译码器_15_data16 , \显示译码器_15_data17 , \显示译码器_15_data18 , \显示译码器_15_data19 , \显示译码器_15_data20 ,
       \显示译码器_15_data21 , \显示译码器_15_data22 , \显示译码器_15_data23 , \显示译码器_15_data24 , \显示译码器_15_data25 ,
       \显示译码器_15_data26 , \显示译码器_15_data27 , \显示译码器_15_data28 , \显示译码器_15_data29 , \显示译码器_15_data30 ,
       \显示译码器_15_data31 , \显示译码器_15_data32 , \显示译码器_16_data1 , \显示译码器_16_data2 , \显示译码器_16_data3 ,
       \显示译码器_16_data4 , \显示译码器_16_data5 , \显示译码器_16_data6 , \显示译码器_16_data7 , \显示译码器_16_data8 ,
       \显示译码器_16_data9 , \显示译码器_16_data10 , \显示译码器_16_data11 , \显示译码器_16_data12 , \显示译码器_16_data13 ,
       \显示译码器_16_data14 , \显示译码器_16_data15 , \显示译码器_16_data16 , \显示译码器_16_data17 , \显示译码器_16_data18 ,
       \显示译码器_16_data19 , \显示译码器_16_data20 , \显示译码器_16_data21 , \显示译码器_16_data22 , \显示译码器_16_data23 ,
       \显示译码器_16_data24 , \显示译码器_16_data25 , \显示译码器_16_data26 , \显示译码器_16_data27 , \显示译码器_16_data28 ,
       \显示译码器_16_data29 , \显示译码器_16_data30 , \显示译码器_16_data31 , \显示译码器_16_data32 ;
  wire [31:28] adder_1_out_2;

  Clock #(.highDuration(1), .lowDuration(1)) clock_1 (.out(CLK));
  Button \u_继续运行  (.out(Go));
  LED #(.active("true")) led_1 (.in(W1));
  LED #(.active("true")) led_2 (.in(W2));
  LED #(.active("true")) led_3 (.in(W3));
  D_Flip_Flop #(.trigger("high"), .Pre_Clr_Positions("LEGACY"), .NegatePresetClear("false"), .enable("true"), .NewFFLayout("false")) d_ff_1 (.Q(d_ff_1_q));  // open: clk, D, Qn, preset, en, reset
  Hex_Digit_Display hex_digit_display_1 (.value(LedData[31:28]));  // open: dp
  // Probe on 13'ha
  Clock #(.highDuration(1), .lowDuration(1)) clock_2 (.out(clock_2_out));
  Multiplexer #(.select(1), .width(32), .disabled("Z"), .enable("false")) multiplexer_1 (
    .in0({adder_1_out_2, adder_1_out}), .in1(adder_2_out), .out(multiplexer_1_out), .sel(or_6_out));
  Multiplexer #(.select(1), .width(32), .disabled("Z"), .enable("false")) multiplexer_2 (
    .in0({adder_1_out_2, IR[25:0], 2'b00}), .in1(a0), .out(multiplexer_2_out), .sel(\单周期硬布线控制器_1_jr ));
  Hex_Digit_Display hex_digit_display_2 (.value(LedData[23:20]));  // open: dp
  Hex_Digit_Display hex_digit_display_3 (.value(LedData[27:24]));  // open: dp
  Comparator #(.width(13), .mode("twosComplement")) comparator_1 (
    .a(CNT_num), .b(13'ha), .eq(comparator_1_eq), .lt(comparator_1_lt));  // open: gt
  Multiplexer #(.select(1), .width(32), .disabled("Z"), .enable("false")) multiplexer_3 (
    .in0(multiplexer_1_out), .in1(multiplexer_2_out), .out(nextPC), .sel(\单周期硬布线控制器_1_jmp ));
  Hex_Digit_Display hex_digit_display_4 (.value(LedData[19:16]));  // open: dp
  Hex_Digit_Display hex_digit_display_5 (.value(LedData[15:12]));  // open: dp
  nand nand_1 (nand_1_out, d_ff_1_q, comparator_1_eq);
  Counter #(.width(13), .max('h1fff), .ongoal("stay"), .trigger("rising"), .behavior("old")) counter_1 (
    .count(comparator_1_lt), .Q(CNT_num), .clk(clock_2_out));  // open: load, D, carry, clr, preset
  Register #(.width(32), .trigger("rising"), .Select("low")) u_PC (
    .D(PCin), .en(1'b1), .Q(PC), .clk(CLK));  // open: clr
  Hex_Digit_Display hex_digit_display_6 (.value(LedData[7:4]));  // open: dp
  Hex_Digit_Display hex_digit_display_7 (.value(LedData[11:8]));  // open: dp
  // Probe on \总周期数 
  assign controlled_buffer_1_out = nand_1_out ? clock_2_out : 1'bz;  // Controlled_Buffer controlled_buffer_1
  Pull_Resistor #(.pull(1)) pull_resistor_1 (.node(controlled_buffer_1_out));
  Hex_Digit_Display hex_digit_display_8 (.value(LedData[3:0]));  // open: dp
  Adder #(.width(32)) adder_1 (.a(PC), .b(32'h4), .out({adder_1_out_2, adder_1_out}));  // open: cin, cout
  // Probe on PC
  // Probe on IR
  // Probe on RDin
  // Probe on MemWrite
  // Probe on MDin
  // Probe on LedData
  Comparator #(.width(32), .mode("unsigned")) comparator_2 (.a(32'h42000018), .b(IR), .eq(ERET));  // open: gt, lt
  ROM #(.addrWidth(10), .dataWidth(32), .Select("high")) rom_1 (.addr(PC[11:2]), .data(IR));
  or or_1 (IR1_t, IR1, IRA);
  // Probe on RegWrite
  // Mips_Probe mips_probe_1: pin names not known; wires that end beside it: IR
  and and_1 (and_1_out, _2048data, sys);
  or or_2 (IR2_t, IR2, IRB);
  Counter #(.width(16), .max('hffff), .ongoal("stay"), .trigger("rising"), .behavior("old")) counter_2 (
    .count(en), .Q(\总周期数 ), .clk(CLK));  // open: load, D, carry, clr, preset
  \单周期硬布线控制器  \u_单周期硬布线控制器_1  (
    .Func(IR[5:0]), .OP(IR[31:26]), .ALU_OP(\单周期硬布线控制器_1_alu_op ), .MemToReg(\单周期硬布线控制器_1_memtoreg ),
    .MemWrite(MemWrite), .ALU_SRC(\单周期硬布线控制器_1_alu_src ), .RegWrite(RegWrite), .SysCALL(sys),
    .SignedExt(SignedExt), .RegDst(\单周期硬布线控制器_1_regdst ), .JR(\单周期硬布线控制器_1_jr ), .JMP(\单周期硬布线控制器_1_jmp ),
    .Beq(\单周期硬布线控制器_1_beq ), .JAL(\单周期硬布线控制器_1_jal ), .Bne(\单周期硬布线控制器_1_bne ), .SB(SB),
    .BLTZ(\单周期硬布线控制器_1_bltz ));
  Multiplexer #(.select(1), .width(5), .disabled("Z"), .enable("false")) multiplexer_4 (
    .in0(IR[25:21]), .in1(5'b00100), .out(multiplexer_4_out), .sel(sys));
  Multiplexer #(.select(1), .width(5), .disabled("Z"), .enable("false")) multiplexer_5 (
    .in0(IR[20:16]), .in1(5'b00010), .out(multiplexer_5_out), .sel(sys));
  assign bit_extender_1_out = {{16{1'b0}}, IR[15:0]};  // Bit_Extender bit_extender_1
  assign bit_extender_2_out = {{16{IR[15]}}, IR[15:0]};  // Bit_Extender bit_extender_2
  Multiplexer #(.select(1), .width(10), .disabled("Z"), .enable("false")) multiplexer_6 (
    .in0(AIN[11:2]), .in1({10{1'b0}}), .out(multiplexer_6_out), .sel(and_1_out));
  Multiplexer #(.select(1), .width(10), .disabled("Z"), .enable("false")) multiplexer_7 (
    .in0(AIN[11:2]), .in1(10'h1), .out(multiplexer_7_out), .sel(and_1_out));
  Multiplexer #(.select(1), .width(10), .disabled("Z"), .enable("false")) multiplexer_8 (
    .in0(AIN[11:2]), .in1(10'h2), .out(multiplexer_8_out), .sel(and_1_out));
  Multiplexer #(.select(1), .width(10), .disabled("Z"), .enable("false")) multiplexer_9 (
    .in0(AIN[11:2]), .in1(10'h3), .out(multiplexer_9_out), .sel(and_1_out));
  Multiplexer #(.select(1), .width(10), .disabled("Z"), .enable("false")) multiplexer_10 (
    .in0(AIN[11:2]), .in1(10'h4), .out(multiplexer_10_out), .sel(and_1_out));
  Multiplexer #(.select(1), .width(10), .disabled("Z"), .enable("false")) multiplexer_11 (
    .in0(AIN[11:2]), .in1(10'h5), .out(multiplexer_11_out), .sel(and_1_out));
  Multiplexer #(.select(1), .width(10), .disabled("Z"), .enable("false")) multiplexer_12 (
    .in0(AIN[11:2]), .in1(10'h6), .out(multiplexer_12_out), .sel(and_1_out));
  Multiplexer #(.select(1), .width(10), .disabled("Z"), .enable("false")) multiplexer_13 (
    .in0(AIN[11:2]), .in1(10'h7), .out(multiplexer_13_out), .sel(and_1_out));
  Multiplexer #(.select(1), .width(10), .disabled("Z"), .enable("false")) multiplexer_14 (
    .in0(AIN[11:2]), .in1(10'h8), .out(multiplexer_14_out), .sel(and_1_out));
  Multiplexer #(.select(1), .width(10), .disabled("Z"), .enable("false")) multiplexer_15 (
    .in0(AIN[11:2]), .in1(10'h9), .out(multiplexer_15_out), .sel(and_1_out));
  Multiplexer #(.select(1), .width(10), .disabled("Z"), .enable("false")) multiplexer_16 (
    .in0(AIN[11:2]), .in1(10'ha), .out(multiplexer_16_out), .sel(and_1_out));
  Multiplexer #(.select(1), .width(10), .disabled("Z"), .enable("false")) multiplexer_17 (
    .in0(AIN[11:2]), .in1(10'hb), .out(multiplexer_17_out), .sel(and_1_out));
  Multiplexer #(.select(1), .width(10), .disabled("Z"), .enable("false")) multiplexer_18 (
    .in0(AIN[11:2]), .in1(10'hc), .out(multiplexer_18_out), .sel(and_1_out));
  Multiplexer #(.select(1), .width(10), .disabled("Z"), .enable("false")) multiplexer_19 (
    .in0(AIN[11:2]), .in1(10'hd), .out(multiplexer_19_out), .sel(and_1_out));
  Multiplexer #(.select(1), .width(10), .disabled("Z"), .enable("false")) multiplexer_20 (
    .in0(AIN[11:2]), .in1(10'he), .out(multiplexer_20_out), .sel(and_1_out));
  Multiplexer #(.select(1), .width(10), .disabled("Z"), .enable("false")) multiplexer_21 (
    .in0(AIN[11:2]), .in1(10'hf), .out(multiplexer_21_out), .sel(and_1_out));
  or or_3 (IR3_t, IR3, IRC);
  or or_4 (IR4_t, IR4, IRD);
  Multiplexer #(.select(1), .width(5), .disabled("Z"), .enable("false")) multiplexer_22 (
    .in0(IR[20:16]), .in1(IR[15:11]), .out(multiplexer_22_out), .sel(\单周期硬布线控制器_1_regdst ));
  Multiplexer #(.select(1), .width(32), .disabled("Z"), .enable("false")) multiplexer_23 (
    .in0(bit_extender_1_out), .in1(bit_extender_2_out), .out(multiplexer_23_out), .sel(SignedExt));
  Multiplexer #(.select(1), .width(5), .disabled("Z"), .enable("false")) multiplexer_24 (
    .in0(multiplexer_22_out), .in1({5{1'b1}}), .out(wp), .sel(\单周期硬布线控制器_1_jal ));
  Multiplexer #(.select(1), .width(32), .disabled("Z"), .enable("false")) multiplexer_25 (
    .in0(multiplexer_30_out), .in1({adder_1_out_2, adder_1_out}), .out(RDin), .sel(\单周期硬布线控制器_1_jal ));
  MIPS_Regifile mips_regifile_1 (
    .Din(Din_t), .Clk(CLK), .R1(a0), .R2(DIN), .WE(rW), .W_num(w_num), .R1_num(multiplexer_4_out),
    .R2_num(multiplexer_5_out));
  ram ram_1 (
    .CLK(CLK), .str(MemWrite), .data(MDin), .in_5(multiplexer_6_out), .in_6(multiplexer_7_out),
    .in_7(multiplexer_8_out), .in_8(multiplexer_9_out), .in_9(multiplexer_10_out),
    .in_10(multiplexer_11_out), .in_11(multiplexer_12_out), .in_12(multiplexer_13_out),
    .in_13(multiplexer_14_out), .in_14(multiplexer_15_out), .in_15(multiplexer_16_out),
    .in_16(multiplexer_17_out), .in_17(multiplexer_18_out), .in_18(multiplexer_19_out),
    .in_19(multiplexer_20_out), .in_20(multiplexer_21_out), .out_25(data1), .out_26(data2), .out_27(data3),
    .out_28(data4), .out_29(data5), .out_30(data6), .out_31(data7), .out_32(data8), .out_33(data9),
    .out_34(data10), .out_35(data11), .out_36(data12), .out_37(data13), .out_38(data14), .out_39(data15),
    .out_40(data16));  // open: clr, in_21, in_22, in_23, in_24, out_41, out_42, out_43, out_44
  Multiplexer #(.select(2), .width(32), .disabled("Z"), .enable("false")) multiplexer_26 (
    .in0({DOUT[31:8], DIN[7:0]}), .in1({DOUT[31:16], DIN[7:0], DOUT[7:0]}),
    .in2({DOUT[31:24], DIN[7:0], DOUT[15:0]}), .in3({DIN[7:0], DOUT[23:0]}), .out(DIN1), .sel(AIN[1:0]));
  Multiplexer #(.select(1), .width(32), .disabled("Z"), .enable("false")) multiplexer_27 (
    .in0(DIN), .in1(multiplexer_23_out), .out(multiplexer_27_out), .sel(\单周期硬布线控制器_1_alu_src ));
  Multiplexer #(.select(1), .width(32), .disabled("Z"), .enable("false")) multiplexer_28 (
    .in0(multiplexer_27_out), .in1({32{1'b0}}), .out(multiplexer_28_out), .sel(\单周期硬布线控制器_1_bltz ));
  Shifter #(.width(32), .shift("ll")) shifter_1 (.in(bit_extender_2_out), .\dist (5'b00010), .out(shifter_1_out));
  MIPS_ALU mips_alu_1 (
    .X(a0), .Y(multiplexer_28_out), .AluOP(\单周期硬布线控制器_1_alu_op ), .Equal(mips_alu_1_equal), .Result(AIN),
    .shamt(IR[10:6]));  // open: Result_2
  Comparator #(.width(32), .mode("twosComplement")) comparator_3 (
    .a(32'h1), .b(AIN), .eq(comparator_3_eq));  // open: gt, lt
  Multiplexer #(.select(1), .width(32), .disabled("Z"), .enable("false")) multiplexer_29 (
    .in0(DIN), .in1(DIN1), .out(MDin), .sel(SB));
  Adder #(.width(32)) adder_2 (
    .a(shifter_1_out), .b({adder_1_out_2, adder_1_out}), .out(adder_2_out));  // open: cin, cout
  \中断按键  \u_中断按键_1  (
    .epc_next(nextPC), .CLK(CLK), .IR1(IR1_t), .IR2(IR2_t), .IR3(IR3_t), .IR4(IR4_t), .IR1_Addr(32'h31e0),
    .IR2_Addr(32'h30a0), .IR3_Addr(32'h3320), .IR4_Addr(32'h3460), .W1(W1), .W2(W2), .W3(W3), .addr(PCin),
    .W4(W4), .ERET(ERET));
  Comparator #(.width(32), .mode("unsigned")) comparator_4 (.a(DIN), .b(32'h22), .eq(comparator_4_eq));  // open: gt, lt
  Comparator #(.width(16), .mode("twosComplement")) comparator_5 (
    .a(16'h23b), .b(\总周期数 ), .eq(comparator_5_eq));  // open: gt, lt
  Comparator #(.width(16), .mode("twosComplement")) comparator_6 (
    .a(\总周期数 ), .b(16'h1), .eq(comparator_6_eq));  // open: gt, lt
  Comparator #(.width(16), .mode("twosComplement")) comparator_7 (
    .a(\总周期数 ), .b(16'h4), .eq(comparator_7_eq));  // open: gt, lt
  Comparator #(.width(16), .mode("twosComplement")) comparator_8 (
    .a(\总周期数 ), .b(16'h7), .eq(comparator_8_eq));  // open: gt, lt
  Register #(.width(32), .trigger("rising"), .Select("low")) register_1 (
    .D(a0), .en(sys), .Q(LedData), .clk(CLK));  // open: clr
  and and_2 (_2048data, comparator_4_eq, sys);
  and and_3 (and_3_out, \单周期硬布线控制器_1_beq , mips_alu_1_equal);
  and and_4 (and_4_out, \单周期硬布线控制器_1_bne , ~mips_alu_1_equal);  // AND_Gate
  and and_5 (and_5_out, \单周期硬布线控制器_1_bltz , comparator_3_eq);
  or or_5 (or_5_out, comparator_5_eq, comparator_6_eq);
  assign controlled_inverter_1_out = or_5_out ? ~CLK : 1'bz;  // Controlled_Inverter controlled_inverter_1
  assign controlled_inverter_2_out = comparator_7_eq ? ~CLK : 1'bz;  // Controlled_Inverter controlled_inverter_2
  assign controlled_inverter_3_out = comparator_8_eq ? ~CLK : 1'bz;  // Controlled_Inverter controlled_inverter_3
  or or_6 (or_6_out, and_3_out, and_4_out, and_5_out);
  RAM #(.addrWidth(10), .dataWidth(32), .bus("separate"), .Select("high")) ram_2 (
    .addr(AIN[11:2]), .din(MDin), .data(DOUT), .str(MemWrite), .clk(CLK));  // open: sel, ld, clr
  Pull_Resistor #(.pull(0)) pull_resistor_2 (.node(controlled_inverter_1_out));
  Pull_Resistor #(.pull(0)) pull_resistor_3 (.node(controlled_inverter_2_out));
  Pull_Resistor #(.pull(0)) pull_resistor_4 (.node(controlled_inverter_3_out));
  Multiplexer #(.select(1), .width(32), .disabled("Z"), .enable("false")) multiplexer_30 (
    .in0(AIN), .in1(DOUT), .out(multiplexer_30_out), .sel(\单周期硬布线控制器_1_memtoreg ));
  and and_6 (and_6_out, _2048data, sys);
  and and_7 (and_7_out, _2048data, sys);
  and and_8 (and_8_out, _2048data, sys);
  and and_9 (and_9_out, _2048data, sys);
  Comparator #(.width(32), .mode("unsigned")) comparator_9 (
    .a(DIN), .b(32'h1), .eq(comparator_9_eq[0]));  // open: gt, lt
  Comparator #(.width(32), .mode("unsigned")) comparator_10 (
    .a(DIN), .b(32'h2), .eq(comparator_9_eq[1]));  // open: gt, lt
  Register #(.width(32), .trigger("rising"), .Select("low")) register_2 (
    .D(data1), .en(and_6_out), .Q(_2048d1), .clk(CLK));  // open: clr
  Register #(.width(32), .trigger("rising"), .Select("low")) register_3 (
    .D(data2), .en(and_7_out), .Q(_2048d2), .clk(CLK));  // open: clr
  Register #(.width(32), .trigger("rising"), .Select("low")) register_4 (
    .D(data3), .en(and_8_out), .Q(_2048d3), .clk(CLK));  // open: clr
  Register #(.width(32), .trigger("rising"), .Select("low")) register_5 (
    .D(data4), .en(and_9_out), .Q(_2048d4), .clk(CLK));  // open: clr
  or or_7 (rW, RegWrite, random);
  Multiplexer #(.select(1), .width(5), .disabled("Z"), .enable("false")) multiplexer_31 (
    .in0(wp), .in1(5'b01111), .out(w_num), .sel(random));
  or or_8 (or_8_out, comparator_9_eq[0], comparator_9_eq[1]);
  Multiplexer #(.select(2), .width(8), .disabled("Z"), .enable("false")) multiplexer_32 (
    .in0({8{1'b0}}), .in1(\n2个随机数_1_out_3 ), .in2(\n4个随机数_1_out_3 ), .out(multiplexer_32_out),
    .sel(comparator_9_eq));  // open: in3
  \_2个随机数  \u_2个随机数_1  (.in_1(CLK), .in_2(1'b0), .out_3(\n2个随机数_1_out_3 ));
  \_4个随机数  \u_4个随机数_1  (.in_1(CLK), .in_2(1'b0), .out_3(\n4个随机数_1_out_3 ));
  Multiplexer #(.select(1), .width(32), .disabled("Z"), .enable("false")) multiplexer_33 (
    .in0(RDin), .in1(randomNum), .out(Din_t), .sel(random));
  and and_10 (and_10_out, _2048data, sys);
  and and_11 (and_11_out, _2048data, sys);
  and and_12 (and_12_out, _2048data, sys);
  and and_13 (and_13_out, _2048data, sys);
  and and_14 (random, or_8_out, sys);
  assign randomNum = {{24{1'b0}}, multiplexer_32_out};  // Bit_Extender bit_extender_3
  Register #(.width(32), .trigger("rising"), .Select("low")) register_6 (
    .D(data5), .en(and_10_out), .Q(_2048d5), .clk(CLK));  // open: clr
  Register #(.width(32), .trigger("rising"), .Select("low")) register_7 (
    .D(data6), .en(and_11_out), .Q(_2048d6), .clk(CLK));  // open: clr
  Register #(.width(32), .trigger("rising"), .Select("low")) register_8 (
    .D(data7), .en(and_12_out), .Q(_2048d7), .clk(CLK));  // open: clr
  Register #(.width(32), .trigger("rising"), .Select("low")) register_9 (
    .D(data8), .en(and_13_out), .Q(_2048d8), .clk(CLK));  // open: clr
  and and_15 (and_15_out, _2048data, sys);
  and and_16 (and_16_out, _2048data, sys);
  and and_17 (and_17_out, _2048data, sys);
  and and_18 (and_18_out, _2048data, sys);
  Register #(.width(32), .trigger("rising"), .Select("low")) register_10 (
    .D(data9), .en(and_15_out), .Q(_2048d9), .clk(CLK));  // open: clr
  Register #(.width(32), .trigger("rising"), .Select("low")) register_11 (
    .D(data10), .en(and_16_out), .Q(_2048d10), .clk(CLK));  // open: clr
  Register #(.width(32), .trigger("rising"), .Select("low")) register_12 (
    .D(data11), .en(and_17_out), .Q(_2048d11), .clk(CLK));  // open: clr
  Register #(.width(32), .trigger("rising"), .Select("low")) register_13 (
    .D(data12), .en(and_18_out), .Q(_2048d12), .clk(CLK));  // open: clr
  DotMatrix #(.inputtype("column"), .matrixcols(32), .matrixrows(32), .persist(0), .dotshape("square")) dotmatrix_1 (
    .col0(\显示译码器_1_data1 ), .col1(\显示译码器_1_data2 ), .col2(\显示译码器_1_data3 ), .col3(\显示译码器_1_data4 ),
    .col4(\显示译码器_1_data5 ), .col5(\显示译码器_1_data6 ), .col6(\显示译码器_1_data7 ), .col7(\显示译码器_1_data8 ),
    .col8(\显示译码器_1_data9 ), .col9(\显示译码器_1_data10 ), .col10(\显示译码器_1_data11 ), .col11(\显示译码器_1_data12 ),
    .col12(\显示译码器_1_data13 ), .col13(\显示译码器_1_data14 ), .col14(\显示译码器_1_data15 ), .col15(\显示译码器_1_data16 ),
    .col16(\显示译码器_1_data17 ), .col17(\显示译码器_1_data18 ), .col18(\显示译码器_1_data19 ), .col19(\显示译码器_1_data20 ),
    .col20(\显示译码器_1_data21 ), .col21(\显示译码器_1_data22 ), .col22(\显示译码器_1_data23 ), .col23(\显示译码器_1_data24 ),
    .col24(\显示译码器_1_data25 ), .col25(\显示译码器_1_data26 ), .col26(\显示译码器_1_data27 ), .col27(\显示译码器_1_data28 ),
    .col28(\显示译码器_1_data29 ), .col29(\显示译码器_1_data30 ), .col30(\显示译码器_1_data31 ), .col31(\显示译码器_1_data32 ));
  \显示译码器  \u_显示译码器_1  (
    .\input (_2048d1), .data1(\显示译码器_1_data1 ), .data9(\显示译码器_1_data9 ), .data17(\显示译码器_1_data17 ),
    .data25(\显示译码器_1_data25 ), .data2(\显示译码器_1_data2 ), .data10(\显示译码器_1_data10 ), .data18(\显示译码器_1_data18 ),
    .data26(\显示译码器_1_data26 ), .data3(\显示译码器_1_data3 ), .data11(\显示译码器_1_data11 ), .data19(\显示译码器_1_data19 ),
    .data27(\显示译码器_1_data27 ), .data4(\显示译码器_1_data4 ), .data12(\显示译码器_1_data12 ), .data20(\显示译码器_1_data20 ),
    .data28(\显示译码器_1_data28 ), .data5(\显示译码器_1_data5 ), .data13(\显示译码器_1_data13 ), .data21(\显示译码器_1_data21 ),
    .data29(\显示译码器_1_data29 ), .data6(\显示译码器_1_data6 ), .data14(\显示译码器_1_data14 ), .data22(\显示译码器_1_data22 ),
    .data30(\显示译码器_1_data30 ), .data7(\显示译码器_1_data7 ), .data15(\显示译码器_1_data15 ), .data23(\显示译码器_1_data23 ),
    .data31(\显示译码器_1_data31 ), .data8(\显示译码器_1_data8 ), .data16(\显示译码器_1_data16 ), .data24(\显示译码器_1_data24 ),
    .data32(\显示译码器_1_data32 ));
  DotMatrix #(.inputtype("column"), .matrixcols(32), .matrixrows(32), .persist(0), .dotshape("square")) dotmatrix_2 (
    .col0(\显示译码器_2_data1 ), .col1(\显示译码器_2_data2 ), .col2(\显示译码器_2_data3 ), .col3(\显示译码器_2_data4 ),
    .col4(\显示译码器_2_data5 ), .col5(\显示译码器_2_data6 ), .col6(\显示译码器_2_data7 ), .col7(\显示译码器_2_data8 ),
    .col8(\显示译码器_2_data9 ), .col9(\显示译码器_2_data10 ), .col10(\显示译码器_2_data11 ), .col11(\显示译码器_2_data12 ),
    .col12(\显示译码器_2_data13 ), .col13(\显示译码器_2_data14 ), .col14(\显示译码器_2_data15 ), .col15(\显示译码器_2_data16 ),
    .col16(\显示译码器_2_data17 ), .col17(\显示译码器_2_data18 ), .col18(\显示译码器_2_data19 ), .col19(\显示译码器_2_data20 ),
    .col20(\显示译码器_2_data21 ), .col21(\显示译码器_2_data22 ), .col22(\显示译码器_2_data23 ), .col23(\显示译码器_2_data24 ),
    .col24(\显示译码器_2_data25 ), .col25(\显示译码器_2_data26 ), .col26(\显示译码器_2_data27 ), .col27(\显示译码器_2_data28 ),
    .col28(\显示译码器_2_data29 ), .col29(\显示译码器_2_data30 ), .col30(\显示译码器_2_data31 ), .col31(\显示译码器_2_data32 ));
  \显示译码器  \u_显示译码器_2  (
    .\input (_2048d5), .data1(\显示译码器_2_data1 ), .data9(\显示译码器_2_data9 ), .data17(\显示译码器_2_data17 ),
    .data25(\显示译码器_2_data25 ), .data2(\显示译码器_2_data2 ), .data10(\显示译码器_2_data10 ), .data18(\显示译码器_2_data18 ),
    .data26(\显示译码器_2_data26 ), .data3(\显示译码器_2_data3 ), .data11(\显示译码器_2_data11 ), .data19(\显示译码器_2_data19 ),
    .data27(\显示译码器_2_data27 ), .data4(\显示译码器_2_data4 ), .data12(\显示译码器_2_data12 ), .data20(\显示译码器_2_data20 ),
    .data28(\显示译码器_2_data28 ), .data5(\显示译码器_2_data5 ), .data13(\显示译码器_2_data13 ), .data21(\显示译码器_2_data21 ),
    .data29(\显示译码器_2_data29 ), .data6(\显示译码器_2_data6 ), .data14(\显示译码器_2_data14 ), .data22(\显示译码器_2_data22 ),
    .data30(\显示译码器_2_data30 ), .data7(\显示译码器_2_data7 ), .data15(\显示译码器_2_data15 ), .data23(\显示译码器_2_data23 ),
    .data31(\显示译码器_2_data31 ), .data8(\显示译码器_2_data8 ), .data16(\显示译码器_2_data16 ), .data24(\显示译码器_2_data24 ),
    .data32(\显示译码器_2_data32 ));
  DotMatrix #(.inputtype("column"), .matrixcols(32), .matrixrows(32), .persist(0), .dotshape("square")) dotmatrix_3 (
    .col0(\显示译码器_3_data1 ), .col1(\显示译码器_3_data2 ), .col2(\显示译码器_3_data3 ), .col3(\显示译码器_3_data4 ),
    .col4(\显示译码器_3_data5 ), .col5(\显示译码器_3_data6 ), .col6(\显示译码器_3_data7 ), .col7(\显示译码器_3_data8 ),
    .col8(\显示译码器_3_data9 ), .col9(\显示译码器_3_data10 ), .col10(\显示译码器_3_data11 ), .col11(\显示译码器_3_data12 ),
    .col12(\显示译码器_3_data13 ), .col13(\显示译码器_3_data14 ), .col14(\显示译码器_3_data15 ), .col15(\显示译码器_3_data16 ),
    .col16(\显示译码器_3_data17 ), .col17(\显示译码器_3_data18 ), .col18(\显示译码器_3_data19 ), .col19(\显示译码器_3_data20 ),
    .col20(\显示译码器_3_data21 ), .col21(\显示译码器_3_data22 ), .col22(\显示译码器_3_data23 ), .col23(\显示译码器_3_data24 ),
    .col24(\显示译码器_3_data25 ), .col25(\显示译码器_3_data26 ), .col26(\显示译码器_3_data27 ), .col27(\显示译码器_3_data28 ),
    .col28(\显示译码器_3_data29 ), .col29(\显示译码器_3_data30 ), .col30(\显示译码器_3_data31 ), .col31(\显示译码器_3_data32 ));
  \显示译码器  \u_显示译码器_3  (
    .\input (_2048d9), .data1(\显示译码器_3_data1 ), .data9(\显示译码器_3_data9 ), .data17(\显示译码器_3_data17 ),
    .data25(\显示译码器_3_data25 ), .data2(\显示译码器_3_data2 ), .data10(\显示译码器_3_data10 ), .data18(\显示译码器_3_data18 ),
    .data26(\显示译码器_3_data26 ), .data3(\显示译码器_3_data3 ), .data11(\显示译码器_3_data11 ), .data19(\显示译码器_3_data19 ),
    .data27(\显示译码器_3_data27 ), .data4(\显示译码器_3_data4 ), .data12(\显示译码器_3_data12 ), .data20(\显示译码器_3_data20 ),
    .data28(\显示译码器_3_data28 ), .data5(\显示译码器_3_data5 ), .data13(\显示译码器_3_data13 ), .data21(\显示译码器_3_data21 ),
    .data29(\显示译码器_3_data29 ), .data6(\显示译码器_3_data6 ), .data14(\显示译码器_3_data14 ), .data22(\显示译码器_3_data22 ),
    .data30(\显示译码器_3_data30 ), .data7(\显示译码器_3_data7 ), .data15(\显示译码器_3_data15 ), .data23(\显示译码器_3_data23 ),
    .data31(\显示译码器_3_data31 ), .data8(\显示译码器_3_data8 ), .data16(\显示译码器_3_data16 ), .data24(\显示译码器_3_data24 ),
    .data32(\显示译码器_3_data32 ));
  DotMatrix #(.inputtype("column"), .matrixcols(32), .matrixrows(32), .persist(0), .dotshape("square")) dotmatrix_4 (
    .col0(\显示译码器_4_data1 ), .col1(\显示译码器_4_data2 ), .col2(\显示译码器_4_data3 ), .col3(\显示译码器_4_data4 ),
    .col4(\显示译码器_4_data5 ), .col5(\显示译码器_4_data6 ), .col6(\显示译码器_4_data7 ), .col7(\显示译码器_4_data8 ),
    .col8(\显示译码器_4_data9 ), .col9(\显示译码器_4_data10 ), .col10(\显示译码器_4_data11 ), .col11(\显示译码器_4_data12 ),
    .col12(\显示译码器_4_data13 ), .col13(\显示译码器_4_data14 ), .col14(\显示译码器_4_data15 ), .col15(\显示译码器_4_data16 ),
    .col16(\显示译码器_4_data17 ), .col17(\显示译码器_4_data18 ), .col18(\显示译码器_4_data19 ), .col19(\显示译码器_4_data20 ),
    .col20(\显示译码器_4_data21 ), .col21(\显示译码器_4_data22 ), .col22(\显示译码器_4_data23 ), .col23(\显示译码器_4_data24 ),
    .col24(\显示译码器_4_data25 ), .col25(\显示译码器_4_data26 ), .col26(\显示译码器_4_data27 ), .col27(\显示译码器_4_data28 ),
    .col28(\显示译码器_4_data29 ), .col29(\显示译码器_4_data30 ), .col30(\显示译码器_4_data31 ), .col31(\显示译码器_4_data32 ));
  \显示译码器  \u_显示译码器_4  (
    .\input (_2048d13), .data1(\显示译码器_4_data1 ), .data9(\显示译码器_4_data9 ), .data17(\显示译码器_4_data17 ),
    .data25(\显示译码器_4_data25 ), .data2(\显示译码器_4_data2 ), .data10(\显示译码器_4_data10 ), .data18(\显示译码器_4_data18 ),
    .data26(\显示译码器_4_data26 ), .data3(\显示译码器_4_data3 ), .data11(\显示译码器_4_data11 ), .data19(\显示译码器_4_data19 ),
    .data27(\显示译码器_4_data27 ), .data4(\显示译码器_4_data4 ), .data12(\显示译码器_4_data12 ), .data20(\显示译码器_4_data20 ),
    .data28(\显示译码器_4_data28 ), .data5(\显示译码器_4_data5 ), .data13(\显示译码器_4_data13 ), .data21(\显示译码器_4_data21 ),
    .data29(\显示译码器_4_data29 ), .data6(\显示译码器_4_data6 ), .data14(\显示译码器_4_data14 ), .data22(\显示译码器_4_data22 ),
    .data30(\显示译码器_4_data30 ), .data7(\显示译码器_4_data7 ), .data15(\显示译码器_4_data15 ), .data23(\显示译码器_4_data23 ),
    .data31(\显示译码器_4_data31 ), .data8(\显示译码器_4_data8 ), .data16(\显示译码器_4_data16 ), .data24(\显示译码器_4_data24 ),
    .data32(\显示译码器_4_data32 ));
  and and_19 (and_19_out, _2048data, sys);
  and and_20 (and_20_out, _2048data, sys);
  and and_21 (and_21_out, _2048data, sys);
  and and_22 (and_22_out, _2048data, sys);
  Register #(.width(32), .trigger("rising"), .Select("low")) register_14 (
    .D(data13), .en(and_19_out), .Q(_2048d13), .clk(CLK));  // open: clr
  Register #(.width(32), .trigger("rising"), .Select("low")) register_15 (
    .D(data14), .en(and_20_out), .Q(_2048d14), .clk(CLK));  // open: clr
  Register #(.width(32), .trigger("rising"), .Select("low")) register_16 (
    .D(data15), .en(and_21_out), .Q(_2048d15), .clk(CLK));  // open: clr
  Register #(.width(32), .trigger("rising"), .Select("low")) register_17 (
    .D(data16), .en(and_22_out), .Q(_2048d16), .clk(CLK));  // open: clr
  DotMatrix #(.inputtype("column"), .matrixcols(32), .matrixrows(32), .persist(0), .dotshape("square")) dotmatrix_5 (
    .col0(\显示译码器_5_data1 ), .col1(\显示译码器_5_data2 ), .col2(\显示译码器_5_data3 ), .col3(\显示译码器_5_data4 ),
    .col4(\显示译码器_5_data5 ), .col5(\显示译码器_5_data6 ), .col6(\显示译码器_5_data7 ), .col7(\显示译码器_5_data8 ),
    .col8(\显示译码器_5_data9 ), .col9(\显示译码器_5_data10 ), .col10(\显示译码器_5_data11 ), .col11(\显示译码器_5_data12 ),
    .col12(\显示译码器_5_data13 ), .col13(\显示译码器_5_data14 ), .col14(\显示译码器_5_data15 ), .col15(\显示译码器_5_data16 ),
    .col16(\显示译码器_5_data17 ), .col17(\显示译码器_5_data18 ), .col18(\显示译码器_5_data19 ), .col19(\显示译码器_5_data20 ),
    .col20(\显示译码器_5_data21 ), .col21(\显示译码器_5_data22 ), .col22(\显示译码器_5_data23 ), .col23(\显示译码器_5_data24 ),
    .col24(\显示译码器_5_data25 ), .col25(\显示译码器_5_data26 ), .col26(\显示译码器_5_data27 ), .col27(\显示译码器_5_data28 ),
    .col28(\显示译码器_5_data29 ), .col29(\显示译码器_5_data30 ), .col30(\显示译码器_5_data31 ), .col31(\显示译码器_5_data32 ));
  \显示译码器  \u_显示译码器_5  (
    .\input (_2048d2), .data1(\显示译码器_5_data1 ), .data9(\显示译码器_5_data9 ), .data17(\显示译码器_5_data17 ),
    .data25(\显示译码器_5_data25 ), .data2(\显示译码器_5_data2 ), .data10(\显示译码器_5_data10 ), .data18(\显示译码器_5_data18 ),
    .data26(\显示译码器_5_data26 ), .data3(\显示译码器_5_data3 ), .data11(\显示译码器_5_data11 ), .data19(\显示译码器_5_data19 ),
    .data27(\显示译码器_5_data27 ), .data4(\显示译码器_5_data4 ), .data12(\显示译码器_5_data12 ), .data20(\显示译码器_5_data20 ),
    .data28(\显示译码器_5_data28 ), .data5(\显示译码器_5_data5 ), .data13(\显示译码器_5_data13 ), .data21(\显示译码器_5_data21 ),
    .data29(\显示译码器_5_data29 ), .data6(\显示译码器_5_data6 ), .data14(\显示译码器_5_data14 ), .data22(\显示译码器_5_data22 ),
    .data30(\显示译码器_5_data30 ), .data7(\显示译码器_5_data7 ), .data15(\显示译码器_5_data15 ), .data23(\显示译码器_5_data23 ),
    .data31(\显示译码器_5_data31 ), .data8(\显示译码器_5_data8 ), .data16(\显示译码器_5_data16 ), .data24(\显示译码器_5_data24 ),
    .data32(\显示译码器_5_data32 ));
  DotMatrix #(.inputtype("column"), .matrixcols(32), .matrixrows(32), .persist(0), .dotshape("square")) dotmatrix_6 (
    .col0(\显示译码器_6_data1 ), .col1(\显示译码器_6_data2 ), .col2(\显示译码器_6_data3 ), .col3(\显示译码器_6_data4 ),
    .col4(\显示译码器_6_data5 ), .col5(\显示译码器_6_data6 ), .col6(\显示译码器_6_data7 ), .col7(\显示译码器_6_data8 ),
    .col8(\显示译码器_6_data9 ), .col9(\显示译码器_6_data10 ), .col10(\显示译码器_6_data11 ), .col11(\显示译码器_6_data12 ),
    .col12(\显示译码器_6_data13 ), .col13(\显示译码器_6_data14 ), .col14(\显示译码器_6_data15 ), .col15(\显示译码器_6_data16 ),
    .col16(\显示译码器_6_data17 ), .col17(\显示译码器_6_data18 ), .col18(\显示译码器_6_data19 ), .col19(\显示译码器_6_data20 ),
    .col20(\显示译码器_6_data21 ), .col21(\显示译码器_6_data22 ), .col22(\显示译码器_6_data23 ), .col23(\显示译码器_6_data24 ),
    .col24(\显示译码器_6_data25 ), .col25(\显示译码器_6_data26 ), .col26(\显示译码器_6_data27 ), .col27(\显示译码器_6_data28 ),
    .col28(\显示译码器_6_data29 ), .col29(\显示译码器_6_data30 ), .col30(\显示译码器_6_data31 ), .col31(\显示译码器_6_data32 ));
  \显示译码器  \u_显示译码器_6  (
    .\input (_2048d6), .data1(\显示译码器_6_data1 ), .data9(\显示译码器_6_data9 ), .data17(\显示译码器_6_data17 ),
    .data25(\显示译码器_6_data25 ), .data2(\显示译码器_6_data2 ), .data10(\显示译码器_6_data10 ), .data18(\显示译码器_6_data18 ),
    .data26(\显示译码器_6_data26 ), .data3(\显示译码器_6_data3 ), .data11(\显示译码器_6_data11 ), .data19(\显示译码器_6_data19 ),
    .data27(\显示译码器_6_data27 ), .data4(\显示译码器_6_data4 ), .data12(\显示译码器_6_data12 ), .data20(\显示译码器_6_data20 ),
    .data28(\显示译码器_6_data28 ), .data5(\显示译码器_6_data5 ), .data13(\显示译码器_6_data13 ), .data21(\显示译码器_6_data21 ),
    .data29(\显示译码器_6_data29 ), .data6(\显示译码器_6_data6 ), .data14(\显示译码器_6_data14 ), .data22(\显示译码器_6_data22 ),
    .data30(\显示译码器_6_data30 ), .data7(\显示译码器_6_data7 ), .data15(\显示译码器_6_data15 ), .data23(\显示译码器_6_data23 ),
    .data31(\显示译码器_6_data31 ), .data8(\显示译码器_6_data8 ), .data16(\显示译码器_6_data16 ), .data24(\显示译码器_6_data24 ),
    .data32(\显示译码器_6_data32 ));
  DotMatrix #(.inputtype("column"), .matrixcols(32), .matrixrows(32), .persist(0), .dotshape("square")) dotmatrix_7 (
    .col0(\显示译码器_7_data1 ), .col1(\显示译码器_7_data2 ), .col2(\显示译码器_7_data3 ), .col3(\显示译码器_7_data4 ),
    .col4(\显示译码器_7_data5 ), .col5(\显示译码器_7_data6 ), .col6(\显示译码器_7_data7 ), .col7(\显示译码器_7_data8 ),
    .col8(\显示译码器_7_data9 ), .col9(\显示译码器_7_data10 ), .col10(\显示译码器_7_data11 ), .col11(\显示译码器_7_data12 ),
    .col12(\显示译码器_7_data13 ), .col13(\显示译码器_7_data14 ), .col14(\显示译码器_7_data15 ), .col15(\显示译码器_7_data16 ),
    .col16(\显示译码器_7_data17 ), .col17(\显示译码器_7_data18 ), .col18(\显示译码器_7_data19 ), .col19(\显示译码器_7_data20 ),
    .col20(\显示译码器_7_data21 ), .col21(\显示译码器_7_data22 ), .col22(\显示译码器_7_data23 ), .col23(\显示译码器_7_data24 ),
    .col24(\显示译码器_7_data25 ), .col25(\显示译码器_7_data26 ), .col26(\显示译码器_7_data27 ), .col27(\显示译码器_7_data28 ),
    .col28(\显示译码器_7_data29 ), .col29(\显示译码器_7_data30 ), .col30(\显示译码器_7_data31 ), .col31(\显示译码器_7_data32 ));
  \显示译码器  \u_显示译码器_7  (
    .\input (_2048d10), .data1(\显示译码器_7_data1 ), .data9(\显示译码器_7_data9 ), .data17(\显示译码器_7_data17 ),
    .data25(\显示译码器_7_data25 ), .data2(\显示译码器_7_data2 ), .data10(\显示译码器_7_data10 ), .data18(\显示译码器_7_data18 ),
    .data26(\显示译码器_7_data26 ), .data3(\显示译码器_7_data3 ), .data11(\显示译码器_7_data11 ), .data19(\显示译码器_7_data19 ),
    .data27(\显示译码器_7_data27 ), .data4(\显示译码器_7_data4 ), .data12(\显示译码器_7_data12 ), .data20(\显示译码器_7_data20 ),
    .data28(\显示译码器_7_data28 ), .data5(\显示译码器_7_data5 ), .data13(\显示译码器_7_data13 ), .data21(\显示译码器_7_data21 ),
    .data29(\显示译码器_7_data29 ), .data6(\显示译码器_7_data6 ), .data14(\显示译码器_7_data14 ), .data22(\显示译码器_7_data22 ),
    .data30(\显示译码器_7_data30 ), .data7(\显示译码器_7_data7 ), .data15(\显示译码器_7_data15 ), .data23(\显示译码器_7_data23 ),
    .data31(\显示译码器_7_data31 ), .data8(\显示译码器_7_data8 ), .data16(\显示译码器_7_data16 ), .data24(\显示译码器_7_data24 ),
    .data32(\显示译码器_7_data32 ));
  DotMatrix #(.inputtype("column"), .matrixcols(32), .matrixrows(32), .persist(0), .dotshape("square")) dotmatrix_8 (
    .col0(\显示译码器_8_data1 ), .col1(\显示译码器_8_data2 ), .col2(\显示译码器_8_data3 ), .col3(\显示译码器_8_data4 ),
    .col4(\显示译码器_8_data5 ), .col5(\显示译码器_8_data6 ), .col6(\显示译码器_8_data7 ), .col7(\显示译码器_8_data8 ),
    .col8(\显示译码器_8_data9 ), .col9(\显示译码器_8_data10 ), .col10(\显示译码器_8_data11 ), .col11(\显示译码器_8_data12 ),
    .col12(\显示译码器_8_data13 ), .col13(\显示译码器_8_data14 ), .col14(\显示译码器_8_data15 ), .col15(\显示译码器_8_data16 ),
    .col16(\显示译码器_8_data17 ), .col17(\显示译码器_8_data18 ), .col18(\显示译码器_8_data19 ), .col19(\显示译码器_8_data20 ),
    .col20(\显示译码器_8_data21 ), .col21(\显示译码器_8_data22 ), .col22(\显示译码器_8_data23 ), .col23(\显示译码器_8_data24 ),
    .col24(\显示译码器_8_data25 ), .col25(\显示译码器_8_data26 ), .col26(\显示译码器_8_data27 ), .col27(\显示译码器_8_data28 ),
    .col28(\显示译码器_8_data29 ), .col29(\显示译码器_8_data30 ), .col30(\显示译码器_8_data31 ), .col31(\显示译码器_8_data32 ));
  \显示译码器  \u_显示译码器_8  (
    .\input (_2048d14), .data1(\显示译码器_8_data1 ), .data9(\显示译码器_8_data9 ), .data17(\显示译码器_8_data17 ),
    .data25(\显示译码器_8_data25 ), .data2(\显示译码器_8_data2 ), .data10(\显示译码器_8_data10 ), .data18(\显示译码器_8_data18 ),
    .data26(\显示译码器_8_data26 ), .data3(\显示译码器_8_data3 ), .data11(\显示译码器_8_data11 ), .data19(\显示译码器_8_data19 ),
    .data27(\显示译码器_8_data27 ), .data4(\显示译码器_8_data4 ), .data12(\显示译码器_8_data12 ), .data20(\显示译码器_8_data20 ),
    .data28(\显示译码器_8_data28 ), .data5(\显示译码器_8_data5 ), .data13(\显示译码器_8_data13 ), .data21(\显示译码器_8_data21 ),
    .data29(\显示译码器_8_data29 ), .data6(\显示译码器_8_data6 ), .data14(\显示译码器_8_data14 ), .data22(\显示译码器_8_data22 ),
    .data30(\显示译码器_8_data30 ), .data7(\显示译码器_8_data7 ), .data15(\显示译码器_8_data15 ), .data23(\显示译码器_8_data23 ),
    .data31(\显示译码器_8_data31 ), .data8(\显示译码器_8_data8 ), .data16(\显示译码器_8_data16 ), .data24(\显示译码器_8_data24 ),
    .data32(\显示译码器_8_data32 ));
  DotMatrix #(.inputtype("column"), .matrixcols(32), .matrixrows(32), .persist(0), .dotshape("square")) dotmatrix_9 (
    .col0(\显示译码器_9_data1 ), .col1(\显示译码器_9_data2 ), .col2(\显示译码器_9_data3 ), .col3(\显示译码器_9_data4 ),
    .col4(\显示译码器_9_data5 ), .col5(\显示译码器_9_data6 ), .col6(\显示译码器_9_data7 ), .col7(\显示译码器_9_data8 ),
    .col8(\显示译码器_9_data9 ), .col9(\显示译码器_9_data10 ), .col10(\显示译码器_9_data11 ), .col11(\显示译码器_9_data12 ),
    .col12(\显示译码器_9_data13 ), .col13(\显示译码器_9_data14 ), .col14(\显示译码器_9_data15 ), .col15(\显示译码器_9_data16 ),
    .col16(\显示译码器_9_data17 ), .col17(\显示译码器_9_data18 ), .col18(\显示译码器_9_data19 ), .col19(\显示译码器_9_data20 ),
    .col20(\显示译码器_9_data21 ), .col21(\显示译码器_9_data22 ), .col22(\显示译码器_9_data23 ), .col23(\显示译码器_9_data24 ),
    .col24(\显示译码器_9_data25 ), .col25(\显示译码器_9_data26 ), .col26(\显示译码器_9_data27 ), .col27(\显示译码器_9_data28 ),
    .col28(\显示译码器_9_data29 ), .col29(\显示译码器_9_data30 ), .col30(\显示译码器_9_data31 ), .col31(\显示译码器_9_data32 ));
  \显示译码器  \u_显示译码器_9  (
    .\input (_2048d3), .data1(\显示译码器_9_data1 ), .data9(\显示译码器_9_data9 ), .data17(\显示译码器_9_data17 ),
    .data25(\显示译码器_9_data25 ), .data2(\显示译码器_9_data2 ), .data10(\显示译码器_9_data10 ), .data18(\显示译码器_9_data18 ),
    .data26(\显示译码器_9_data26 ), .data3(\显示译码器_9_data3 ), .data11(\显示译码器_9_data11 ), .data19(\显示译码器_9_data19 ),
    .data27(\显示译码器_9_data27 ), .data4(\显示译码器_9_data4 ), .data12(\显示译码器_9_data12 ), .data20(\显示译码器_9_data20 ),
    .data28(\显示译码器_9_data28 ), .data5(\显示译码器_9_data5 ), .data13(\显示译码器_9_data13 ), .data21(\显示译码器_9_data21 ),
    .data29(\显示译码器_9_data29 ), .data6(\显示译码器_9_data6 ), .data14(\显示译码器_9_data14 ), .data22(\显示译码器_9_data22 ),
    .data30(\显示译码器_9_data30 ), .data7(\显示译码器_9_data7 ), .data15(\显示译码器_9_data15 ), .data23(\显示译码器_9_data23 ),
    .data31(\显示译码器_9_data31 ), .data8(\显示译码器_9_data8 ), .data16(\显示译码器_9_data16 ), .data24(\显示译码器_9_data24 ),
    .data32(\显示译码器_9_data32 ));
  DotMatrix #(.inputtype("column"), .matrixcols(32), .matrixrows(32), .persist(0), .dotshape("square")) dotmatrix_10 (
    .col0(\显示译码器_10_data1 ), .col1(\显示译码器_10_data2 ), .col2(\显示译码器_10_data3 ), .col3(\显示译码器_10_data4 ),
    .col4(\显示译码器_10_data5 ), .col5(\显示译码器_10_data6 ), .col6(\显示译码器_10_data7 ), .col7(\显示译码器_10_data8 ),
    .col8(\显示译码器_10_data9 ), .col9(\显示译码器_10_data10 ), .col10(\显示译码器_10_data11 ), .col11(\显示译码器_10_data12 ),
    .col12(\显示译码器_10_data13 ), .col13(\显示译码器_10_data14 ), .col14(\显示译码器_10_data15 ),
    .col15(\显示译码器_10_data16 ), .col16(\显示译码器_10_data17 ), .col17(\显示译码器_10_data18 ),
    .col18(\显示译码器_10_data19 ), .col19(\显示译码器_10_data20 ), .col20(\显示译码器_10_data21 ),
    .col21(\显示译码器_10_data22 ), .col22(\显示译码器_10_data23 ), .col23(\显示译码器_10_data24 ),
    .col24(\显示译码器_10_data25 ), .col25(\显示译码器_10_data26 ), .col26(\显示译码器_10_data27 ),
    .col27(\显示译码器_10_data28 ), .col28(\显示译码器_10_data29 ), .col29(\显示译码器_10_data30 ),
    .col30(\显示译码器_10_data31 ), .col31(\显示译码器_10_data32 ));
  \显示译码器  \u_显示译码器_10  (
    .\input (_2048d7), .data1(\显示译码器_10_data1 ), .data9(\显示译码器_10_data9 ), .data17(\显示译码器_10_data17 ),
    .data25(\显示译码器_10_data25 ), .data2(\显示译码器_10_data2 ), .data10(\显示译码器_10_data10 ),
    .data18(\显示译码器_10_data18 ), .data26(\显示译码器_10_data26 ), .data3(\显示译码器_10_data3 ),
    .data11(\显示译码器_10_data11 ), .data19(\显示译码器_10_data19 ), .data27(\显示译码器_10_data27 ),
    .data4(\显示译码器_10_data4 ), .data12(\显示译码器_10_data12 ), .data20(\显示译码器_10_data20 ),
    .data28(\显示译码器_10_data28 ), .data5(\显示译码器_10_data5 ), .data13(\显示译码器_10_data13 ),
    .data21(\显示译码器_10_data21 ), .data29(\显示译码器_10_data29 ), .data6(\显示译码器_10_data6 ),
    .data14(\显示译码器_10_data14 ), .data22(\显示译码器_10_data22 ), .data30(\显示译码器_10_data30 ),
    .data7(\显示译码器_10_data7 ), .data15(\显示译码器_10_data15 ), .data23(\显示译码器_10_data23 ),
    .data31(\显示译码器_10_data31 ), .data8(\显示译码器_10_data8 ), .data16(\显示译码器_10_data16 ),
    .data24(\显示译码器_10_data24 ), .data32(\显示译码器_10_data32 ));
  DotMatrix #(.inputtype("column"), .matrixcols(32), .matrixrows(32), .persist(0), .dotshape("square")) dotmatrix_11 (
    .col0(\显示译码器_11_data1 ), .col1(\显示译码器_11_data2 ), .col2(\显示译码器_11_data3 ), .col3(\显示译码器_11_data4 ),
    .col4(\显示译码器_11_data5 ), .col5(\显示译码器_11_data6 ), .col6(\显示译码器_11_data7 ), .col7(\显示译码器_11_data8 ),
    .col8(\显示译码器_11_data9 ), .col9(\显示译码器_11_data10 ), .col10(\显示译码器_11_data11 ), .col11(\显示译码器_11_data12 ),
    .col12(\显示译码器_11_data13 ), .col13(\显示译码器_11_data14 ), .col14(\显示译码器_11_data15 ),
    .col15(\显示译码器_11_data16 ), .col16(\显示译码器_11_data17 ), .col17(\显示译码器_11_data18 ),
    .col18(\显示译码器_11_data19 ), .col19(\显示译码器_11_data20 ), .col20(\显示译码器_11_data21 ),
    .col21(\显示译码器_11_data22 ), .col22(\显示译码器_11_data23 ), .col23(\显示译码器_11_data24 ),
    .col24(\显示译码器_11_data25 ), .col25(\显示译码器_11_data26 ), .col26(\显示译码器_11_data27 ),
    .col27(\显示译码器_11_data28 ), .col28(\显示译码器_11_data29 ), .col29(\显示译码器_11_data30 ),
    .col30(\显示译码器_11_data31 ), .col31(\显示译码器_11_data32 ));
  \显示译码器  \u_显示译码器_11  (
    .\input (_2048d11), .data1(\显示译码器_11_data1 ), .data9(\显示译码器_11_data9 ), .data17(\显示译码器_11_data17 ),
    .data25(\显示译码器_11_data25 ), .data2(\显示译码器_11_data2 ), .data10(\显示译码器_11_data10 ),
    .data18(\显示译码器_11_data18 ), .data26(\显示译码器_11_data26 ), .data3(\显示译码器_11_data3 ),
    .data11(\显示译码器_11_data11 ), .data19(\显示译码器_11_data19 ), .data27(\显示译码器_11_data27 ),
    .data4(\显示译码器_11_data4 ), .data12(\显示译码器_11_data12 ), .data20(\显示译码器_11_data20 ),
    .data28(\显示译码器_11_data28 ), .data5(\显示译码器_11_data5 ), .data13(\显示译码器_11_data13 ),
    .data21(\显示译码器_11_data21 ), .data29(\显示译码器_11_data29 ), .data6(\显示译码器_11_data6 ),
    .data14(\显示译码器_11_data14 ), .data22(\显示译码器_11_data22 ), .data30(\显示译码器_11_data30 ),
    .data7(\显示译码器_11_data7 ), .data15(\显示译码器_11_data15 ), .data23(\显示译码器_11_data23 ),
    .data31(\显示译码器_11_data31 ), .data8(\显示译码器_11_data8 ), .data16(\显示译码器_11_data16 ),
    .data24(\显示译码器_11_data24 ), .data32(\显示译码器_11_data32 ));
  DotMatrix #(.inputtype("column"), .matrixcols(32), .matrixrows(32), .persist(0), .dotshape("square")) dotmatrix_12 (
    .col0(\显示译码器_12_data1 ), .col1(\显示译码器_12_data2 ), .col2(\显示译码器_12_data3 ), .col3(\显示译码器_12_data4 ),
    .col4(\显示译码器_12_data5 ), .col5(\显示译码器_12_data6 ), .col6(\显示译码器_12_data7 ), .col7(\显示译码器_12_data8 ),
    .col8(\显示译码器_12_data9 ), .col9(\显示译码器_12_data10 ), .col10(\显示译码器_12_data11 ), .col11(\显示译码器_12_data12 ),
    .col12(\显示译码器_12_data13 ), .col13(\显示译码器_12_data14 ), .col14(\显示译码器_12_data15 ),
    .col15(\显示译码器_12_data16 ), .col16(\显示译码器_12_data17 ), .col17(\显示译码器_12_data18 ),
    .col18(\显示译码器_12_data19 ), .col19(\显示译码器_12_data20 ), .col20(\显示译码器_12_data21 ),
    .col21(\显示译码器_12_data22 ), .col22(\显示译码器_12_data23 ), .col23(\显示译码器_12_data24 ),
    .col24(\显示译码器_12_data25 ), .col25(\显示译码器_12_data26 ), .col26(\显示译码器_12_data27 ),
    .col27(\显示译码器_12_data28 ), .col28(\显示译码器_12_data29 ), .col29(\显示译码器_12_data30 ),
    .col30(\显示译码器_12_data31 ), .col31(\显示译码器_12_data32 ));
  \显示译码器  \u_显示译码器_12  (
    .\input (_2048d15), .data1(\显示译码器_12_data1 ), .data9(\显示译码器_12_data9 ), .data17(\显示译码器_12_data17 ),
    .data25(\显示译码器_12_data25 ), .data2(\显示译码器_12_data2 ), .data10(\显示译码器_12_data10 ),
    .data18(\显示译码器_12_data18 ), .data26(\显示译码器_12_data26 ), .data3(\显示译码器_12_data3 ),
    .data11(\显示译码器_12_data11 ), .data19(\显示译码器_12_data19 ), .data27(\显示译码器_12_data27 ),
    .data4(\显示译码器_12_data4 ), .data12(\显示译码器_12_data12 ), .data20(\显示译码器_12_data20 ),
    .data28(\显示译码器_12_data28 ), .data5(\显示译码器_12_data5 ), .data13(\显示译码器_12_data13 ),
    .data21(\显示译码器_12_data21 ), .data29(\显示译码器_12_data29 ), .data6(\显示译码器_12_data6 ),
    .data14(\显示译码器_12_data14 ), .data22(\显示译码器_12_data22 ), .data30(\显示译码器_12_data30 ),
    .data7(\显示译码器_12_data7 ), .data15(\显示译码器_12_data15 ), .data23(\显示译码器_12_data23 ),
    .data31(\显示译码器_12_data31 ), .data8(\显示译码器_12_data8 ), .data16(\显示译码器_12_data16 ),
    .data24(\显示译码器_12_data24 ), .data32(\显示译码器_12_data32 ));
  DotMatrix #(.inputtype("column"), .matrixcols(32), .matrixrows(32), .persist(0), .dotshape("square")) dotmatrix_13 (
    .col0(\显示译码器_13_data1 ), .col1(\显示译码器_13_data2 ), .col2(\显示译码器_13_data3 ), .col3(\显示译码器_13_data4 ),
    .col4(\显示译码器_13_data5 ), .col5(\显示译码器_13_data6 ), .col6(\显示译码器_13_data7 ), .col7(\显示译码器_13_data8 ),
    .col8(\显示译码器_13_data9 ), .col9(\显示译码器_13_data10 ), .col10(\显示译码器_13_data11 ), .col11(\显示译码器_13_data12 ),
    .col12(\显示译码器_13_data13 ), .col13(\显示译码器_13_data14 ), .col14(\显示译码器_13_data15 ),
    .col15(\显示译码器_13_data16 ), .col16(\显示译码器_13_data17 ), .col17(\显示译码器_13_data18 ),
    .col18(\显示译码器_13_data19 ), .col19(\显示译码器_13_data20 ), .col20(\显示译码器_13_data21 ),
    .col21(\显示译码器_13_data22 ), .col22(\显示译码器_13_data23 ), .col23(\显示译码器_13_data24 ),
    .col24(\显示译码器_13_data25 ), .col25(\显示译码器_13_data26 ), .col26(\显示译码器_13_data27 ),
    .col27(\显示译码器_13_data28 ), .col28(\显示译码器_13_data29 ), .col29(\显示译码器_13_data30 ),
    .col30(\显示译码器_13_data31 ), .col31(\显示译码器_13_data32 ));
  \显示译码器  \u_显示译码器_13  (
    .\input (_2048d4), .data1(\显示译码器_13_data1 ), .data9(\显示译码器_13_data9 ), .data17(\显示译码器_13_data17 ),
    .data25(\显示译码器_13_data25 ), .data2(\显示译码器_13_data2 ), .data10(\显示译码器_13_data10 ),
    .data18(\显示译码器_13_data18 ), .data26(\显示译码器_13_data26 ), .data3(\显示译码器_13_data3 ),
    .data11(\显示译码器_13_data11 ), .data19(\显示译码器_13_data19 ), .data27(\显示译码器_13_data27 ),
    .data4(\显示译码器_13_data4 ), .data12(\显示译码器_13_data12 ), .data20(\显示译码器_13_data20 ),
    .data28(\显示译码器_13_data28 ), .data5(\显示译码器_13_data5 ), .data13(\显示译码器_13_data13 ),
    .data21(\显示译码器_13_data21 ), .data29(\显示译码器_13_data29 ), .data6(\显示译码器_13_data6 ),
    .data14(\显示译码器_13_data14 ), .data22(\显示译码器_13_data22 ), .data30(\显示译码器_13_data30 ),
    .data7(\显示译码器_13_data7 ), .data15(\显示译码器_13_data15 ), .data23(\显示译码器_13_data23 ),
    .data31(\显示译码器_13_data31 ), .data8(\显示译码器_13_data8 ), .data16(\显示译码器_13_data16 ),
    .data24(\显示译码器_13_data24 ), .data32(\显示译码器_13_data32 ));
  DotMatrix #(.inputtype("column"), .matrixcols(32), .matrixrows(32), .persist(0), .dotshape("square")) dotmatrix_14 (
    .col0(\显示译码器_14_data1 ), .col1(\显示译码器_14_data2 ), .col2(\显示译码器_14_data3 ), .col3(\显示译码器_14_data4 ),
    .col4(\显示译码器_14_data5 ), .col5(\显示译码器_14_data6 ), .col6(\显示译码器_14_data7 ), .col7(\显示译码器_14_data8 ),
    .col8(\显示译码器_14_data9 ), .col9(\显示译码器_14_data10 ), .col10(\显示译码器_14_data11 ), .col11(\显示译码器_14_data12 ),
    .col12(\显示译码器_14_data13 ), .col13(\显示译码器_14_data14 ), .col14(\显示译码器_14_data15 ),
    .col15(\显示译码器_14_data16 ), .col16(\显示译码器_14_data17 ), .col17(\显示译码器_14_data18 ),
    .col18(\显示译码器_14_data19 ), .col19(\显示译码器_14_data20 ), .col20(\显示译码器_14_data21 ),
    .col21(\显示译码器_14_data22 ), .col22(\显示译码器_14_data23 ), .col23(\显示译码器_14_data24 ),
    .col24(\显示译码器_14_data25 ), .col25(\显示译码器_14_data26 ), .col26(\显示译码器_14_data27 ),
    .col27(\显示译码器_14_data28 ), .col28(\显示译码器_14_data29 ), .col29(\显示译码器_14_data30 ),
    .col30(\显示译码器_14_data31 ), .col31(\显示译码器_14_data32 ));
  \显示译码器  \u_显示译码器_14  (
    .\input (_2048d8), .data1(\显示译码器_14_data1 ), .data9(\显示译码器_14_data9 ), .data17(\显示译码器_14_data17 ),
    .data25(\显示译码器_14_data25 ), .data2(\显示译码器_14_data2 ), .data10(\显示译码器_14_data10 ),
    .data18(\显示译码器_14_data18 ), .data26(\显示译码器_14_data26 ), .data3(\显示译码器_14_data3 ),
    .data11(\显示译码器_14_data11 ), .data19(\显示译码器_14_data19 ), .data27(\显示译码器_14_data27 ),
    .data4(\显示译码器_14_data4 ), .data12(\显示译码器_14_data12 ), .data20(\显示译码器_14_data20 ),
    .data28(\显示译码器_14_data28 ), .data5(\显示译码器_14_data5 ), .data13(\显示译码器_14_data13 ),
    .data21(\显示译码器_14_data21 ), .data29(\显示译码器_14_data29 ), .data6(\显示译码器_14_data6 ),
    .data14(\显示译码器_14_data14 ), .data22(\显示译码器_14_data22 ), .data30(\显示译码器_14_data30 ),
    .data7(\显示译码器_14_data7 ), .data15(\显示译码器_14_data15 ), .data23(\显示译码器_14_data23 ),
    .data31(\显示译码器_14_data31 ), .data8(\显示译码器_14_data8 ), .data16(\显示译码器_14_data16 ),
    .data24(\显示译码器_14_data24 ), .data32(\显示译码器_14_data32 ));
  DotMatrix #(.inputtype("column"), .matrixcols(32), .matrixrows(32), .persist(0), .dotshape("square")) dotmatrix_15 (
    .col0(\显示译码器_15_data1 ), .col1(\显示译码器_15_data2 ), .col2(\显示译码器_15_data3 ), .col3(\显示译码器_15_data4 ),
    .col4(\显示译码器_15_data5 ), .col5(\显示译码器_15_data6 ), .col6(\显示译码器_15_data7 ), .col7(\显示译码器_15_data8 ),
    .col8(\显示译码器_15_data9 ), .col9(\显示译码器_15_data10 ), .col10(\显示译码器_15_data11 ), .col11(\显示译码器_15_data12 ),
    .col12(\显示译码器_15_data13 ), .col13(\显示译码器_15_data14 ), .col14(\显示译码器_15_data15 ),
    .col15(\显示译码器_15_data16 ), .col16(\显示译码器_15_data17 ), .col17(\显示译码器_15_data18 ),
    .col18(\显示译码器_15_data19 ), .col19(\显示译码器_15_data20 ), .col20(\显示译码器_15_data21 ),
    .col21(\显示译码器_15_data22 ), .col22(\显示译码器_15_data23 ), .col23(\显示译码器_15_data24 ),
    .col24(\显示译码器_15_data25 ), .col25(\显示译码器_15_data26 ), .col26(\显示译码器_15_data27 ),
    .col27(\显示译码器_15_data28 ), .col28(\显示译码器_15_data29 ), .col29(\显示译码器_15_data30 ),
    .col30(\显示译码器_15_data31 ), .col31(\显示译码器_15_data32 ));
  \显示译码器  \u_显示译码器_15  (
    .\input (_2048d12), .data1(\显示译码器_15_data1 ), .data9(\显示译码器_15_data9 ), .data17(\显示译码器_15_data17 ),
    .data25(\显示译码器_15_data25 ), .data2(\显示译码器_15_data2 ), .data10(\显示译码器_15_data10 ),
    .data18(\显示译码器_15_data18 ), .data26(\显示译码器_15_data26 ), .data3(\显示译码器_15_data3 ),
    .data11(\显示译码器_15_data11 ), .data19(\显示译码器_15_data19 ), .data27(\显示译码器_15_data27 ),
    .data4(\显示译码器_15_data4 ), .data12(\显示译码器_15_data12 ), .data20(\显示译码器_15_data20 ),
    .data28(\显示译码器_15_data28 ), .data5(\显示译码器_15_data5 ), .data13(\显示译码器_15_data13 ),
    .data21(\显示译码器_15_data21 ), .data29(\显示译码器_15_data29 ), .data6(\显示译码器_15_data6 ),
    .data14(\显示译码器_15_data14 ), .data22(\显示译码器_15_data22 ), .data30(\显示译码器_15_data30 ),
    .data7(\显示译码器_15_data7 ), .data15(\显示译码器_15_data15 ), .data23(\显示译码器_15_data23 ),
    .data31(\显示译码器_15_data31 ), .data8(\显示译码器_15_data8 ), .data16(\显示译码器_15_data16 ),
    .data24(\显示译码器_15_data24 ), .data32(\显示译码器_15_data32 ));
  DotMatrix #(.inputtype("column"), .matrixcols(32), .matrixrows(32), .persist(0), .dotshape("square")) dotmatrix_16 (
    .col0(\显示译码器_16_data1 ), .col1(\显示译码器_16_data2 ), .col2(\显示译码器_16_data3 ), .col3(\显示译码器_16_data4 ),
    .col4(\显示译码器_16_data5 ), .col5(\显示译码器_16_data6 ), .col6(\显示译码器_16_data7 ), .col7(\显示译码器_16_data8 ),
    .col8(\显示译码器_16_data9 ), .col9(\显示译码器_16_data10 ), .col10(\显示译码器_16_data11 ), .col11(\显示译码器_16_data12 ),
    .col12(\显示译码器_16_data13 ), .col13(\显示译码器_16_data14 ), .col14(\显示译码器_16_data15 ),
    .col15(\显示译码器_16_data16 ), .col16(\显示译码器_16_data17 ), .col17(\显示译码器_16_data18 ),
    .col18(\显示译码器_16_data19 ), .col19(\显示译码器_16_data20 ), .col20(\显示译码器_16_data21 ),
    .col21(\显示译码器_16_data22 ), .col22(\显示译码器_16_data23 ), .col23(\显示译码器_16_data24 ),
    .col24(\显示译码器_16_data25 ), .col25(\显示译码器_16_data26 ), .col26(\显示译码器_16_data27 ),
    .col27(\显示译码器_16_data28 ), .col28(\显示译码器_16_data29 ), .col29(\显示译码器_16_data30 ),
    .col30(\显示译码器_16_data31 ), .col31(\显示译码器_16_data32 ));
  \显示译码器  \u_显示译码器_16  (
    .\input (_2048d16), .data1(\显示译码器_16_data1 ), .data9(\显示译码器_16_data9 ), .data17(\显示译码器_16_data17 ),
    .data25(\显示译码器_16_data25 ), .data2(\显示译码器_16_data2 ), .data10(\显示译码器_16_data10 ),
    .data18(\显示译码器_16_data18 ), .data26(\显示译码器_16_data26 ), .data3(\显示译码器_16_data3 ),
    .data11(\显示译码器_16_data11 ), .data19(\显示译码器_16_data19 ), .data27(\显示译码器_16_data27 ),
    .data4(\显示译码器_16_data4 ), .data12(\显示译码器_16_data12 ), .data20(\显示译码器_16_data20 ),
    .data28(\显示译码器_16_data28 ), .data5(\显示译码器_16_data5 ), .data13(\显示译码器_16_data13 ),
    .data21(\显示译码器_16_data21 ), .data29(\显示译码器_16_data29 ), .data6(\显示译码器_16_data6 ),
    .data14(\显示译码器_16_data14 ), .data22(\显示译码器_16_data22 ), .data30(\显示译码器_16_data30 ),
    .data7(\显示译码器_16_data7 ), .data15(\显示译码器_16_data15 ), .data23(\显示译码器_16_data23 ),
    .data31(\显示译码器_16_data31 ), .data8(\显示译码器_16_data8 ), .data16(\显示译码器_16_data16 ),
    .data24(\显示译码器_16_data24 ), .data32(\显示译码器_16_data32 ));
  Button \u_左  ();  // open: out
  Comparator #(.width(7), .mode("unsigned")) comparator_11 (
    .a(register_18_q), .b(7'b1110111), .eq(IRC));  // open: gt, lt
  Comparator #(.width(7), .mode("unsigned")) comparator_12 (
    .a(register_18_q), .b(7'b1100001), .eq(IRB));  // open: gt, lt
  Comparator #(.width(7), .mode("unsigned")) comparator_13 (
    .a(register_18_q), .b(7'b1110011), .eq(IRD));  // open: gt, lt
  Button \u_上  ();  // open: out
  Button \u_下  ();  // open: out
  Comparator #(.width(7), .mode("unsigned")) comparator_14 (
    .a(register_18_q), .b(7'b1100100), .eq(IRA));  // open: gt, lt
  Button \u_右  ();  // open: out
  Keyboard #(.Char_bit_width(7), .buflen(32), .trigger("rising")) keyboard_1 (
    .clk(CLK), .data(keyboard_1_data));  // open: re, clr, avail
  Register #(.width(7), .trigger("rising"), .Select("low")) register_18 (
    .D(keyboard_1_data), .Q(register_18_q), .clk(CLK));  // open: en, clr

  // Other names for the same wires on the sheet: v0[31:0] = DIN; MAddr[9:0] = AIN[11:2]

  // Notes on the sheet:
  //   中断源
  //   中断等待指示
  //   总复位信号应将除ROM以外所有存储组件全部清零
  //   控制位
  //   暂停节拍，不能为0
  //   用这个时钟源需要去掉电路中的其他时钟源
  //   戳工具置1进入计数暂停模式，ctrl+k时钟自动运行到对应节拍暂停
  //   ctrl+k关闭时钟连续运行，将控制位置零，进入单步调试模式调试
  //   数码管输出
  //   数码管输出应该用寄存器锁存，否则显示数据只能一闪而过
  //   可计数暂停的时钟源
  //   指令存储器
  //   contents of rom_1 (hex, n*v repeats v):
  //   20100000 20110010 20120020 20130030 20140002 20020002 c 20080000 110f0003 22100004 21080001 8000c08
  //   ae140000 20020002 c 20080000 110f0003 22310004 21080001 8000c10 ae340000 20020002 c 20080000
  //   110f0003 22520004 21080001 8000c18 ae540000 20020002 c 20080000 110f0003 22730004 21080001 8000c20
  //   ae740000 20020022 c 8000c27 20080000 200a0040 8d100000 8d110004 8d120008 8d13000c 16200002 22110000
  //   20100000 16400003 22320000 22110000 20100000 20090000 12000004 16110003 20090001 2308820 20100000
  //   12200005 16320004 20090001 2519020 22110000 20100000 12400006 16530005 20090001 2729820 22320000
  //   22110000 20100000 1520ffec 200b0000 200c0004 16000006 22300000 22510000 22720000 20130000 216b0001
  //   156cfff9 ad100000 ad110004 ad120008 ad13000c 21080010 150affd2 2008000c 8d100000 8d110010 8d120020
  //   8d130030 16000006 20020001 c 11e00003 20100002 ad100000 8000c75 16200006 20020001 c 11e00003
  //   20110002 ad110010 8000c75 16400006 20020001 c 11e00003 20120002 ad120020 8000c75 16600002 20130002
  //   ad130030 20020022 c 42000018 20080000 200a0040 8d10000c 8d110008 8d120004 8d130000 16200002 22110000
  //   20100000 16400003 22320000 22110000 20100000 20090000 12000004 16110003 20090001 2308820 20100000
  //   12200005 16320004 20090001 2519020 22110000 20100000 12400006 16530005 20090001 2729820 22320000
  //   22110000 20100000 1520ffec 200b0000 200c0004 16000006 22300000 22510000 22720000 20130000 216b0001
  //   156cfff9 ad10000c ad110008 ad120004 ad130000 21080010 150affd2 20080000 8d100000 8d110010 8d120020
  //   8d130030 16000006 20020001 c 11e00003 20100002 ad100000 8000cc5 16200006 20020001 c 11e00003
  //   20110002 ad110010 8000cc5 16400006 20020001 c 11e00003 20120002 ad120020 8000cc5 16600002 20130002
  //   ad130030 20020022 c 42000018 20080000 200a0010 8d100000 8d110010 8d120020 8d130030 16200002 22110000
  //   20100000 16400003 22320000 22110000 20100000 20090000 12000004 16110003 20090001 2308820 20100000
  //   12200005 16320004 20090001 2519020 22110000 20100000 12400006 16530005 20090001 2729820 22320000
  //   22110000 20100000 1520ffec 200b0000 200c0004 16000006 22300000 22510000 22720000 20130000 216b0001
  //   156cfff9 ad100000 ad110010 ad120020 ad130030 21080004 150affd2 20080030 8d100000 8d110004 8d120008
  //   8d13000c 16000006 20020001 c 11e00003 20100002 ad100000 8000d15 16200006 20020001 c 11e00003
  //   20110002 ad110004 8000d15 16400006 20020001 c 11e00003 20120002 ad120008 8000d15 16600002 20130002
  //   ad13000c 20020022 c 42000018 20080000 200a0010 8d100030 8d110020 8d120010 8d130000 16200002 22110000
  //   20100000 16400003 22320000 22110000 20100000 20090000 12000004 16110003 20090001 2308820 20100000
  //   12200005 16320004 20090001 2519020 22110000 20100000 12400006 16530005 20090001 2729820 22320000
  //   22110000 20100000 1520ffec 200b0000 200c0004 16000006 22300000 22510000 22720000 20130000 216b0001
  //   156cfff9 ad100030 ad110020 ad120010 ad130000 21080004 150affd2 20080000 8d100000 8d110004 8d120008
  //   8d13000c 16000006 20020001 c 11e00003 20100002 ad100000 8000d65 16200006 20020001 c 11e00003
  //   20110002 ad110004 8000d65 16400006 20020001 c 11e00003 20120002 ad120008 8000d65 16600002 20130002
  //   ad13000c 20020022 c 42000018
  //   指令字
  //   JMP
  //   JR
  //   OP
  //   OP
  //   Func
  //   Func
  //   rs
  //   rt
  //   rd
  //   SB
  //   BLTZ
  //   Beq
  //   Bne
  //   MemToReg
  //   MemWrite
  //   AluOP
  //   AluSrcB
  //   RegWrite
  //   JAL
  //   RegDst
  //   Syscall
  //   为方便自动评测，需要输出PC，IR，寄存器堆写如数据RDin
  //   RAM写使能MemWrite、RAM写入数据MDin等信号
  //   单级中断测试信号模拟器
endmodule
module \单周期MIPS_多级中断  (
  input  IR1,
  input  IR2,
  input  IR3,
  output RegWrite,
  output MemWrite,
  output [31:0] PC,
  output [31:0] IR,
  output [31:0] RDin,
  output [31:0] MDin,
  output [31:0] LedData
);

  wire and_1_out, and_2_out, and_3_out, and_9_out, and_10_out, and_11_out, and_12_out, and_13_out,
       and_14_out, and_15_out, and_17_out, and_18_out, CLK, clock_2_out, comparator_1_eq, comparator_1_lt,
       comparator_2_eq, comparator_3_eq, comparator_4_eq, comparator_6_eq, comparator_7_eq, comparator_8_eq,
       comparator_9_eq, comparator_10_gt, comparator_11_eq, comparator_12_eq, comparator_13_eq,
       comparator_14_eq, comparator_15_eq, comparator_16_eq, comparator_17_eq, d_ff_1_q, d_ff_2_q, d_ff_3_q,
       d_ff_4_q, decoder_1_out1, decoder_1_out2, decoder_1_out3, en, ERET, Go, \IE_0为开中断_q , \IE_0为开中断_qn ,
       IE_in, INT, IR1_t, ir1_t_t, IR2_t, ir2_t_t, IR3_t, ir3_t_t, IRA, IRB, IRC, MFC0, mips_alu_1_equal,
       MTC0, multiplexer_18_out, nand_1_out, or_4_out, or_5_out, or_6_out, or_11_out, or_12_out, or_13_out,
       or_14_out, or_15_out, priority_encoder_1_gs, priority_encoder_2_out, priority_encoder_3_out,
       pull_resistor_2_node, Rst1, Rst2, Rst3, SB, SignedExt, sys, W1, W2, W3, \单周期硬布线控制器_1_alu_src ,
       \单周期硬布线控制器_1_beq , \单周期硬布线控制器_1_bltz , \单周期硬布线控制器_1_bne , \单周期硬布线控制器_1_jal , \单周期硬布线控制器_1_jmp ,
       \单周期硬布线控制器_1_jr , \单周期硬布线控制器_1_memtoreg , \单周期硬布线控制器_1_regdst , \单周期硬布线控制器_1_regwrite ;
  wire [1:0] IR_now, priority_encoder_1_out;
  wire [1:1] IE_sell;
  wire [3:0] \单周期硬布线控制器_1_alu_op ;
  wire [4:0] multiplexer_4_out, multiplexer_5_out, multiplexer_6_out, multiplexer_8_out;
  wire [12:0] CNT_num;
  wire [15:0] \总周期数 ;
  wire [31:0] a0, adder_1_out, adder_2_out, AIN, bit_extender_1_out, bit_extender_2_out,
       demultiplexer_1_out0, DIN1, DOUT, EPC_q, multiplexer_1_out, multiplexer_2_out, multiplexer_7_out,
       multiplexer_9_out, multiplexer_12_out, multiplexer_13_out, multiplexer_16_out, multiplexer_17_out,
       multiplexer_19_out, multiplexer_20_out, multiplexer_22_out, nextPC, PCin, shifter_1_out, siteData, v0;
  wire [31:1] demultiplexer_1_out1;

  Clock #(.highDuration(1), .lowDuration(1)) clock_1 ();  // open: out
  Button _1 ();  // open: out
  Button _2 ();  // open: out
  Button _3 ();  // open: out
  Button \u_继续运行  (.out(Go));
  LED #(.active("true")) led_1 (.in(W1));
  LED #(.active("true")) led_2 (.in(W2));
  LED #(.active("true")) led_3 (.in(W3));
  D_Flip_Flop #(.trigger("high"), .Pre_Clr_Positions("LEGACY"), .NegatePresetClear("false"), .enable("true"), .NewFFLayout("false")) d_ff_1 (.Q(d_ff_1_q));  // open: clk, D, Qn, preset, en, reset
  or or_1 (W1, ir1_t_t, d_ff_2_q);
  or or_2 (W2, ir2_t_t, d_ff_3_q);
  or or_3 (W3, ir3_t_t, d_ff_4_q);
  Hex_Digit_Display hex_digit_display_1 (.value(LedData[31:28]));  // open: dp
  // Probe on 13'h236
  Clock #(.highDuration(1), .lowDuration(1)) clock_2 (.out(clock_2_out));
  Multiplexer #(.select(1), .width(32), .disabled("Z"), .enable("false")) multiplexer_1 (
    .in0(adder_1_out), .in1(adder_2_out), .out(multiplexer_1_out), .sel(or_11_out));
  Multiplexer #(.select(1), .width(32), .disabled("Z"), .enable("false")) multiplexer_2 (
    .in0({adder_1_out[31:28], IR[25:0], 2'b00}), .in1(v0), .out(multiplexer_2_out), .sel(\单周期硬布线控制器_1_jr ));
  D_Flip_Flop #(.trigger("rising"), .Pre_Clr_Positions("LEGACY"), .NegatePresetClear("false"), .enable("true"), .NewFFLayout("false")) d_ff_2 (
    .clk(IR1_t), .D(1'b1), .Q(d_ff_2_q), .reset(ir1_t_t));  // open: Qn, preset, en
  D_Flip_Flop #(.trigger("rising"), .Pre_Clr_Positions("LEGACY"), .NegatePresetClear("false"), .enable("true"), .NewFFLayout("false")) d_ff_3 (
    .clk(IR2_t), .D(1'b1), .Q(d_ff_3_q), .reset(ir2_t_t));  // open: Qn, preset, en
  D_Flip_Flop #(.trigger("rising"), .Pre_Clr_Positions("LEGACY"), .NegatePresetClear("false"), .enable("true"), .NewFFLayout("false")) d_ff_4 (
    .clk(IR3_t), .D(1'b1), .Q(d_ff_4_q), .reset(ir3_t_t));  // open: Qn, preset, en
  Hex_Digit_Display hex_digit_display_2 (.value(LedData[23:20]));  // open: dp
  Hex_Digit_Display hex_digit_display_3 (.value(LedData[27:24]));  // open: dp
  Comparator #(.width(13), .mode("twosComplement")) comparator_1 (
    .a(CNT_num), .b(13'h236), .eq(comparator_1_eq), .lt(comparator_1_lt));  // open: gt
  Multiplexer #(.select(1), .width(32), .disabled("Z"), .enable("false")) multiplexer_3 (
    .in0(multiplexer_1_out), .in1(multiplexer_2_out), .out(nextPC), .sel(\单周期硬布线控制器_1_jmp ));
  or or_4 (or_4_out, d_ff_2_q, ir1_t_t);
  or or_5 (or_5_out, d_ff_3_q, ir2_t_t);
  or or_6 (or_6_out, d_ff_4_q, ir3_t_t);
  Hex_Digit_Display hex_digit_display_4 (.value(LedData[19:16]));  // open: dp
  Hex_Digit_Display hex_digit_display_5 (.value(LedData[15:12]));  // open: dp
  nand nand_1 (nand_1_out, d_ff_1_q, comparator_1_eq);
  Counter #(.width(13), .max('h1fff), .ongoal("stay"), .trigger("rising"), .behavior("old")) counter_1 (
    .count(comparator_1_lt), .Q(CNT_num), .clk(clock_2_out));  // open: load, D, carry, clr, preset
  Register #(.width(32), .trigger("rising"), .Select("low")) u_PC (.D(PCin), .en(en), .Q(PC), .clk(CLK));  // open: clr
  Hex_Digit_Display hex_digit_display_6 (.value(LedData[11:8]));  // open: dp
  Hex_Digit_Display hex_digit_display_7 (.value(LedData[7:4]));  // open: dp
  // Probe on \总周期数 
  assign CLK = nand_1_out ? clock_2_out : 1'bz;  // Controlled_Buffer controlled_buffer_1
  Pull_Resistor #(.pull(1)) pull_resistor_1 (.node(CLK));
  and and_1 (and_1_out, or_4_out, ~Rst1);  // AND_Gate
  and and_2 (and_2_out, or_5_out, ~Rst2);  // AND_Gate
  and and_3 (and_3_out, or_6_out, ~Rst3);  // AND_Gate
  Hex_Digit_Display hex_digit_display_8 (.value(LedData[3:0]));  // open: dp
  Comparator #(.width(6), .mode("unsigned")) comparator_2 (
    .a(IR[31:26]), .b(6'b010000), .eq(comparator_2_eq));  // open: gt, lt
  Comparator #(.width(5), .mode("unsigned")) comparator_3 (
    .a(IR[25:21]), .b({5{1'b0}}), .eq(comparator_3_eq));  // open: gt, lt
  Comparator #(.width(5), .mode("unsigned")) comparator_4 (
    .a(IR[25:21]), .b(5'b00100), .eq(comparator_4_eq));  // open: gt, lt
  Adder #(.width(32)) adder_1 (.a(PC), .b(32'h4), .out(adder_1_out));  // open: cin, cout
  D_Flip_Flop #(.trigger("rising"), .Pre_Clr_Positions("LEGACY"), .NegatePresetClear("false"), .enable("true"), .NewFFLayout("false")) u_IR1 (
    .clk(CLK), .D(and_1_out), .Q(ir1_t_t));  // open: Qn, preset, en, reset
  D_Flip_Flop #(.trigger("rising"), .Pre_Clr_Positions("LEGACY"), .NegatePresetClear("false"), .enable("true"), .NewFFLayout("false")) u_IR2 (
    .clk(CLK), .D(and_2_out), .Q(ir2_t_t));  // open: Qn, preset, en, reset
  D_Flip_Flop #(.trigger("rising"), .Pre_Clr_Positions("LEGACY"), .NegatePresetClear("false"), .enable("true"), .NewFFLayout("false")) u_IR3 (
    .clk(CLK), .D(and_3_out), .Q(ir3_t_t));  // open: Qn, preset, en, reset
  and and_4 (MFC0, comparator_2_eq, comparator_3_eq);
  and and_5 (MTC0, comparator_2_eq, comparator_4_eq);
  Comparator #(.width(32), .mode("unsigned")) comparator_5 (.a(32'h42000018), .b(IR), .eq(ERET));  // open: gt, lt
  ROM #(.addrWidth(10), .dataWidth(32), .Select("high")) rom_1 (.addr(PC[11:2]), .data(IR));
  or or_7 (IR1_t, IR1, IRA);
  // Mips_Probe mips_probe_1: pin names not known; wires that end beside it: IR, IR
  or or_8 (IR2_t, IR2, IRB);
  Counter #(.width(16), .max('hffff), .ongoal("stay"), .trigger("rising"), .behavior("old")) \u_周期数  (
    .count(en), .Q(\总周期数 ), .clk(CLK));  // open: load, D, carry, clr, preset
  \单周期硬布线控制器  \u_单周期硬布线控制器_1  (
    .Func(IR[5:0]), .OP(IR[31:26]), .ALU_OP(\单周期硬布线控制器_1_alu_op ), .MemToReg(\单周期硬布线控制器_1_memtoreg ),
    .MemWrite(MemWrite), .ALU_SRC(\单周期硬布线控制器_1_alu_src ), .RegWrite(\单周期硬布线控制器_1_regwrite ), .SysCALL(sys),
    .SignedExt(SignedExt), .RegDst(\单周期硬布线控制器_1_regdst ), .JR(\单周期硬布线控制器_1_jr ), .JMP(\单周期硬布线控制器_1_jmp ),
    .Beq(\单周期硬布线控制器_1_beq ), .JAL(\单周期硬布线控制器_1_jal ), .Bne(\单周期硬布线控制器_1_bne ), .SB(SB),
    .BLTZ(\单周期硬布线控制器_1_bltz ));
  Multiplexer #(.select(1), .width(5), .disabled("Z"), .enable("false")) multiplexer_4 (
    .in0(IR[25:21]), .in1(5'b00010), .out(multiplexer_4_out), .sel(sys));
  Multiplexer #(.select(1), .width(5), .disabled("Z"), .enable("false")) multiplexer_5 (
    .in0(IR[20:16]), .in1(5'b00100), .out(multiplexer_5_out), .sel(sys));
  assign bit_extender_1_out = {{16{1'b0}}, IR[15:0]};  // Bit_Extender bit_extender_1
  assign bit_extender_2_out = {{16{IR[15]}}, IR[15:0]};  // Bit_Extender bit_extender_2
  or or_9 (IR3_t, IR3, IRC);
  Multiplexer #(.select(1), .width(5), .disabled("Z"), .enable("false")) multiplexer_6 (
    .in0(IR[20:16]), .in1(IR[15:11]), .out(multiplexer_6_out), .sel(\单周期硬布线控制器_1_regdst ));
  Multiplexer #(.select(1), .width(32), .disabled("Z"), .enable("false")) multiplexer_7 (
    .in0(bit_extender_1_out), .in1(bit_extender_2_out), .out(multiplexer_7_out), .sel(SignedExt));
  Decoder #(.select(2), .tristate("false"), .disabled("Z"), .enable("false")) decoder_1 (
    .out1(decoder_1_out1), .out2(decoder_1_out2), .out3(decoder_1_out3), .sel(IR_now));  // open: out0
  Multiplexer #(.select(1), .width(5), .disabled("Z"), .enable("false")) multiplexer_8 (
    .in0(multiplexer_6_out), .in1({5{1'b1}}), .out(multiplexer_8_out), .sel(\单周期硬布线控制器_1_jal ));
  Multiplexer #(.select(1), .width(32), .disabled("Z"), .enable("false")) multiplexer_9 (
    .in0(multiplexer_17_out), .in1(adder_1_out), .out(multiplexer_9_out), .sel(\单周期硬布线控制器_1_jal ));
  or or_10 (RegWrite, \单周期硬布线控制器_1_regwrite , MFC0);
  Multiplexer #(.select(1), .width(32), .disabled("Z"), .enable("false")) multiplexer_10 (
    .in0(multiplexer_9_out), .in1(siteData), .out(RDin), .sel(MFC0));
  MIPS_Regifile mips_regifile_1 (
    .Din(RDin), .Clk(CLK), .R1(v0), .R2(a0), .WE(RegWrite), .W_num(multiplexer_8_out),
    .R1_num(multiplexer_4_out), .R2_num(multiplexer_5_out));
  and and_6 (Rst1, decoder_1_out1, ERET);
  and and_7 (Rst2, decoder_1_out2, ERET);
  and and_8 (Rst3, decoder_1_out3, ERET);
  Multiplexer #(.select(2), .width(32), .disabled("Z"), .enable("false")) multiplexer_11 (
    .in0({DOUT[31:8], a0[7:0]}), .in1({DOUT[31:16], a0[7:0], DOUT[7:0]}),
    .in2({DOUT[31:24], a0[7:0], DOUT[15:0]}), .in3({a0[7:0], DOUT[23:0]}), .out(DIN1), .sel(AIN[1:0]));
  Multiplexer #(.select(1), .width(32), .disabled("Z"), .enable("false")) multiplexer_12 (
    .in0(a0), .in1(multiplexer_7_out), .out(multiplexer_12_out), .sel(\单周期硬布线控制器_1_alu_src ));
  Multiplexer #(.select(1), .width(32), .disabled("Z"), .enable("false")) multiplexer_13 (
    .in0(multiplexer_12_out), .in1({32{1'b0}}), .out(multiplexer_13_out), .sel(\单周期硬布线控制器_1_bltz ));
  Shifter #(.width(32), .shift("ll")) shifter_1 (.in(bit_extender_2_out), .\dist (5'b00010), .out(shifter_1_out));
  MIPS_ALU mips_alu_1 (
    .X(v0), .Y(multiplexer_13_out), .AluOP(\单周期硬布线控制器_1_alu_op ), .Equal(mips_alu_1_equal), .Result(AIN),
    .shamt(IR[10:6]));  // open: Result_2
  Priority_Encoder #(.select(2), .disabled("Z")) priority_encoder_1 (
    .in0(1'b0), .in1(ir1_t_t), .in2(ir2_t_t), .in3(ir3_t_t), .out(priority_encoder_1_out),
    .gs(priority_encoder_1_gs));  // open: en_out, en_in
  Comparator #(.width(32), .mode("twosComplement")) comparator_6 (
    .a(32'h1), .b(AIN), .eq(comparator_6_eq));  // open: gt, lt
  Multiplexer #(.select(1), .width(32), .disabled("Z"), .enable("false")) multiplexer_14 (
    .in0(a0), .in1(DIN1), .out(MDin), .sel(SB));
  Adder #(.width(32)) adder_2 (.a(shifter_1_out), .b(adder_1_out), .out(adder_2_out));  // open: cin, cout
  // Probe on priority_encoder_1_out
  Comparator #(.width(5), .mode("twosComplement")) comparator_7 (
    .a(IR[15:11]), .b(5'b01110), .eq(comparator_7_eq));  // open: gt, lt
  Comparator #(.width(5), .mode("twosComplement")) comparator_8 (
    .a(IR[15:11]), .b(5'b01100), .eq(comparator_8_eq));  // open: gt, lt
  Comparator #(.width(32), .mode("unsigned")) comparator_9 (.a(v0), .b(32'h32), .eq(comparator_9_eq));  // open: gt, lt
  \栈  \u_栈_1  (.INPUT(priority_encoder_1_out), .clk(CLK), .\int (INT), .eret(ERET), .out_5(IR_now));
  Register #(.width(32), .trigger("rising"), .Select("low")) register_1 (
    .D(a0), .en(sys), .Q(LedData), .clk(CLK));  // open: clr
  Multiplexer #(.select(1), .width(1), .disabled("Z"), .enable("false")) multiplexer_15 (
    .in0(1'b1), .in1(Go), .out(en), .sel(and_9_out));
  and and_9 (and_9_out, comparator_9_eq, sys);
  and and_10 (and_10_out, \单周期硬布线控制器_1_beq , mips_alu_1_equal);
  and and_11 (and_11_out, \单周期硬布线控制器_1_bne , ~mips_alu_1_equal);  // AND_Gate
  and and_12 (and_12_out, \单周期硬布线控制器_1_bltz , comparator_6_eq);
  // Probe on IR_now
  Multiplexer #(.select(2), .width(32), .disabled("Z"), .enable("false")) multiplexer_16 (
    .in1(32'h30ac), .in2(32'h3174), .in3(32'h323c), .out(multiplexer_16_out), .sel(priority_encoder_1_out));  // open: in0
  and and_13 (and_13_out, comparator_7_eq, MTC0);
  and and_14 (and_14_out, comparator_8_eq, MTC0);
  or or_11 (or_11_out, and_10_out, and_11_out, and_12_out);
  RAM #(.addrWidth(10), .dataWidth(32), .bus("separate"), .Select("high")) ram_1 (
    .addr(AIN[11:2]), .din(MDin), .data(DOUT), .str(MemWrite), .clk(CLK));  // open: sel, ld, clr
  Pull_Resistor #(.pull(0)) pull_resistor_2 (.node(pull_resistor_2_node));
  Priority_Encoder #(.select(1), .disabled("Z")) priority_encoder_2 (
    .in0(and_13_out), .in1(and_14_out), .out(priority_encoder_2_out));  // open: gs, en_out, en_in
  Multiplexer #(.select(1), .width(32), .disabled("Z"), .enable("false")) multiplexer_17 (
    .in0(AIN), .in1(DOUT), .out(multiplexer_17_out), .sel(\单周期硬布线控制器_1_memtoreg ));
  Multiplexer #(.select(2), .width(1), .disabled("Z"), .enable("false")) multiplexer_18 (
    .in0(1'b1), .in1(1'b0), .in2(IE_in), .out(multiplexer_18_out), .sel({IE_sell[1], ERET}));  // open: in3
  Decoder #(.select(1), .tristate("false"), .disabled("Z"), .enable("false")) decoder_2 (
    .out0(pull_resistor_2_node), .out1(IE_sell[1]), .sel(priority_encoder_2_out));
  Demultiplexer #(.select(1), .width(32), .tristate("false"), .disabled("Z"), .enable("false")) demultiplexer_1 (
    .out0(demultiplexer_1_out0), .out1({demultiplexer_1_out1, IE_in}), .in(a0), .sel(priority_encoder_2_out));
  Comparator #(.width(2), .mode("unsigned")) comparator_10 (
    .a(priority_encoder_1_out), .b(IR_now), .gt(comparator_10_gt));  // open: eq, lt
  Pull_Resistor #(.pull(0)) pull_resistor_3 (.node(IE_sell[1]));
  Pull_Resistor #(.pull(0)) pull_resistor_4 (.node(IE_in));
  and and_15 (and_15_out, priority_encoder_1_gs, \IE_0为开中断_qn );
  D_Flip_Flop #(.trigger("rising"), .Pre_Clr_Positions("LEGACY"), .NegatePresetClear("false"), .enable("true"), .NewFFLayout("false")) \IE_0为开中断  (
    .clk(CLK), .D(multiplexer_18_out), .Q(\IE_0为开中断_q ), .Qn(\IE_0为开中断_qn ), .en(or_12_out));  // open: preset, reset
  or or_12 (or_12_out, IE_sell[1], INT, ERET);
  Comparator #(.width(16), .mode("twosComplement")) comparator_11 (
    .a(\总周期数 ), .b(16'h7), .eq(comparator_11_eq));  // open: gt, lt
  Comparator #(.width(16), .mode("twosComplement")) comparator_12 (
    .a(\总周期数 ), .b(16'h241), .eq(comparator_12_eq));  // open: gt, lt
  Multiplexer #(.select(1), .width(32), .disabled("Z"), .enable("false")) multiplexer_19 (
    .in0(nextPC), .in1(multiplexer_16_out), .out(multiplexer_19_out), .sel(INT));
  and and_16 (INT, comparator_10_gt, and_15_out);
  Comparator #(.width(16), .mode("twosComplement")) comparator_13 (
    .a(16'h258), .b(\总周期数 ), .eq(comparator_13_eq));  // open: gt, lt
  or or_13 (or_13_out, comparator_13_eq, comparator_14_eq);
  Comparator #(.width(16), .mode("twosComplement")) comparator_14 (
    .a(\总周期数 ), .b(16'h1), .eq(comparator_14_eq));  // open: gt, lt
  Comparator #(.width(16), .mode("twosComplement")) comparator_15 (
    .a(\总周期数 ), .b(16'h4), .eq(comparator_15_eq));  // open: gt, lt
  or or_14 (or_14_out, comparator_11_eq, comparator_12_eq);
  Multiplexer #(.select(1), .width(32), .disabled("Z"), .enable("false")) multiplexer_20 (
    .in0(nextPC), .in1(demultiplexer_1_out0), .out(multiplexer_20_out), .sel(pull_resistor_2_node));
  or or_15 (or_15_out, INT, pull_resistor_2_node);
  Pull_Resistor #(.pull(0)) pull_resistor_5 (.node(IRA));
  assign IRA = or_13_out ? ~CLK : 1'bz;  // Controlled_Inverter controlled_inverter_1
  Pull_Resistor #(.pull(0)) pull_resistor_6 (.node(IRB));
  assign IRB = comparator_15_eq ? ~CLK : 1'bz;  // Controlled_Inverter controlled_inverter_2
  Pull_Resistor #(.pull(0)) pull_resistor_7 (.node(IRC));
  assign IRC = or_14_out ? ~CLK : 1'bz;  // Controlled_Inverter controlled_inverter_3
  Register #(.width(32), .trigger("rising"), .Select("low")) EPC (
    .D(multiplexer_20_out), .en(or_15_out), .Q(EPC_q), .clk(CLK));  // open: clr
  Multiplexer #(.select(1), .width(32), .disabled("Z"), .enable("false")) multiplexer_21 (
    .in0(multiplexer_19_out), .in1(EPC_q), .out(PCin), .sel(ERET));
  Comparator #(.width(5), .mode("twosComplement")) comparator_16 (
    .a(IR[15:11]), .b(5'b01110), .eq(comparator_16_eq));  // open: gt, lt
  Comparator #(.width(5), .mode("twosComplement")) comparator_17 (
    .a(IR[15:11]), .b(5'b01100), .eq(comparator_17_eq));  // open: gt, lt
  and and_17 (and_17_out, comparator_16_eq, MFC0);
  and and_18 (and_18_out, comparator_17_eq, MFC0);
  Multiplexer #(.select(1), .width(32), .disabled("Z"), .enable("false")) multiplexer_22 (
    .in0({32{1'b0}}), .in1(32'h1), .out(multiplexer_22_out), .sel(\IE_0为开中断_q ));
  Priority_Encoder #(.select(1), .disabled("Z")) priority_encoder_3 (
    .in0(and_17_out), .in1(and_18_out), .out(priority_encoder_3_out));  // open: gs, en_out, en_in
  Multiplexer #(.select(1), .width(32), .disabled("Z"), .enable("false")) multiplexer_23 (
    .in0(EPC_q), .in1(multiplexer_22_out), .out(siteData), .sel(priority_encoder_3_out));

  // Other names for the same wires on the sheet: DIN[31:0] = a0; IE_sell[0] = ERET; Rd[4:0] = IR[15:11]

  // Notes on the sheet:
  //   中断源
  //   中断等待指示
  //   总复位信号应将除ROM以外所有存储组件全部清零
  //   控制位
  //   暂停节拍，不能为0
  //   用这个时钟源需要去掉电路中的其他时钟源
  //   戳工具置1进入计数暂停模式，ctrl+k时钟自动运行到对应节拍暂停
  //   ctrl+k关闭时钟连续运行，将控制位置零，进入单步调试模式调试
  //   数码管输出
  //   数码管输出应该用寄存器锁存，否则显示数据只能一闪而过
  //   可计数暂停的时钟源
  //   Reset 
  //   Reset 
  //   Reset 
  //   指令存储器
  //   contents of rom_1 (hex, n*v repeats v):
  //   201d07d0 20100001 109fc0 139fc3 8021 2012000c 24160008 26100001 3210000f 20080008 20090001 139900
  //   2709825 132020 20020022 c 1094022 1500fff9 22100001 2018000f 2188024 108700 20080008 20090001 139902
  //   2709825 132021 20020022 c 1094022 1500fff9 108702 2c9b022 12c00001 8000c07 4020 1084027 84400
  //   3508ffff 82021 20020022 c 8000c01 afa20000 23bd0004 afa40000 23bd0004 afb00000 23bd0004 afb30000
  //   23bd0004 afb40000 23bd0004 afb50000 23bd0004 afb60000 23bd0004 40167000 afb60000 23bd0004 40806000
  //   20160001 20140003 20150001 168020 108100 2149825 132020 20020022 c 1600fffa 295a022 1680fff7
  //   20160001 40966000 23bdfffc 8fb60000 40967000 23bdfffc 8fb60000 23bdfffc 8fb50000 23bdfffc 8fb40000
  //   23bdfffc 8fb30000 23bdfffc 8fb00000 23bdfffc 8fa40000 23bdfffc 8fa20000 42000018 afa20000 23bd0004
  //   afa40000 23bd0004 afb00000 23bd0004 afb30000 23bd0004 afb40000 23bd0004 afb50000 23bd0004 afb60000
  //   23bd0004 40167000 afb60000 23bd0004 40806000 20160002 20140003 20150001 168020 108100 2149825 132020
  //   20020022 c 1600fffa 295a022 1680fff7 20160001 40966000 23bdfffc 8fb60000 40967000 23bdfffc 8fb60000
  //   23bdfffc 8fb50000 23bdfffc 8fb40000 23bdfffc 8fb30000 23bdfffc 8fb00000 23bdfffc 8fa40000 23bdfffc
  //   8fa20000 42000018 afa20000 23bd0004 afa40000 23bd0004 afb00000 23bd0004 afb30000 23bd0004 afb40000
  //   23bd0004 afb50000 23bd0004 afb60000 23bd0004 40167000 afb60000 23bd0004 40806000 20160003 20140003
  //   20150001 168020 108100 2149825 132020 20020022 c 1600fffa 295a022 1680fff7 20160001 40966000
  //   23bdfffc 8fb60000 40967000 23bdfffc 8fb60000 23bdfffc 8fb50000 23bdfffc 8fb40000 23bdfffc 8fb30000
  //   23bdfffc 8fb00000 23bdfffc 8fa40000 23bdfffc 8fa20000 42000018
  //   指令字
  //   JMP
  //   JR
  //   OP
  //   OP
  //   Func
  //   Func
  //   rs
  //   rt
  //   rd
  //   SB
  //   BLTZ
  //   Beq
  //   Bne
  //   MemToReg
  //   MemWrite
  //   AluOP
  //   AluSrcB
  //   RegWrite
  //   JAL
  //   RegDst
  //   Syscall
  //   修改清除中断的逻辑
  //   为方便自动评测，需要输出PC，IR，寄存器堆写如数据RDin
  //   RAM写使能MemWrite、RAM写入数据MDin等信号
  //   关键，引入了一个栈，用来存放发生的中断
  //   cp0 14 EPC
  //   cp0 12 IE
  //   mtc0,改变EPC的值
  //   mtc0,改变IE的值
  //   多级中断测试信号模拟器
  //   中断响应阶段，值为0，应该关中断，将IE置为1
  //   ERET时，值为1，应该开中断，将IE置为0
  //   mtc0时，值为2，将IE置为对应的值
  //   cp0 14 EPC
  //   cp0 12 IE
endmodule

module \封装正确性测试  (
);

  wire IR1, IR2, IR3, MemW, RegW;
  wire [31:0] EX_PC, ID_PC, IF_PC, IR, LED, MDin, MDinr, MEM_PC, PC, RDin, RDinr, WB_PC;

  \单周期MIPS  \u_单周期mips_1  (
    .IR1(IR1), .IR2(IR2), .IR3(IR3), .RegWrite(RegW), .MemWrite(MemW), .PC(PC), .IR(IR), .RDin(RDin),
    .MDin(MDin), .LedData(LED));
  \气泡流水线  \u_气泡流水线_1  (
    .RegWrite(RegW), .MemWrite(MemW), .IF_PC(IF_PC), .ID_PC(ID_PC), .EX_PC(EX_PC), .M_PC(MEM_PC),
    .WB_PC(WB_PC), .RDin(RDinr), .MDin(MDinr), .LedData(LED));
  \单周期MIPS_单级中断  \u_单周期mips_单级中断_1  (
    .IR2(IR1), .IR3(IR2), .IR4(IR3), .RegWrite(RegW), .MemWrite(MemW), .PC(PC), .IR(IR), .RDin(RDin),
    .MDin(MDin), .LedData(LED));  // open: IR1
  \理想流水线  \u_理想流水线_1  (
    .RegWrite(RegW), .MemWrite(MemW), .IF_PC(IF_PC), .ID_PC(ID_PC), .EX_PC(EX_PC), .M_PC(MEM_PC),
    .WB_PC(WB_PC), .RDin(RDinr), .MDin(MDinr), .LedData(LED));
  \重定向流水线  \u_重定向流水线_1  (
    .RegWrite(RegW), .MemWrite(MemW), .IF_PC(IF_PC), .ID_PC(ID_PC), .EX_PC(EX_PC), .M_PC(MEM_PC),
    .WB_PC(WB_PC), .RDin(RDinr), .MDin(MDinr), .LedData(LED));
  \单周期MIPS_多级中断  \u_单周期mips_多级中断_1  (
    .IR1(IR1), .IR2(IR2), .IR3(IR3), .RegWrite(RegW), .MemWrite(MemW), .PC(PC), .IR(IR), .RDin(RDin),
    .MDin(MDin), .LedData(LED));

  // Notes on the sheet:
  //   单周期封装测试
  //   气泡流水封装测试
  //   单周期+单级中断封装测试
  //   请检查上面封装有无位宽不匹配，引脚标签是否和连接的标签相对应，否则无法在educoder平台上正确测试
  //   理想流水封装测试
  //   重定向流水封装测试
  //   单周期+多级中断封装测试
endmodule

module IF_ID (
  input  CLR,
  input  [31:0] PC,
  input  EN,
  input  CLK,
  input  RST,
  input  [31:0] IR,
  input  [31:0] PCN,
  output [31:0] PC_2,
  output [31:0] IR_2,
  output [31:0] PCN_2
);

  wire not_1_out;
  wire [31:0] multiplexer_1_out, multiplexer_2_out, multiplexer_3_out;

  not not_1 (not_1_out, EN);
  Multiplexer #(.select(1), .width(32), .disabled("Z"), .enable("false")) multiplexer_1 (
    .in0(PC), .in1({32{1'b0}}), .out(multiplexer_1_out), .sel(CLR));
  Multiplexer #(.select(1), .width(32), .disabled("Z"), .enable("false")) multiplexer_2 (
    .in0(IR), .in1({32{1'b0}}), .out(multiplexer_2_out), .sel(CLR));
  Multiplexer #(.select(1), .width(32), .disabled("Z"), .enable("false")) multiplexer_3 (
    .in0(PCN), .in1({32{1'b0}}), .out(multiplexer_3_out), .sel(CLR));
  Register #(.width(32), .trigger("rising"), .Select("low")) register_1 (
    .D(multiplexer_1_out), .en(not_1_out), .Q(PC_2), .clk(CLK), .clr(RST));
  Register #(.width(32), .trigger("rising"), .Select("low")) register_2 (
    .D(multiplexer_2_out), .en(not_1_out), .Q(IR_2), .clk(CLK), .clr(RST));
  Register #(.width(32), .trigger("rising"), .Select("low")) register_3 (
    .D(multiplexer_3_out), .en(not_1_out), .Q(PCN_2), .clk(CLK), .clr(RST));
endmodule

module ID_EX (
  input  CLR,
  input  JMP,
  input  JR,
  input  SB,
  input  BLTZ,
  input  Beq,
  input  RegWrite,
  input  SysCall,
  input  EN,
  input  RST,
  input  Bne,
  input  MemToReg,
  input  MemWrite,
  input  AluSrcB,
  input  JAL,
  input  [3:0] in_16,
  input  CLK,
  input  [31:0] RS,
  input  [31:0] E1,
  input  [31:0] PCN,
  input  [31:0] RT,
  input  [31:0] E2,
  input  [31:0] IR,
  input  [31:0] PC,
  input  [4:0] WR,
  input  [4:0] shamt,
  input  [1:0] RsForward,
  input  [1:0] RtForward,
  output JMP_2,
  output JR_2,
  output SB_2,
  output BLTZ_2,
  output Beq_2,
  output RegWrite_2,
  output SysCall_2,
  output Bne_2,
  output MemToReg_2,
  output MemWrite_2,
  output AluSrcB_2,
  output JAL_2,
  output [3:0] AluOP,
  output [31:0] RS_2,
  output [31:0] E1_2,
  output [31:0] PCN_2,
  output [31:0] RT_2,
  output [31:0] E2_2,
  output [31:0] IR_2,
  output [31:0] PC_2,
  output [4:0] WR_2,
  output [4:0] shamt_2,
  output [1:0] RsForward_2,
  output [1:0] RtForward_2
);

  wire multiplexer_1_out, multiplexer_2_out, multiplexer_7_out, multiplexer_8_out, multiplexer_9_out,
       multiplexer_10_out, multiplexer_11_out, multiplexer_16_out, multiplexer_17_out, multiplexer_18_out,
       multiplexer_19_out, multiplexer_24_out, not_1_out;
  wire [1:0] multiplexer_6_out, multiplexer_15_out;
  wire [3:0] multiplexer_23_out;
  wire [4:0] multiplexer_14_out, multiplexer_20_out;
  wire [31:0] multiplexer_3_out, multiplexer_4_out, multiplexer_5_out, multiplexer_12_out,
       multiplexer_13_out, multiplexer_21_out, multiplexer_22_out;

  not not_1 (not_1_out, EN);
  Multiplexer #(.select(1), .width(1), .disabled("Z"), .enable("false")) multiplexer_1 (
    .in0(JMP), .in1(1'b0), .out(multiplexer_1_out), .sel(CLR));
  Register #(.width(1), .trigger("rising"), .Select("low")) register_1 (
    .D(multiplexer_1_out), .en(not_1_out), .Q(JMP_2), .clk(CLK), .clr(RST));
  Multiplexer #(.select(1), .width(1), .disabled("Z"), .enable("false")) multiplexer_2 (
    .in0(Bne), .in1(1'b0), .out(multiplexer_2_out), .sel(CLR));
  Register #(.width(1), .trigger("rising"), .Select("low")) register_2 (
    .D(multiplexer_2_out), .en(not_1_out), .Q(Bne_2), .clk(CLK), .clr(RST));
  Multiplexer #(.select(1), .width(32), .disabled("Z"), .enable("false")) multiplexer_3 (
    .in0(RS), .in1({32{1'b0}}), .out(multiplexer_3_out), .sel(CLR));
  Multiplexer #(.select(1), .width(32), .disabled("Z"), .enable("false")) multiplexer_4 (
    .in0(RT), .in1({32{1'b0}}), .out(multiplexer_4_out), .sel(CLR));
  Multiplexer #(.select(1), .width(32), .disabled("Z"), .enable("false")) multiplexer_5 (
    .in0(PC), .in1({32{1'b0}}), .out(multiplexer_5_out), .sel(CLR));
  Multiplexer #(.select(1), .width(2), .disabled("Z"), .enable("false")) multiplexer_6 (
    .in0(RsForward), .in1(2'b00), .out(multiplexer_6_out), .sel(CLR));
  Register #(.width(2), .trigger("rising"), .Select("low")) register_3 (
    .D(multiplexer_6_out), .en(not_1_out), .Q(RsForward_2), .clk(CLK), .clr(RST));
  Multiplexer #(.select(1), .width(1), .disabled("Z"), .enable("false")) multiplexer_7 (
    .in0(JR), .in1(1'b0), .out(multiplexer_7_out), .sel(CLR));
  Register #(.width(1), .trigger("rising"), .Select("low")) register_4 (
    .D(multiplexer_7_out), .en(not_1_out), .Q(JR_2), .clk(CLK), .clr(RST));
  Register #(.width(32), .trigger("rising"), .Select("low")) register_5 (
    .D(multiplexer_3_out), .en(not_1_out), .Q(RS_2), .clk(CLK), .clr(RST));
  Register #(.width(32), .trigger("rising"), .Select("low")) register_6 (
    .D(multiplexer_4_out), .en(not_1_out), .Q(RT_2), .clk(CLK), .clr(RST));
  Register #(.width(32), .trigger("rising"), .Select("low")) register_7 (
    .D(multiplexer_5_out), .en(not_1_out), .Q(PC_2), .clk(CLK), .clr(RST));
  Multiplexer #(.select(1), .width(1), .disabled("Z"), .enable("false")) multiplexer_8 (
    .in0(MemToReg), .in1(1'b0), .out(multiplexer_8_out), .sel(CLR));
  Register #(.width(1), .trigger("rising"), .Select("low")) register_8 (
    .D(multiplexer_8_out), .en(not_1_out), .Q(MemToReg_2), .clk(CLK), .clr(RST));
  Multiplexer #(.select(1), .width(1), .disabled("Z"), .enable("false")) multiplexer_9 (
    .in0(SB), .in1(1'b0), .out(multiplexer_9_out), .sel(CLR));
  Register #(.width(1), .trigger("rising"), .Select("low")) register_9 (
    .D(multiplexer_9_out), .en(not_1_out), .Q(SB_2), .clk(CLK), .clr(RST));
  Multiplexer #(.select(1), .width(1), .disabled("Z"), .enable("false")) multiplexer_10 (
    .in0(MemWrite), .in1(1'b0), .out(multiplexer_10_out), .sel(CLR));
  Register #(.width(1), .trigger("rising"), .Select("low")) register_10 (
    .D(multiplexer_11_out), .en(not_1_out), .Q(BLTZ_2), .clk(CLK), .clr(RST));
  Multiplexer #(.select(1), .width(1), .disabled("Z"), .enable("false")) multiplexer_11 (
    .in0(BLTZ), .in1(1'b0), .out(multiplexer_11_out), .sel(CLR));
  Register #(.width(1), .trigger("rising"), .Select("low")) register_11 (
    .D(multiplexer_10_out), .en(not_1_out), .Q(MemWrite_2), .clk(CLK), .clr(RST));
  Multiplexer #(.select(1), .width(32), .disabled("Z"), .enable("false")) multiplexer_12 (
    .in0(E1), .in1({32{1'b0}}), .out(multiplexer_12_out), .sel(CLR));
  Multiplexer #(.select(1), .width(32), .disabled("Z"), .enable("false")) multiplexer_13 (
    .in0(E2), .in1({32{1'b0}}), .out(multiplexer_13_out), .sel(CLR));
  Multiplexer #(.select(1), .width(5), .disabled("Z"), .enable("false")) multiplexer_14 (
    .in0(WR), .in1({5{1'b0}}), .out(multiplexer_14_out), .sel(CLR));
  Multiplexer #(.select(1), .width(2), .disabled("Z"), .enable("false")) multiplexer_15 (
    .in0(RtForward), .in1(2'b00), .out(multiplexer_15_out), .sel(CLR));
  Register #(.width(2), .trigger("rising"), .Select("low")) register_12 (
    .D(multiplexer_15_out), .en(not_1_out), .Q(RtForward_2), .clk(CLK), .clr(RST));
  Multiplexer #(.select(1), .width(1), .disabled("Z"), .enable("false")) multiplexer_16 (
    .in0(AluSrcB), .in1(1'b0), .out(multiplexer_16_out), .sel(CLR));
  Register #(.width(32), .trigger("rising"), .Select("low")) register_13 (
    .D(multiplexer_12_out), .en(not_1_out), .Q(E1_2), .clk(CLK), .clr(RST));
  Register #(.width(32), .trigger("rising"), .Select("low")) register_14 (
    .D(multiplexer_13_out), .en(not_1_out), .Q(E2_2), .clk(CLK), .clr(RST));
  Register #(.width(5), .trigger("rising"), .Select("low")) register_15 (
    .D(multiplexer_14_out), .en(not_1_out), .Q(WR_2), .clk(CLK), .clr(RST));
  Multiplexer #(.select(1), .width(1), .disabled("Z"), .enable("false")) multiplexer_17 (
    .in0(Beq), .in1(1'b0), .out(multiplexer_17_out), .sel(CLR));
  Register #(.width(1), .trigger("rising"), .Select("low")) register_16 (
    .D(multiplexer_17_out), .en(not_1_out), .Q(Beq_2), .clk(CLK), .clr(RST));
  Register #(.width(1), .trigger("rising"), .Select("low")) register_17 (
    .D(multiplexer_16_out), .en(not_1_out), .Q(AluSrcB_2), .clk(CLK), .clr(RST));
  Multiplexer #(.select(1), .width(1), .disabled("Z"), .enable("false")) multiplexer_18 (
    .in0(JAL), .in1(1'b0), .out(multiplexer_18_out), .sel(CLR));
  Multiplexer #(.select(1), .width(1), .disabled("Z"), .enable("false")) multiplexer_19 (
    .in0(RegWrite), .in1(1'b0), .out(multiplexer_19_out), .sel(CLR));
  Register #(.width(1), .trigger("rising"), .Select("low")) register_18 (
    .D(multiplexer_18_out), .en(not_1_out), .Q(JAL_2), .clk(CLK), .clr(RST));
  Multiplexer #(.select(1), .width(5), .disabled("Z"), .enable("false")) multiplexer_20 (
    .in0(shamt), .in1({5{1'b0}}), .out(multiplexer_20_out), .sel(CLR));
  Register #(.width(1), .trigger("rising"), .Select("low")) register_19 (
    .D(multiplexer_19_out), .en(not_1_out), .Q(RegWrite_2), .clk(CLK), .clr(RST));
  Multiplexer #(.select(1), .width(32), .disabled("Z"), .enable("false")) multiplexer_21 (
    .in0(PCN), .in1({32{1'b0}}), .out(multiplexer_21_out), .sel(CLR));
  Register #(.width(32), .trigger("rising"), .Select("low")) register_20 (
    .D(multiplexer_21_out), .en(not_1_out), .Q(PCN_2), .clk(CLK), .clr(RST));
  Register #(.width(32), .trigger("rising"), .Select("low")) register_21 (
    .D(multiplexer_22_out), .en(not_1_out), .Q(IR_2), .clk(CLK), .clr(RST));
  Multiplexer #(.select(1), .width(32), .disabled("Z"), .enable("false")) multiplexer_22 (
    .in0(IR), .in1({32{1'b0}}), .out(multiplexer_22_out), .sel(CLR));
  Register #(.width(5), .trigger("rising"), .Select("low")) register_22 (
    .D(multiplexer_20_out), .en(not_1_out), .Q(shamt_2), .clk(CLK), .clr(RST));
  Multiplexer #(.select(1), .width(4), .disabled("Z"), .enable("false")) multiplexer_23 (
    .in0(in_16), .in1(4'b0000), .out(multiplexer_23_out), .sel(CLR));
  Register #(.width(4), .trigger("rising"), .Select("low")) register_23 (
    .D(multiplexer_23_out), .en(not_1_out), .Q(AluOP), .clk(CLK), .clr(RST));
  Multiplexer #(.select(1), .width(1), .disabled("Z"), .enable("false")) multiplexer_24 (
    .in0(SysCall), .in1(1'b0), .out(multiplexer_24_out), .sel(CLR));
  Register #(.width(1), .trigger("rising"), .Select("low")) register_24 (
    .D(multiplexer_24_out), .en(not_1_out), .Q(SysCall_2), .clk(CLK), .clr(RST));
endmodule

module EX_MEM (
  input  SysCall,
  input  CLR,
  input  SB,
  input  CLK,
  input  EN,
  input  MemToReg,
  input  RST,
  input  MemWrite,
  input  RegWrite,
  input  JAL,
  input  [4:0] WR,
  input  [31:0] AluResult,
  input  [31:0] WriteData,
  input  [31:0] PC,
  input  [31:0] IR,
  input  [31:0] PCN,
  input  [31:0] RS,
  input  [31:0] RT,
  output SysCall_2,
  output SB_2,
  output MemToReg_2,
  output MemWrite_2,
  output RegWrite_2,
  output JAL_2,
  output [4:0] WR_2,
  output [31:0] AluResult_2,
  output [31:0] WriteData_2,
  output [31:0] PC_2,
  output [31:0] IR_2,
  output [31:0] PCN_2,
  output [31:0] RS_2,
  output [31:0] RT_2
);

  wire multiplexer_1_out, multiplexer_2_out, multiplexer_3_out, multiplexer_4_out, multiplexer_5_out,
       multiplexer_6_out, not_1_out;
  wire [4:0] multiplexer_7_out;
  wire [31:0] multiplexer_8_out, multiplexer_9_out, multiplexer_10_out, multiplexer_11_out,
       multiplexer_12_out, multiplexer_13_out, multiplexer_14_out;

  not not_1 (not_1_out, EN);
  Multiplexer #(.select(1), .width(1), .disabled("Z"), .enable("false")) multiplexer_1 (
    .in0(SysCall), .in1(1'b0), .out(multiplexer_1_out), .sel(CLR));
  Multiplexer #(.select(1), .width(1), .disabled("Z"), .enable("false")) multiplexer_2 (
    .in0(SB), .in1(1'b0), .out(multiplexer_2_out), .sel(CLR));
  Multiplexer #(.select(1), .width(1), .disabled("Z"), .enable("false")) multiplexer_3 (
    .in0(MemToReg), .in1(1'b0), .out(multiplexer_3_out), .sel(CLR));
  Multiplexer #(.select(1), .width(1), .disabled("Z"), .enable("false")) multiplexer_4 (
    .in0(MemWrite), .in1(1'b0), .out(multiplexer_4_out), .sel(CLR));
  Multiplexer #(.select(1), .width(1), .disabled("Z"), .enable("false")) multiplexer_5 (
    .in0(RegWrite), .in1(1'b0), .out(multiplexer_5_out), .sel(CLR));
  Multiplexer #(.select(1), .width(1), .disabled("Z"), .enable("false")) multiplexer_6 (
    .in0(JAL), .in1(1'b0), .out(multiplexer_6_out), .sel(CLR));
  Multiplexer #(.select(1), .width(5), .disabled("Z"), .enable("false")) multiplexer_7 (
    .in0(WR), .in1({5{1'b0}}), .out(multiplexer_7_out), .sel(CLR));
  Multiplexer #(.select(1), .width(32), .disabled("Z"), .enable("false")) multiplexer_8 (
    .in0(AluResult), .in1({32{1'b0}}), .out(multiplexer_8_out), .sel(CLR));
  Multiplexer #(.select(1), .width(32), .disabled("Z"), .enable("false")) multiplexer_9 (
    .in0(WriteData), .in1({32{1'b0}}), .out(multiplexer_9_out), .sel(CLR));
  Multiplexer #(.select(1), .width(32), .disabled("Z"), .enable("false")) multiplexer_10 (
    .in0(PC), .in1({32{1'b0}}), .out(multiplexer_10_out), .sel(CLR));
  Multiplexer #(.select(1), .width(32), .disabled("Z"), .enable("false")) multiplexer_11 (
    .in0(IR), .in1({32{1'b0}}), .out(multiplexer_11_out), .sel(CLR));
  Multiplexer #(.select(1), .width(32), .disabled("Z"), .enable("false")) multiplexer_12 (
    .in0(PCN), .in1({32{1'b0}}), .out(multiplexer_12_out), .sel(CLR));
  Multiplexer #(.select(1), .width(32), .disabled("Z"), .enable("false")) multiplexer_13 (
    .in0(RS), .in1({32{1'b0}}), .out(multiplexer_13_out), .sel(CLR));
  Multiplexer #(.select(1), .width(32), .disabled("Z"), .enable("false")) multiplexer_14 (
    .in0(RT), .in1({32{1'b0}}), .out(multiplexer_14_out), .sel(CLR));
  Register #(.width(1), .trigger("rising"), .Select("low")) register_1 (
    .D(multiplexer_1_out), .en(not_1_out), .Q(SysCall_2), .clk(CLK), .clr(RST));
  Register #(.width(1), .trigger("rising"), .Select("low")) register_2 (
    .D(multiplexer_2_out), .en(not_1_out), .Q(SB_2), .clk(CLK), .clr(RST));
  Register #(.width(1), .trigger("rising"), .Select("low")) register_3 (
    .D(multiplexer_3_out), .en(not_1_out), .Q(MemToReg_2), .clk(CLK), .clr(RST));
  Register #(.width(1), .trigger("rising"), .Select("low")) register_4 (
    .D(multiplexer_4_out), .en(not_1_out), .Q(MemWrite_2), .clk(CLK), .clr(RST));
  Register #(.width(1), .trigger("rising"), .Select("low")) register_5 (
    .D(multiplexer_5_out), .en(not_1_out), .Q(RegWrite_2), .clk(CLK), .clr(RST));
  Register #(.width(1), .trigger("rising"), .Select("low")) register_6 (
    .D(multiplexer_6_out), .en(not_1_out), .Q(JAL_2), .clk(CLK), .clr(RST));
  Register #(.width(5), .trigger("rising"), .Select("low")) register_7 (
    .D(multiplexer_7_out), .en(not_1_out), .Q(WR_2), .clk(CLK), .clr(RST));
  Register #(.width(32), .trigger("rising"), .Select("low")) register_8 (
    .D(multiplexer_8_out), .en(not_1_out), .Q(AluResult_2), .clk(CLK), .clr(RST));
  Register #(.width(32), .trigger("rising"), .Select("low")) register_9 (
    .D(multiplexer_9_out), .en(not_1_out), .Q(WriteData_2), .clk(CLK), .clr(RST));
  Register #(.width(32), .trigger("rising"), .Select("low")) register_10 (
    .D(multiplexer_10_out), .en(not_1_out), .Q(PC_2), .clk(CLK), .clr(RST));
  Register #(.width(32), .trigger("rising"), .Select("low")) register_11 (
    .D(multiplexer_11_out), .en(not_1_out), .Q(IR_2), .clk(CLK), .clr(RST));
  Register #(.width(32), .trigger("rising"), .Select("low")) register_12 (
    .D(multiplexer_12_out), .en(not_1_out), .Q(PCN_2), .clk(CLK), .clr(RST));
  Register #(.width(32), .trigger("rising"), .Select("low")) register_13 (
    .D(multiplexer_13_out), .en(not_1_out), .Q(RS_2), .clk(CLK), .clr(RST));
  Register #(.width(32), .trigger("rising"), .Select("low")) register_14 (
    .D(multiplexer_14_out), .en(not_1_out), .Q(RT_2), .clk(CLK), .clr(RST));
endmodule

module MEM_WB (
  input  CLR,
  input  RegWrite,
  input  MemToReg,
  input  SysCall,
  input  EN,
  input  CLK,
  input  JAL,
  input  in_8,
  input  [31:0] AluResult,
  input  [31:0] Dout,
  input  [4:0] WR,
  input  [31:0] PC,
  input  [31:0] IR,
  input  [31:0] PCN,
  input  [31:0] RS,
  input  [31:0] RT,
  output RegWrite_2,
  output MemToReg_2,
  output SysCall_2,
  output JAL_2,
  output [31:0] AluResult_2,
  output [31:0] Dout_2,
  output [4:0] WR_2,
  output [31:0] PC_2,
  output [31:0] IR_2,
  output [31:0] PCN_2,
  output [31:0] RS_2,
  output [31:0] RT_2
);

  wire multiplexer_1_out, multiplexer_2_out, multiplexer_11_out, multiplexer_12_out, not_1_out;
  wire [4:0] multiplexer_3_out;
  wire [31:0] multiplexer_4_out, multiplexer_5_out, multiplexer_6_out, multiplexer_7_out, multiplexer_8_out,
       multiplexer_9_out, multiplexer_10_out;

  not not_1 (not_1_out, EN);
  Multiplexer #(.select(1), .width(1), .disabled("Z"), .enable("false")) multiplexer_1 (
    .in0(RegWrite), .in1(1'b0), .out(multiplexer_1_out), .sel(CLR));
  Multiplexer #(.select(1), .width(1), .disabled("Z"), .enable("false")) multiplexer_2 (
    .in0(JAL), .in1(1'b0), .out(multiplexer_2_out), .sel(CLR));
  Multiplexer #(.select(1), .width(5), .disabled("Z"), .enable("false")) multiplexer_3 (
    .in0(WR), .in1({5{1'b0}}), .out(multiplexer_3_out), .sel(CLR));
  Register #(.width(1), .trigger("rising"), .Select("low")) register_1 (
    .D(multiplexer_1_out), .en(not_1_out), .Q(RegWrite_2), .clk(CLK), .clr(in_8));
  Register #(.width(1), .trigger("rising"), .Select("low")) register_2 (
    .D(multiplexer_2_out), .en(not_1_out), .Q(JAL_2), .clk(CLK), .clr(in_8));
  Multiplexer #(.select(1), .width(32), .disabled("Z"), .enable("false")) multiplexer_4 (
    .in0(AluResult), .in1({32{1'b0}}), .out(multiplexer_4_out), .sel(CLR));
  Register #(.width(32), .trigger("rising"), .Select("low")) register_3 (
    .D(multiplexer_4_out), .en(not_1_out), .Q(AluResult_2), .clk(CLK), .clr(in_8));
  Multiplexer #(.select(1), .width(32), .disabled("Z"), .enable("false")) multiplexer_5 (
    .in0(Dout), .in1({32{1'b0}}), .out(multiplexer_5_out), .sel(CLR));
  Register #(.width(32), .trigger("rising"), .Select("low")) register_4 (
    .D(multiplexer_5_out), .en(not_1_out), .Q(Dout_2), .clk(CLK), .clr(in_8));
  Register #(.width(5), .trigger("rising"), .Select("low")) register_5 (
    .D(multiplexer_3_out), .en(not_1_out), .Q(WR_2), .clk(CLK), .clr(in_8));
  Register #(.width(32), .trigger("rising"), .Select("low")) register_6 (
    .D(multiplexer_6_out), .en(not_1_out), .Q(PC_2), .clk(CLK), .clr(in_8));
  Multiplexer #(.select(1), .width(32), .disabled("Z"), .enable("false")) multiplexer_6 (
    .in0(PC), .in1({32{1'b0}}), .out(multiplexer_6_out), .sel(CLR));
  Multiplexer #(.select(1), .width(32), .disabled("Z"), .enable("false")) multiplexer_7 (
    .in0(IR), .in1({32{1'b0}}), .out(multiplexer_7_out), .sel(CLR));
  Register #(.width(32), .trigger("rising"), .Select("low")) register_7 (
    .D(multiplexer_7_out), .en(not_1_out), .Q(IR_2), .clk(CLK), .clr(in_8));
  Multiplexer #(.select(1), .width(32), .disabled("Z"), .enable("false")) multiplexer_8 (
    .in0(PCN), .in1({32{1'b0}}), .out(multiplexer_8_out), .sel(CLR));
  Register #(.width(32), .trigger("rising"), .Select("low")) register_8 (
    .D(multiplexer_8_out), .en(not_1_out), .Q(PCN_2), .clk(CLK), .clr(in_8));
  Register #(.width(32), .trigger("rising"), .Select("low")) register_9 (
    .D(multiplexer_9_out), .en(not_1_out), .Q(RS_2), .clk(CLK), .clr(in_8));
  Multiplexer #(.select(1), .width(32), .disabled("Z"), .enable("false")) multiplexer_9 (
    .in0(RS), .in1({32{1'b0}}), .out(multiplexer_9_out), .sel(CLR));
  Register #(.width(32), .trigger("rising"), .Select("low")) register_10 (
    .D(multiplexer_10_out), .en(not_1_out), .Q(RT_2), .clk(CLK), .clr(in_8));
  Multiplexer #(.select(1), .width(32), .disabled("Z"), .enable("false")) multiplexer_10 (
    .in0(RT), .in1({32{1'b0}}), .out(multiplexer_10_out), .sel(CLR));
  Multiplexer #(.select(1), .width(1), .disabled("Z"), .enable("false")) multiplexer_11 (
    .in0(MemToReg), .in1(1'b0), .out(multiplexer_11_out), .sel(CLR));
  Register #(.width(1), .trigger("rising"), .Select("low")) register_11 (
    .D(multiplexer_11_out), .en(not_1_out), .Q(MemToReg_2), .clk(CLK), .clr(in_8));
  Multiplexer #(.select(1), .width(1), .disabled("Z"), .enable("false")) multiplexer_12 (
    .in0(SysCall), .in1(1'b0), .out(multiplexer_12_out), .sel(CLR));
  Register #(.width(1), .trigger("rising"), .Select("low")) register_12 (
    .D(multiplexer_12_out), .en(not_1_out), .Q(SysCall_2), .clk(CLK), .clr(in_8));
endmodule

// 相关处理逻辑
module \气泡流水线处理逻辑  (
  input  [4:0] rt,
  input  [4:0] rs,
  input  MEM_RegWrite,
  input  EX_RegWrite,
  input  [4:0] MEM_WR,
  input  [4:0] EX_WR,
  input  [31:0] Instr,
  input  BranchTaken,
  output Flush,
  output Stall
);

  wire and_2_out, and_3_out, and_4_out, and_5_out, comparator_1_eq, comparator_2_eq, comparator_3_eq,
       comparator_4_eq, comparator_5_eq, comparator_6_eq, comparator_7_eq, comparator_8_eq, DataHazzard,
       not_1_out, not_2_out, not_3_out, not_4_out, RsUsed, RtUsed;

  \寄存器判断  \u_寄存器判断_1  (
    .OP0(Instr[26]), .OP1(Instr[27]), .OP2(Instr[28]), .OP3(Instr[29]), .OP4(Instr[30]), .OP5(Instr[31]),
    .F0(Instr[0]), .F1(Instr[1]), .F2(Instr[2]), .F3(Instr[3]), .F4(Instr[4]), .F5(Instr[5]), .RS(RsUsed),
    .RT(RtUsed));
  or or_1 (Flush, BranchTaken, DataHazzard);
  and and_1 (Stall, ~BranchTaken, DataHazzard);  // AND_Gate
  Comparator #(.width(5), .mode("unsigned")) comparator_1 (
    .a(rs), .b({5{1'b0}}), .eq(comparator_1_eq));  // open: gt, lt
  Comparator #(.width(5), .mode("unsigned")) comparator_2 (.a(rs), .b(EX_WR), .eq(comparator_2_eq));  // open: gt, lt
  Comparator #(.width(5), .mode("unsigned")) comparator_3 (
    .a(rs), .b({5{1'b0}}), .eq(comparator_3_eq));  // open: gt, lt
  Comparator #(.width(5), .mode("unsigned")) comparator_4 (.a(rs), .b(MEM_WR), .eq(comparator_4_eq));  // open: gt, lt
  Comparator #(.width(5), .mode("unsigned")) comparator_5 (
    .a(rt), .b({5{1'b0}}), .eq(comparator_5_eq));  // open: gt, lt
  Comparator #(.width(5), .mode("unsigned")) comparator_6 (.a(rt), .b(EX_WR), .eq(comparator_6_eq));  // open: gt, lt
  Comparator #(.width(5), .mode("unsigned")) comparator_7 (
    .a(rt), .b({5{1'b0}}), .eq(comparator_7_eq));  // open: gt, lt
  Comparator #(.width(5), .mode("unsigned")) comparator_8 (.a(rt), .b(MEM_WR), .eq(comparator_8_eq));  // open: gt, lt
  not not_1 (not_1_out, comparator_1_eq);
  not not_2 (not_2_out, comparator_3_eq);
  not not_3 (not_3_out, comparator_5_eq);
  not not_4 (not_4_out, comparator_7_eq);
  and and_2 (and_2_out, RsUsed, EX_RegWrite, not_1_out, comparator_2_eq);
  and and_3 (and_3_out, RsUsed, MEM_RegWrite, not_2_out, comparator_4_eq);
  and and_4 (and_4_out, RtUsed, EX_RegWrite, not_3_out, comparator_6_eq);
  and and_5 (and_5_out, RtUsed, MEM_RegWrite, not_4_out, comparator_8_eq);
  or or_2 (DataHazzard, and_2_out, and_3_out, and_4_out, and_5_out);

  // Other names for the same wires on the sheet: Func[5:0] = Instr[5:0]; OP[5:0] = Instr[31:26]
endmodule

// 相关处理逻辑(重定向)
module \重定向流水线处理逻辑  (
  input  [31:0] Instr,
  input  MEM_RegWrite,
  input  EX_RegWrite,
  input  [4:0] MEM_WR,
  input  [4:0] EX_WR,
  input  [4:0] rt,
  input  [4:0] rs,
  input  EX_MemToReg,
  input  BranchTaken,
  output LoadUse,
  output [1:0] RsForward,
  output Flush,
  output Stall,
  output [1:0] RtForward
);

  wire and_2_out, and_3_out, and_4_out, and_5_out, and_6_out, and_7_out, comparator_1_eq, comparator_2_eq,
       comparator_3_eq, comparator_4_eq, comparator_5_eq, comparator_6_eq, comparator_7_eq, comparator_8_eq,
       comparator_9_eq, comparator_10_eq, comparator_11_eq, comparator_12_eq, not_1_out, not_2_out,
       not_3_out, not_4_out, not_5_out, not_6_out, RsUsed, RtUsed;
  wire [1:0] multiplexer_2_out, multiplexer_4_out;

  \寄存器判断  \u_寄存器判断_1  (
    .OP0(Instr[26]), .OP1(Instr[27]), .OP2(Instr[28]), .OP3(Instr[29]), .OP4(Instr[30]), .OP5(Instr[31]),
    .F0(Instr[0]), .F1(Instr[1]), .F2(Instr[2]), .F3(Instr[3]), .F4(Instr[4]), .F5(Instr[5]), .RS(RsUsed),
    .RT(RtUsed));
  or or_1 (Flush, LoadUse, BranchTaken);
  and and_1 (Stall, ~BranchTaken, LoadUse);  // AND_Gate
  Comparator #(.width(5), .mode("unsigned")) comparator_1 (
    .a(rs), .b({5{1'b0}}), .eq(comparator_1_eq));  // open: gt, lt
  Comparator #(.width(5), .mode("unsigned")) comparator_2 (.a(rs), .b(EX_WR), .eq(comparator_2_eq));  // open: gt, lt
  Comparator #(.width(5), .mode("unsigned")) comparator_3 (
    .a(rt), .b({5{1'b0}}), .eq(comparator_3_eq));  // open: gt, lt
  Comparator #(.width(5), .mode("unsigned")) comparator_4 (.a(rt), .b(EX_WR), .eq(comparator_4_eq));  // open: gt, lt
  Comparator #(.width(5), .mode("unsigned")) comparator_5 (
    .a(rs), .b({5{1'b0}}), .eq(comparator_5_eq));  // open: gt, lt
  Comparator #(.width(5), .mode("unsigned")) comparator_6 (.a(rs), .b(EX_WR), .eq(comparator_6_eq));  // open: gt, lt
  Comparator #(.width(5), .mode("unsigned")) comparator_7 (
    .a(rs), .b({5{1'b0}}), .eq(comparator_7_eq));  // open: gt, lt
  Comparator #(.width(5), .mode("unsigned")) comparator_8 (.a(rs), .b(MEM_WR), .eq(comparator_8_eq));  // open: gt, lt
  Comparator #(.width(5), .mode("unsigned")) comparator_9 (
    .a(rt), .b({5{1'b0}}), .eq(comparator_9_eq));  // open: gt, lt
  Comparator #(.width(5), .mode("unsigned")) comparator_10 (.a(rt), .b(EX_WR), .eq(comparator_10_eq));  // open: gt, lt
  Comparator #(.width(5), .mode("unsigned")) comparator_11 (
    .a(rt), .b({5{1'b0}}), .eq(comparator_11_eq));  // open: gt, lt
  Comparator #(.width(5), .mode("unsigned")) comparator_12 (.a(rt), .b(MEM_WR), .eq(comparator_12_eq));  // open: gt, lt
  not not_1 (not_1_out, comparator_1_eq);
  not not_2 (not_2_out, comparator_3_eq);
  not not_3 (not_3_out, comparator_5_eq);
  not not_4 (not_4_out, comparator_7_eq);
  not not_5 (not_5_out, comparator_9_eq);
  not not_6 (not_6_out, comparator_11_eq);
  and and_2 (and_2_out, RsUsed, not_1_out, EX_MemToReg, comparator_2_eq);
  and and_3 (and_3_out, RtUsed, not_2_out, EX_MemToReg, comparator_4_eq);
  and and_4 (and_4_out, RsUsed, not_3_out, EX_RegWrite, comparator_6_eq);
  and and_5 (and_5_out, RsUsed, not_4_out, MEM_RegWrite, comparator_8_eq);
  and and_6 (and_6_out, RtUsed, not_5_out, EX_RegWrite, comparator_10_eq);
  and and_7 (and_7_out, RtUsed, not_6_out, MEM_RegWrite, comparator_12_eq);
  or or_2 (LoadUse, and_2_out, and_3_out);
  Multiplexer #(.select(1), .width(2), .disabled("Z"), .enable("false")) multiplexer_1 (
    .in0(multiplexer_2_out), .in1(2'b10), .out(RsForward), .sel(and_4_out));
  Multiplexer #(.select(1), .width(2), .disabled("Z"), .enable("false")) multiplexer_2 (
    .in0(2'b00), .in1(2'b01), .out(multiplexer_2_out), .sel(and_5_out));
  Multiplexer #(.select(1), .width(2), .disabled("Z"), .enable("false")) multiplexer_3 (
    .in0(multiplexer_4_out), .in1(2'b10), .out(RtForward), .sel(and_6_out));
  Multiplexer #(.select(1), .width(2), .disabled("Z"), .enable("false")) multiplexer_4 (
    .in0(2'b00), .in1(2'b01), .out(multiplexer_4_out), .sel(and_7_out));

  // Other names for the same wires on the sheet: EX_MemRead = EX_MemToReg; Func[5:0] = Instr[5:0];
  //   OP[5:0] = Instr[31:26]
endmodule

module \寄存器判断  (
  input  OP0,
  input  OP1,
  input  OP2,
  input  OP3,
  input  OP4,
  input  OP5,
  input  F0,
  input  F1,
  input  F2,
  input  F3,
  input  F4,
  input  F5,
  output RS,
  output RT
);

  wire and_1_out, and_2_out, and_3_out, and_4_out, and_5_out, and_6_out, and_7_out, and_8_out, and_9_out,
       and_10_out, and_11_out, and_12_out, and_13_out, and_14_out, and_15_out, and_16_out, and_17_out,
       and_18_out, and_19_out, and_20_out, and_21_out, and_22_out, and_23_out, and_24_out, and_25_out,
       and_26_out, and_27_out, and_28_out, and_29_out, and_30_out, and_31_out, and_32_out, and_33_out,
       and_34_out, and_35_out, and_36_out, and_37_out, and_38_out, and_39_out, and_40_out, not_1_out,
       not_2_out, not_3_out, not_4_out, not_5_out, not_6_out, not_7_out, not_8_out, not_9_out, not_10_out,
       not_11_out, not_12_out, not_13_out, not_14_out, not_15_out, not_16_out, not_17_out, not_18_out,
       not_19_out, not_20_out, not_21_out, not_22_out, not_23_out, not_24_out, not_25_out, not_26_out,
       not_27_out, not_28_out, not_29_out, not_30_out, not_31_out, not_32_out, not_33_out, not_34_out,
       not_35_out, not_36_out, not_37_out, not_38_out, not_39_out, not_40_out, not_41_out, not_42_out,
       not_43_out, not_44_out, not_45_out, not_46_out, not_47_out, not_48_out, not_49_out, not_50_out,
       not_51_out, not_52_out, not_53_out, not_54_out, not_55_out, not_56_out, not_57_out, not_58_out,
       not_59_out, not_60_out, not_61_out, not_62_out, not_63_out, not_64_out, not_65_out, not_66_out,
       not_67_out, not_68_out, not_69_out, not_70_out, not_71_out, not_72_out, not_73_out, not_74_out,
       not_75_out, not_76_out, not_77_out, not_78_out, not_79_out, not_80_out, not_81_out, not_82_out,
       not_83_out, not_84_out, not_85_out, not_86_out, not_87_out, not_88_out, not_89_out, not_90_out,
       not_91_out, not_92_out, not_93_out, not_94_out, not_95_out, not_96_out, not_97_out, not_98_out,
       not_99_out, not_100_out, not_101_out, not_102_out, not_103_out, not_104_out, not_105_out, not_106_out,
       not_107_out, not_108_out, not_109_out, not_110_out, not_111_out, not_112_out, not_113_out,
       not_114_out, not_115_out, not_116_out, not_117_out, not_118_out, not_119_out, not_120_out,
       not_121_out, not_122_out, not_123_out, not_124_out, not_125_out, not_126_out, not_127_out,
       not_128_out, not_129_out, not_130_out, not_131_out, not_132_out, not_133_out, not_134_out,
       not_135_out, not_136_out, not_137_out, not_138_out, not_139_out, not_140_out, not_141_out,
       not_142_out, not_143_out, not_144_out, not_145_out, not_146_out, not_147_out, not_148_out,
       not_149_out, not_150_out, not_151_out, not_152_out, not_153_out, not_154_out, not_155_out,
       not_156_out, not_157_out, not_158_out, not_159_out, not_160_out, not_161_out, not_162_out,
       not_163_out, not_164_out, not_165_out, not_166_out, not_167_out, not_168_out, not_169_out,
       not_170_out, not_171_out, not_172_out, not_173_out, not_174_out, not_175_out, not_176_out,
       not_177_out, not_178_out, not_179_out, not_180_out, not_181_out, not_182_out, not_183_out,
       not_184_out, not_185_out, not_186_out, not_187_out, not_188_out, not_189_out, not_190_out,
       not_191_out, not_192_out, not_193_out, not_194_out, not_195_out, not_196_out, not_197_out,
       not_198_out, not_199_out, not_200_out, not_201_out, not_202_out, not_203_out, not_204_out,
       not_205_out, not_206_out, not_207_out, not_208_out, not_209_out, not_210_out, not_211_out,
       not_212_out, not_213_out, not_214_out, not_215_out, not_216_out, not_217_out, not_218_out,
       not_219_out, not_220_out, not_221_out, not_222_out, not_223_out, not_224_out, not_225_out,
       not_226_out, not_227_out, not_228_out, not_229_out, not_230_out, not_231_out, not_232_out,
       not_233_out, not_234_out, not_235_out, not_236_out, not_237_out, not_238_out, not_239_out,
       not_240_out, not_241_out, not_242_out, not_243_out, not_244_out, not_245_out, not_246_out,
       not_247_out, not_248_out, not_249_out, not_250_out, not_251_out, not_252_out, not_253_out,
       not_254_out, not_255_out, not_256_out, not_257_out, not_258_out, not_259_out, not_260_out,
       not_261_out, not_262_out, not_263_out, not_264_out, not_265_out, not_266_out, not_267_out,
       not_268_out, not_269_out, not_270_out, not_271_out, not_272_out, not_273_out, not_274_out,
       not_275_out, not_276_out, not_277_out, not_278_out, not_279_out, not_280_out, not_281_out,
       not_282_out, not_283_out, not_284_out, not_285_out, not_286_out, not_287_out, not_288_out,
       not_289_out, not_290_out, not_291_out, not_292_out, not_293_out;

  not not_1 (not_1_out, OP5);
  not not_2 (not_2_out, OP4);
  not not_3 (not_3_out, OP3);
  not not_4 (not_4_out, OP2);
  not not_5 (not_5_out, OP1);
  not not_6 (not_6_out, OP0);
  not not_7 (not_7_out, F4);
  not not_8 (not_8_out, F3);
  not not_9 (not_9_out, F2);
  not not_10 (not_10_out, F1);
  not not_11 (not_11_out, F0);
  not not_12 (not_12_out, OP5);
  not not_13 (not_13_out, OP4);
  not not_14 (not_14_out, OP3);
  not not_15 (not_15_out, OP2);
  not not_16 (not_16_out, OP1);
  not not_17 (not_17_out, OP0);
  not not_18 (not_18_out, F4);
  not not_19 (not_19_out, F3);
  not not_20 (not_20_out, F2);
  not not_21 (not_21_out, F1);
  not not_22 (not_22_out, OP5);
  not not_23 (not_23_out, OP4);
  not not_24 (not_24_out, OP3);
  not not_25 (not_25_out, OP2);
  not not_26 (not_26_out, OP1);
  not not_27 (not_27_out, OP0);
  not not_28 (not_28_out, F4);
  not not_29 (not_29_out, F3);
  not not_30 (not_30_out, F2);
  not not_31 (not_31_out, F0);
  not not_32 (not_32_out, OP5);
  not not_33 (not_33_out, OP4);
  not not_34 (not_34_out, OP3);
  not not_35 (not_35_out, OP2);
  not not_36 (not_36_out, OP1);
  not not_37 (not_37_out, OP0);
  not not_38 (not_38_out, F4);
  not not_39 (not_39_out, F3);
  not not_40 (not_40_out, F1);
  not not_41 (not_41_out, F0);
  not not_42 (not_42_out, OP5);
  not not_43 (not_43_out, OP4);
  not not_44 (not_44_out, OP3);
  not not_45 (not_45_out, OP2);
  not not_46 (not_46_out, OP1);
  not not_47 (not_47_out, OP0);
  not not_48 (not_48_out, F4);
  not not_49 (not_49_out, F3);
  not not_50 (not_50_out, F1);
  not not_51 (not_51_out, OP5);
  not not_52 (not_52_out, OP4);
  not not_53 (not_53_out, OP3);
  not not_54 (not_54_out, OP2);
  not not_55 (not_55_out, OP1);
  not not_56 (not_56_out, OP0);
  not not_57 (not_57_out, F4);
  not not_58 (not_58_out, F3);
  not not_59 (not_59_out, OP5);
  not not_60 (not_60_out, OP4);
  not not_61 (not_61_out, OP3);
  not not_62 (not_62_out, OP2);
  not not_63 (not_63_out, OP1);
  not not_64 (not_64_out, OP0);
  not not_65 (not_65_out, F4);
  not not_66 (not_66_out, F2);
  not not_67 (not_67_out, F0);
  not not_68 (not_68_out, OP5);
  not not_69 (not_69_out, OP4);
  not not_70 (not_70_out, OP3);
  not not_71 (not_71_out, OP2);
  not not_72 (not_72_out, OP1);
  not not_73 (not_73_out, OP0);
  not not_74 (not_74_out, F4);
  not not_75 (not_75_out, F2);
  not not_76 (not_76_out, OP5);
  not not_77 (not_77_out, OP4);
  not not_78 (not_78_out, OP3);
  not not_79 (not_79_out, OP2);
  not not_80 (not_80_out, OP1);
  not not_81 (not_81_out, OP0);
  not not_82 (not_82_out, F5);
  not not_83 (not_83_out, F4);
  not not_84 (not_84_out, F2);
  not not_85 (not_85_out, F1);
  not not_86 (not_86_out, F0);
  not not_87 (not_87_out, OP5);
  not not_88 (not_88_out, OP4);
  not not_89 (not_89_out, OP3);
  not not_90 (not_90_out, OP2);
  not not_91 (not_91_out, OP1);
  not not_92 (not_92_out, OP0);
  not not_93 (not_93_out, F5);
  not not_94 (not_94_out, F4);
  not not_95 (not_95_out, F1);
  not not_96 (not_96_out, F0);
  not not_97 (not_97_out, OP5);
  not not_98 (not_98_out, OP4);
  not not_99 (not_99_out, OP3);
  not not_100 (not_100_out, OP1);
  not not_101 (not_101_out, OP0);
  not not_102 (not_102_out, OP5);
  not not_103 (not_103_out, OP4);
  not not_104 (not_104_out, OP3);
  not not_105 (not_105_out, OP1);
  not not_106 (not_106_out, OP5);
  not not_107 (not_107_out, OP4);
  not not_108 (not_108_out, OP2);
  not not_109 (not_109_out, OP1);
  not not_110 (not_110_out, OP0);
  not not_111 (not_111_out, OP5);
  not not_112 (not_112_out, OP4);
  not not_113 (not_113_out, OP1);
  not not_114 (not_114_out, OP0);
  not not_115 (not_115_out, OP5);
  not not_116 (not_116_out, OP4);
  not not_117 (not_117_out, OP2);
  not not_118 (not_118_out, OP1);
  not not_119 (not_119_out, OP5);
  not not_120 (not_120_out, OP4);
  not not_121 (not_121_out, OP2);
  not not_122 (not_122_out, OP0);
  not not_123 (not_123_out, OP5);
  not not_124 (not_124_out, OP4);
  not not_125 (not_125_out, OP1);
  not not_126 (not_126_out, OP4);
  not not_127 (not_127_out, OP3);
  not not_128 (not_128_out, OP2);
  not not_129 (not_129_out, OP4);
  not not_130 (not_130_out, OP2);
  not not_131 (not_131_out, OP5);
  not not_132 (not_132_out, OP4);
  not not_133 (not_133_out, OP3);
  not not_134 (not_134_out, OP2);
  not not_135 (not_135_out, OP1);
  not not_136 (not_136_out, OP0);
  not not_137 (not_137_out, F4);
  not not_138 (not_138_out, F3);
  not not_139 (not_139_out, F0);
  not not_140 (not_140_out, OP5);
  not not_141 (not_141_out, OP4);
  not not_142 (not_142_out, OP2);
  not not_143 (not_143_out, OP4);
  not not_144 (not_144_out, OP2);
  not not_145 (not_145_out, OP1);
  not not_146 (not_146_out, OP0);
  not not_147 (not_147_out, OP5);
  not not_148 (not_148_out, OP4);
  not not_149 (not_149_out, OP3);
  not not_150 (not_150_out, OP2);
  not not_151 (not_151_out, OP1);
  not not_152 (not_152_out, OP5);
  not not_153 (not_153_out, OP4);
  not not_154 (not_154_out, OP3);
  not not_155 (not_155_out, OP2);
  not not_156 (not_156_out, OP1);
  not not_157 (not_157_out, OP0);
  not not_158 (not_158_out, F5);
  not not_159 (not_159_out, F4);
  not not_160 (not_160_out, F3);
  not not_161 (not_161_out, F2);
  not not_162 (not_162_out, F1);
  not not_163 (not_163_out, F0);
  not not_164 (not_164_out, OP5);
  not not_165 (not_165_out, OP4);
  not not_166 (not_166_out, OP3);
  not not_167 (not_167_out, OP2);
  not not_168 (not_168_out, OP1);
  not not_169 (not_169_out, OP0);
  not not_170 (not_170_out, F5);
  not not_171 (not_171_out, F4);
  not not_172 (not_172_out, F3);
  not not_173 (not_173_out, F2);
  not not_174 (not_174_out, OP5);
  not not_175 (not_175_out, OP4);
  not not_176 (not_176_out, OP3);
  not not_177 (not_177_out, OP2);
  not not_178 (not_178_out, OP1);
  not not_179 (not_179_out, OP0);
  not not_180 (not_180_out, F5);
  not not_181 (not_181_out, F4);
  not not_182 (not_182_out, F3);
  not not_183 (not_183_out, F2);
  not not_184 (not_184_out, F0);
  not not_185 (not_185_out, OP5);
  not not_186 (not_186_out, OP4);
  not not_187 (not_187_out, OP3);
  not not_188 (not_188_out, OP2);
  not not_189 (not_189_out, OP1);
  not not_190 (not_190_out, OP0);
  not not_191 (not_191_out, F4);
  not not_192 (not_192_out, F3);
  not not_193 (not_193_out, F2);
  not not_194 (not_194_out, F1);
  not not_195 (not_195_out, F0);
  not not_196 (not_196_out, OP5);
  not not_197 (not_197_out, OP4);
  not not_198 (not_198_out, OP3);
  not not_199 (not_199_out, OP2);
  not not_200 (not_200_out, OP1);
  not not_201 (not_201_out, OP0);
  not not_202 (not_202_out, F4);
  not not_203 (not_203_out, F3);
  not not_204 (not_204_out, F2);
  not not_205 (not_205_out, F1);
  not not_206 (not_206_out, OP5);
  not not_207 (not_207_out, OP4);
  not not_208 (not_208_out, OP3);
  not not_209 (not_209_out, OP2);
  not not_210 (not_210_out, OP1);
  not not_211 (not_211_out, OP0);
  not not_212 (not_212_out, F4);
  not not_213 (not_213_out, F3);
  not not_214 (not_214_out, F2);
  not not_215 (not_215_out, F0);
  not not_216 (not_216_out, OP5);
  not not_217 (not_217_out, OP4);
  not not_218 (not_218_out, OP3);
  not not_219 (not_219_out, OP2);
  not not_220 (not_220_out, OP1);
  not not_221 (not_221_out, OP0);
  not not_222 (not_222_out, F4);
  not not_223 (not_223_out, F3);
  not not_224 (not_224_out, F1);
  not not_225 (not_225_out, F0);
  not not_226 (not_226_out, OP5);
  not not_227 (not_227_out, OP4);
  not not_228 (not_228_out, OP3);
  not not_229 (not_229_out, OP2);
  not not_230 (not_230_out, OP1);
  not not_231 (not_231_out, OP0);
  not not_232 (not_232_out, F4);
  not not_233 (not_233_out, F3);
  not not_234 (not_234_out, F1);
  not not_235 (not_235_out, OP5);
  not not_236 (not_236_out, OP4);
  not not_237 (not_237_out, OP3);
  not not_238 (not_238_out, OP2);
  not not_239 (not_239_out, OP1);
  not not_240 (not_240_out, OP0);
  not not_241 (not_241_out, F4);
  not not_242 (not_242_out, F3);
  not not_243 (not_243_out, OP5);
  not not_244 (not_244_out, OP4);
  not not_245 (not_245_out, OP3);
  not not_246 (not_246_out, OP2);
  not not_247 (not_247_out, OP1);
  not not_248 (not_248_out, OP0);
  not not_249 (not_249_out, F4);
  not not_250 (not_250_out, F2);
  not not_251 (not_251_out, F0);
  not not_252 (not_252_out, OP5);
  not not_253 (not_253_out, OP4);
  not not_254 (not_254_out, OP3);
  not not_255 (not_255_out, OP2);
  not not_256 (not_256_out, OP1);
  not not_257 (not_257_out, OP0);
  not not_258 (not_258_out, F4);
  not not_259 (not_259_out, F2);
  not not_260 (not_260_out, OP5);
  not not_261 (not_261_out, OP4);
  not not_262 (not_262_out, OP3);
  not not_263 (not_263_out, OP2);
  not not_264 (not_264_out, OP1);
  not not_265 (not_265_out, OP0);
  not not_266 (not_266_out, F5);
  not not_267 (not_267_out, F4);
  not not_268 (not_268_out, F1);
  not not_269 (not_269_out, F0);
  not not_270 (not_270_out, OP5);
  not not_271 (not_271_out, OP4);
  not not_272 (not_272_out, OP3);
  not not_273 (not_273_out, OP1);
  not not_274 (not_274_out, OP0);
  not not_275 (not_275_out, OP5);
  not not_276 (not_276_out, OP4);
  not not_277 (not_277_out, OP3);
  not not_278 (not_278_out, OP1);
  not not_279 (not_279_out, OP4);
  not not_280 (not_280_out, OP2);
  not not_281 (not_281_out, OP5);
  not not_282 (not_282_out, OP4);
  not not_283 (not_283_out, OP3);
  not not_284 (not_284_out, OP2);
  not not_285 (not_285_out, OP1);
  not not_286 (not_286_out, OP0);
  not not_287 (not_287_out, F4);
  not not_288 (not_288_out, F3);
  not not_289 (not_289_out, F0);
  not not_290 (not_290_out, OP4);
  not not_291 (not_291_out, OP2);
  not not_292 (not_292_out, OP1);
  not not_293 (not_293_out, OP0);
  and and_1 (and_1_out, not_1_out, not_2_out, not_3_out, not_4_out, not_5_out, not_6_out, F5, not_7_out, not_8_out, not_9_out, not_10_out, not_11_out);
  and and_2 (and_2_out, not_12_out, not_13_out, not_14_out, not_15_out, not_16_out, not_17_out, F5, not_18_out, not_19_out, not_20_out, not_21_out, F0);
  and and_3 (and_3_out, not_22_out, not_23_out, not_24_out, not_25_out, not_26_out, not_27_out, F5, not_28_out, not_29_out, not_30_out, F1, not_31_out);
  and and_4 (and_4_out, not_32_out, not_33_out, not_34_out, not_35_out, not_36_out, not_37_out, F5, not_38_out, not_39_out, F2, not_40_out, not_41_out);
  and and_5 (and_5_out, not_42_out, not_43_out, not_44_out, not_45_out, not_46_out, not_47_out, F5, not_48_out, not_49_out, F2, not_50_out, F0);
  and and_6 (and_6_out, not_51_out, not_52_out, not_53_out, not_54_out, not_55_out, not_56_out, F5, not_57_out, not_58_out, F2, F1, F0);
  and and_7 (and_7_out, not_59_out, not_60_out, not_61_out, not_62_out, not_63_out, not_64_out, F5, not_65_out, F3, not_66_out, F1, not_67_out);
  and and_8 (and_8_out, not_68_out, not_69_out, not_70_out, not_71_out, not_72_out, not_73_out, F5, not_74_out, F3, not_75_out, F1, F0);
  and and_9 (and_9_out, not_76_out, not_77_out, not_78_out, not_79_out, not_80_out, not_81_out, not_82_out, not_83_out, F3, not_84_out, not_85_out, not_86_out);
  and and_10 (and_10_out, not_87_out, not_88_out, not_89_out, not_90_out, not_91_out, not_92_out, not_93_out, not_94_out, F3, F2, not_95_out, not_96_out);
  and and_11 (and_11_out, not_97_out, not_98_out, not_99_out, OP2, not_100_out, not_101_out);
  and and_12 (and_12_out, not_102_out, not_103_out, not_104_out, OP2, not_105_out, OP0);
  and and_13 (and_13_out, not_106_out, not_107_out, OP3, not_108_out, not_109_out, not_110_out);
  and and_14 (and_14_out, not_111_out, not_112_out, OP3, OP2, not_113_out, not_114_out);
  and and_15 (and_15_out, not_115_out, not_116_out, OP3, not_117_out, not_118_out, OP0);
  and and_16 (and_16_out, not_119_out, not_120_out, OP3, not_121_out, OP1, not_122_out);
  and and_17 (and_17_out, not_123_out, not_124_out, OP3, OP2, not_125_out, OP0);
  and and_18 (and_18_out, OP5, not_126_out, not_127_out, not_128_out, OP1, OP0);
  and and_19 (and_19_out, OP5, not_129_out, OP3, not_130_out, OP1, OP0);
  and and_20 (and_20_out, not_131_out, not_132_out, not_133_out, not_134_out, not_135_out, not_136_out, F5, not_137_out, not_138_out, F2, F1, not_139_out);
  and and_21 (and_21_out, not_140_out, not_141_out, OP3, not_142_out, OP1, OP0);
  and and_22 (and_22_out, OP5, not_143_out, OP3, not_144_out, not_145_out, not_146_out);
  and and_23 (and_23_out, not_147_out, not_148_out, not_149_out, not_150_out, not_151_out, OP0);
  and and_24 (and_24_out, not_152_out, not_153_out, not_154_out, not_155_out, not_156_out, not_157_out, not_158_out, not_159_out, not_160_out, not_161_out, not_162_out, not_163_out);
  and and_25 (and_25_out, not_164_out, not_165_out, not_166_out, not_167_out, not_168_out, not_169_out, not_170_out, not_171_out, not_172_out, not_173_out, F1, F0);
  and and_26 (and_26_out, not_174_out, not_175_out, not_176_out, not_177_out, not_178_out, not_179_out, not_180_out, not_181_out, not_182_out, not_183_out, F1, not_184_out);
  and and_27 (and_27_out, not_185_out, not_186_out, not_187_out, not_188_out, not_189_out, not_190_out, F5, not_191_out, not_192_out, not_193_out, not_194_out, not_195_out);
  and and_28 (and_28_out, not_196_out, not_197_out, not_198_out, not_199_out, not_200_out, not_201_out, F5, not_202_out, not_203_out, not_204_out, not_205_out, F0);
  and and_29 (and_29_out, not_206_out, not_207_out, not_208_out, not_209_out, not_210_out, not_211_out, F5, not_212_out, not_213_out, not_214_out, F1, not_215_out);
  and and_30 (and_30_out, not_216_out, not_217_out, not_218_out, not_219_out, not_220_out, not_221_out, F5, not_222_out, not_223_out, F2, not_224_out, not_225_out);
  and and_31 (and_31_out, not_226_out, not_227_out, not_228_out, not_229_out, not_230_out, not_231_out, F5, not_232_out, not_233_out, F2, not_234_out, F0);
  and and_32 (and_32_out, not_235_out, not_236_out, not_237_out, not_238_out, not_239_out, not_240_out, F5, not_241_out, not_242_out, F2, F1, F0);
  and and_33 (and_33_out, not_243_out, not_244_out, not_245_out, not_246_out, not_247_out, not_248_out, F5, not_249_out, F3, not_250_out, F1, not_251_out);
  and and_34 (and_34_out, not_252_out, not_253_out, not_254_out, not_255_out, not_256_out, not_257_out, F5, not_258_out, F3, not_259_out, F1, F0);
  and and_35 (and_35_out, not_260_out, not_261_out, not_262_out, not_263_out, not_264_out, not_265_out, not_266_out, not_267_out, F3, F2, not_268_out, not_269_out);
  and and_36 (and_36_out, not_270_out, not_271_out, not_272_out, OP2, not_273_out, not_274_out);
  and and_37 (and_37_out, not_275_out, not_276_out, not_277_out, OP2, not_278_out, OP0);
  and and_38 (and_38_out, OP5, not_279_out, OP3, not_280_out, OP1, OP0);
  and and_39 (and_39_out, not_281_out, not_282_out, not_283_out, not_284_out, not_285_out, not_286_out, F5, not_287_out, not_288_out, F2, F1, not_289_out);
  and and_40 (and_40_out, OP5, not_290_out, OP3, not_291_out, not_292_out, not_293_out);
  or or_1 (RS, and_1_out, and_2_out, and_3_out, and_4_out, and_5_out, and_6_out, and_7_out, and_8_out, and_9_out, and_10_out, and_11_out, and_12_out, and_13_out, and_14_out, and_15_out, and_16_out, and_17_out, and_18_out, and_19_out, and_20_out, and_21_out, and_22_out, and_23_out);
  or or_2 (RT, and_24_out, and_25_out, and_26_out, and_27_out, and_28_out, and_29_out, and_30_out, and_31_out, and_32_out, and_33_out, and_34_out, and_35_out, and_36_out, and_37_out, and_38_out, and_39_out, and_40_out);
endmodule

module \栈  (
  input  [1:0] INPUT,
  input  clk,
  input  \int ,
  input  eret,
  output [1:0] out_5
);

  wire and_1_out, and_2_out, and_3_out, and_4_out, and_5_out, and_6_out, not_1_out, not_2_out, not_3_out,
       not_4_out, or_1_out;
  wire [1:0] counter_1_q, demultiplexer_1_out0, demultiplexer_1_out1, demultiplexer_1_out2, s0_q, s1_q, s2_q,
       subtractor_1_out;

  or or_1 (or_1_out, \int , eret);
  Demultiplexer #(.select(2), .width(2), .tristate("false"), .disabled("Z"), .enable("false")) demultiplexer_1 (
    .out0(demultiplexer_1_out0), .out1(demultiplexer_1_out1), .out2(demultiplexer_1_out2), .in(INPUT),
    .sel(counter_1_q));  // open: out3
  Counter #(.width(2), .max('h3), .ongoal("wrap"), .trigger("rising"), .behavior("new")) counter_1 (
    .count(or_1_out), .Q(counter_1_q), .clk(clk), .down(eret));  // open: load, D, carry, clr, preset
  not not_1 (not_1_out, counter_1_q[1]);
  not not_2 (not_2_out, counter_1_q[0]);
  not not_3 (not_3_out, counter_1_q[1]);
  not not_4 (not_4_out, counter_1_q[0]);
  and and_1 (and_1_out, \int , and_2_out);
  and and_2 (and_2_out, not_1_out, not_2_out);
  and and_3 (and_3_out, not_3_out, counter_1_q[0]);
  and and_4 (and_4_out, counter_1_q[1], not_4_out);
  Register #(.width(2), .trigger("rising"), .Select("low")) s0 (
    .D(demultiplexer_1_out0), .en(and_1_out), .Q(s0_q), .clk(clk));  // open: clr
  Register #(.width(2), .trigger("rising"), .Select("low")) s1 (
    .D(demultiplexer_1_out1), .en(and_5_out), .Q(s1_q), .clk(clk));  // open: clr
  and and_5 (and_5_out, \int , and_3_out);
  Register #(.width(2), .trigger("rising"), .Select("low")) s2 (
    .D(demultiplexer_1_out2), .en(and_6_out), .Q(s2_q), .clk(clk));  // open: clr
  and and_6 (and_6_out, \int , and_4_out);
  Multiplexer #(.select(2), .width(2), .disabled("Z"), .enable("false")) multiplexer_1 (
    .in0(s0_q), .in1(s1_q), .in2(s2_q), .in3(2'b00), .out(out_5), .sel(subtractor_1_out));
  Subtractor #(.width(2)) subtractor_1 (.a(counter_1_q), .b(2'b01), .out(subtractor_1_out));  // open: bin, bout
endmodule

module \_2个随机数  (
  input  in_1,
  input  in_2,
  output [7:0] out_3
);

  wire clock_1_out, multiplexer_1_out;
  wire [7:0] \随机数电路_1_out_3 ;

  Clock #(.highDuration(1), .lowDuration(1)) clock_1 (.out(clock_1_out));
  Multiplexer #(.select(1), .width(1), .disabled("Z"), .enable("false")) multiplexer_1 (
    .in0(clock_1_out), .in1(in_1), .out(multiplexer_1_out), .sel(1'b1));
  \随机数电路  \u_随机数电路_1  (.in_1(multiplexer_1_out), .Reset(in_2), .out_3(\随机数电路_1_out_3 ));
  // Probe on \随机数电路_1_out_3 
  Divider #(.width(8)) divider_1 (.a(\随机数电路_1_out_3 ), .b(8'h2), .rem(out_3));  // open: out, upper
endmodule

module \_16个随机数  (
  input  in_1,
  input  in_2,
  output [7:0] out_3
);

  wire clock_1_out, multiplexer_1_out;
  wire [7:0] \随机数电路_1_out_3 ;

  Clock #(.highDuration(1), .lowDuration(1)) clock_1 (.out(clock_1_out));
  Multiplexer #(.select(1), .width(1), .disabled("Z"), .enable("false")) multiplexer_1 (
    .in0(clock_1_out), .in1(in_1), .out(multiplexer_1_out), .sel(1'b1));
  \随机数电路  \u_随机数电路_1  (.in_1(multiplexer_1_out), .Reset(in_2), .out_3(\随机数电路_1_out_3 ));
  // Probe on \随机数电路_1_out_3 
  Divider #(.width(8)) divider_1 (.a(\随机数电路_1_out_3 ), .b(8'h10), .rem(out_3));  // open: out, upper
endmodule

module \_4个随机数  (
  input  in_1,
  input  in_2,
  output [7:0] out_3
);

  wire clock_1_out, multiplexer_1_out;
  wire [7:0] \随机数电路_1_out_3 ;

  Clock #(.highDuration(1), .lowDuration(1)) clock_1 (.out(clock_1_out));
  Multiplexer #(.select(1), .width(1), .disabled("Z"), .enable("false")) multiplexer_1 (
    .in0(clock_1_out), .in1(in_1), .out(multiplexer_1_out), .sel(1'b1));
  \随机数电路  \u_随机数电路_1  (.in_1(multiplexer_1_out), .Reset(in_2), .out_3(\随机数电路_1_out_3 ));
  // Probe on \随机数电路_1_out_3 
  Divider #(.width(8)) divider_1 (.a(\随机数电路_1_out_3 ), .b(8'h4), .rem(out_3));  // open: out, upper
endmodule

module \显示电路  (
  input  [31:0] In1,
  input  [31:0] In17,
  input  [31:0] In2,
  input  [31:0] In18,
  input  [31:0] In3,
  input  [31:0] In19,
  input  [31:0] In4,
  input  [31:0] In20,
  input  [31:0] In5,
  input  [31:0] In21,
  input  [31:0] In6,
  input  [31:0] In22,
  input  [31:0] In7,
  input  [31:0] In23,
  input  [31:0] In8,
  input  [31:0] In24,
  input  [31:0] In9,
  input  [31:0] In25,
  input  [31:0] In10,
  input  [31:0] In26,
  input  [31:0] In11,
  input  [31:0] In27,
  input  [31:0] In12,
  input  [31:0] In28,
  input  [31:0] In13,
  input  [31:0] In29,
  input  [31:0] In14,
  input  [31:0] In30,
  input  [31:0] In15,
  input  [31:0] In31,
  input  [31:0] In16,
  input  [31:0] In32
);

  wire [31:0] \显示译码器_1_data1 , \显示译码器_1_data2 , \显示译码器_1_data3 , \显示译码器_1_data4 , \显示译码器_1_data5 ,
       \显示译码器_1_data6 , \显示译码器_1_data7 , \显示译码器_1_data8 , \显示译码器_1_data9 , \显示译码器_1_data10 ,
       \显示译码器_1_data11 , \显示译码器_1_data12 , \显示译码器_1_data13 , \显示译码器_1_data14 , \显示译码器_1_data15 ,
       \显示译码器_1_data16 , \显示译码器_1_data17 , \显示译码器_1_data18 , \显示译码器_1_data19 , \显示译码器_1_data20 ,
       \显示译码器_1_data21 , \显示译码器_1_data22 , \显示译码器_1_data23 , \显示译码器_1_data24 , \显示译码器_1_data25 ,
       \显示译码器_1_data26 , \显示译码器_1_data27 , \显示译码器_1_data28 , \显示译码器_1_data29 , \显示译码器_1_data30 ,
       \显示译码器_1_data31 , \显示译码器_1_data32 ;

  // Probe on In1
  // Probe on In2
  // Probe on In3
  // Probe on In4
  // Probe on In5
  // Probe on In6
  // Probe on In7
  // Probe on In8
  // Probe on In9
  // Probe on In10
  // Probe on In11
  // Probe on In12
  // Probe on In13
  DotMatrix #(.inputtype("column"), .matrixcols(32), .matrixrows(32), .persist(0), .dotshape("square")) dotmatrix_1 (
    .col0(In1), .col1(In2), .col2(In3), .col3(In4), .col4(In5), .col5(In6), .col6(In7), .col7(In8),
    .col8(In9), .col9(In10), .col10(In11), .col11(In12), .col12(In13), .col13(In14), .col14(In15),
    .col15(In16), .col16(In17), .col17(In18), .col18(In19), .col19(In20), .col20(In21), .col21(In22),
    .col22(In23), .col23(In24), .col24(In25), .col25(In26), .col26(In27), .col27(In28), .col28(In29),
    .col29(In30), .col30(In31), .col31(In32));
  DotMatrix #(.inputtype("column"), .matrixcols(32), .matrixrows(32), .persist(0), .dotshape("square")) dotmatrix_2 (
    .col0(\显示译码器_1_data1 ), .col1(\显示译码器_1_data2 ), .col2(\显示译码器_1_data3 ), .col3(\显示译码器_1_data4 ),
    .col4(\显示译码器_1_data5 ), .col5(\显示译码器_1_data6 ), .col6(\显示译码器_1_data7 ), .col7(\显示译码器_1_data8 ),
    .col8(\显示译码器_1_data9 ), .col9(\显示译码器_1_data10 ), .col10(\显示译码器_1_data11 ), .col11(\显示译码器_1_data12 ),
    .col12(\显示译码器_1_data13 ), .col13(\显示译码器_1_data14 ), .col14(\显示译码器_1_data15 ), .col15(\显示译码器_1_data16 ),
    .col16(\显示译码器_1_data17 ), .col17(\显示译码器_1_data18 ), .col18(\显示译码器_1_data19 ), .col19(\显示译码器_1_data20 ),
    .col20(\显示译码器_1_data21 ), .col21(\显示译码器_1_data22 ), .col22(\显示译码器_1_data23 ), .col23(\显示译码器_1_data24 ),
    .col24(\显示译码器_1_data25 ), .col25(\显示译码器_1_data26 ), .col26(\显示译码器_1_data27 ), .col27(\显示译码器_1_data28 ),
    .col28(\显示译码器_1_data29 ), .col29(\显示译码器_1_data30 ), .col30(\显示译码器_1_data31 ), .col31(\显示译码器_1_data32 ));
  \显示译码器  \u_显示译码器_1  (
    .\input (32'h800), .data1(\显示译码器_1_data1 ), .data9(\显示译码器_1_data9 ), .data17(\显示译码器_1_data17 ),
    .data25(\显示译码器_1_data25 ), .data2(\显示译码器_1_data2 ), .data10(\显示译码器_1_data10 ), .data18(\显示译码器_1_data18 ),
    .data26(\显示译码器_1_data26 ), .data3(\显示译码器_1_data3 ), .data11(\显示译码器_1_data11 ), .data19(\显示译码器_1_data19 ),
    .data27(\显示译码器_1_data27 ), .data4(\显示译码器_1_data4 ), .data12(\显示译码器_1_data12 ), .data20(\显示译码器_1_data20 ),
    .data28(\显示译码器_1_data28 ), .data5(\显示译码器_1_data5 ), .data13(\显示译码器_1_data13 ), .data21(\显示译码器_1_data21 ),
    .data29(\显示译码器_1_data29 ), .data6(\显示译码器_1_data6 ), .data14(\显示译码器_1_data14 ), .data22(\显示译码器_1_data22 ),
    .data30(\显示译码器_1_data30 ), .data7(\显示译码器_1_data7 ), .data15(\显示译码器_1_data15 ), .data23(\显示译码器_1_data23 ),
    .data31(\显示译码器_1_data31 ), .data8(\显示译码器_1_data8 ), .data16(\显示译码器_1_data16 ), .data24(\显示译码器_1_data24 ),
    .data32(\显示译码器_1_data32 ));
endmodule

// LED Decoder
module \显示译码器  (
  input  [31:0] \input ,
  output [31:0] data1,
  output [31:0] data9,
  output [31:0] data17,
  output [31:0] data25,
  output [31:0] data2,
  output [31:0] data10,
  output [31:0] data18,
  output [31:0] data26,
  output [31:0] data3,
  output [31:0] data11,
  output [31:0] data19,
  output [31:0] data27,
  output [31:0] data4,
  output [31:0] data12,
  output [31:0] data20,
  output [31:0] data28,
  output [31:0] data5,
  output [31:0] data13,
  output [31:0] data21,
  output [31:0] data29,
  output [31:0] data6,
  output [31:0] data14,
  output [31:0] data22,
  output [31:0] data30,
  output [31:0] data7,
  output [31:0] data15,
  output [31:0] data23,
  output [31:0] data31,
  output [31:0] data8,
  output [31:0] data16,
  output [31:0] data24,
  output [31:0] data32
);

  wire [7:0] addr;

  input_to_addr input_to_addr_1 (.in_1(\input ), .out_2(addr));
  ROM #(.addrWidth(8), .dataWidth(32), .Select("low")) rom_1 (.addr(addr), .data(data1));
  ROM #(.addrWidth(8), .dataWidth(32), .Select("low")) rom_2 (.addr(addr), .data(data2));
  ROM #(.addrWidth(8), .dataWidth(32), .Select("low")) rom_3 (.addr(addr), .data(data3));
  ROM #(.addrWidth(8), .dataWidth(32), .Select("low")) rom_4 (.addr(addr), .data(data4));
  ROM #(.addrWidth(8), .dataWidth(32), .Select("low")) rom_5 (.addr(addr), .data(data5));
  ROM #(.addrWidth(8), .dataWidth(32), .Select("low")) rom_6 (.addr(addr), .data(data6));
  ROM #(.addrWidth(8), .dataWidth(32), .Select("low")) rom_7 (.addr(addr), .data(data7));
  ROM #(.addrWidth(8), .dataWidth(32), .Select("low")) rom_8 (.addr(addr), .data(data8));
  ROM #(.addrWidth(8), .dataWidth(32), .Select("low")) rom_9 (.addr(addr), .data(data9));
  ROM #(.addrWidth(8), .dataWidth(32), .Select("low")) rom_10 (.addr(addr), .data(data10));
  ROM #(.addrWidth(8), .dataWidth(32), .Select("low")) rom_11 (.addr(addr), .data(data11));
  ROM #(.addrWidth(8), .dataWidth(32), .Select("low")) rom_12 (.addr(addr), .data(data12));
  ROM #(.addrWidth(8), .dataWidth(32), .Select("low")) rom_13 (.addr(addr), .data(data13));
  ROM #(.addrWidth(8), .dataWidth(32), .Select("low")) rom_14 (.addr(addr), .data(data14));
  ROM #(.addrWidth(8), .dataWidth(32), .Select("low")) rom_15 (.addr(addr), .data(data15));
  ROM #(.addrWidth(8), .dataWidth(32), .Select("low")) rom_16 (.addr(addr), .data(data16));
  ROM #(.addrWidth(8), .dataWidth(32), .Select("low")) rom_17 (.addr(addr), .data(data17));
  ROM #(.addrWidth(8), .dataWidth(32), .Select("low")) rom_18 (.addr(addr), .data(data18));
  ROM #(.addrWidth(8), .dataWidth(32), .Select("low")) rom_19 (.addr(addr), .data(data19));
  ROM #(.addrWidth(8), .dataWidth(32), .Select("low")) rom_20 (.addr(addr), .data(data20));
  ROM #(.addrWidth(8), .dataWidth(32), .Select("low")) rom_21 (.addr(addr), .data(data21));
  ROM #(.addrWidth(8), .dataWidth(32), .Select("low")) rom_22 (.addr(addr), .data(data22));
  ROM #(.addrWidth(8), .dataWidth(32), .Select("low")) rom_23 (.addr(addr), .data(data23));
  ROM #(.addrWidth(8), .dataWidth(32), .Select("low")) rom_24 (.addr(addr), .data(data24));
  ROM #(.addrWidth(8), .dataWidth(32), .Select("low")) rom_25 (.addr(addr), .data(data25));
  ROM #(.addrWidth(8), .dataWidth(32), .Select("low")) rom_26 (.addr(addr), .data(data26));
  ROM #(.addrWidth(8), .dataWidth(32), .Select("low")) rom_27 (.addr(addr), .data(data27));
  ROM #(.addrWidth(8), .dataWidth(32), .Select("low")) rom_28 (.addr(addr), .data(data28));
  ROM #(.addrWidth(8), .dataWidth(32), .Select("low")) rom_29 (.addr(addr), .data(data29));
  ROM #(.addrWidth(8), .dataWidth(32), .Select("low")) rom_30 (.addr(addr), .data(data30));
  ROM #(.addrWidth(8), .dataWidth(32), .Select("low")) rom_31 (.addr(addr), .data(data31));
  ROM #(.addrWidth(8), .dataWidth(32), .Select("low")) rom_32 (.addr(addr), .data(data32));

  // Notes on the sheet:
  //   8 -> 04
  //   16 -> 05
  //   32 -> 06
  //   64 -> 07
  //   128 -> 08
  //   256 -> 09
  //   512 -> 0a
  //   1024 -> 0b
  //   2048 -> 0c
  //   4096 -> 0d
  //   8192 -> 0e
  //   0 -> 00
  //   1 -> 01
  //   2 -> 02
  //   4 -> 03
  //   contents of rom_2 (hex, n*v repeats v):
  //   12*0 c01800
  //   contents of rom_3 (hex, n*v repeats v):
  //   9*0 380700 0 0 1807800
  //   contents of rom_4 (hex, n*v repeats v):
  //   7*0 7ff00 0 600f00 0 7ffe00 101c800
  //   contents of rom_5 (hex, n*v repeats v):
  //   5*0 1000040 600c00 1fff80 1fffc00 c01900 0 0 1070800
  //   contents of rom_6 (hex, n*v repeats v):
  //   5*0 2000040 c00600 7f01c0 0 803100 ff8600 0 18c0800
  //   contents of rom_7 (hex, n*v repeats v):
  //   0 0 0 38000 0 7ffffc0 1800300 e200c0 0 806100 830300 3ffc00 f80800
  //   contents of rom_8 (hex, n*v repeats v):
  //   0 0 0 f8000 0 7ffffc0 1010100 1820040 0 80c100 820100 400200
  //   contents of rom_9 (hex, n*v repeats v):
  //   0 0 0 3f8000 0 40 1010100 3020040 0 c18100 820100 400200
  //   contents of rom_10 (hex, n*v repeats v):
  //   0 0 e00060 1f98000 0 40 1010100 2020040 600c00 630100 820100 400200 fff000
  //   contents of rom_11 (hex, n*v repeats v):
  //   0 0 1e001e0 7818000 f81f00 0 1838300 20200c0 c03c00 3e0100 830300 400200 1000800
  //   contents of rom_12 (hex, n*v repeats v):
  //   0 600030 3c003e0 e018000 18c3180 0 c6c600 20301c0 180e400 0 81fe00 3ffc00 1000800
  //   contents of rom_13 (hex, n*v repeats v):
  //   0 c00030 78007e0 18000 30660c0 0 7c7c00 203ff80 1018400 0 0 0 1000800
  //   contents of rom_14 (hex, n*v repeats v):
  //   0 1800030 7000e60 18000 603c060 0 0 1ff00 1030400 ffc600 0 0 fff000
  //   contents of rom_15 (hex, n*v repeats v):
  //   0 3fffff0 6001c60 18000 6018060 0 0 0 1020400 818300 0 300600
  //   contents of rom_16 (hex, n*v repeats v):
  //   0 3fffff0 6003860 fffffc0 4018020 0 0 0 1860400 810100 ffff00 601e00
  //   contents of rom_17 (hex, n*v repeats v):
  //   0 30 6007060 fffffc0 4018020 fff00 0 38000 cc0400 810100 0 407200
  //   contents of rom_18 (hex, n*v repeats v):
  //   0 30 600e060 18000 6018060 7fff80 0 f8000 780400 810100 0 41c200 1ff0000
  //   contents of rom_19 (hex, n*v repeats v):
  //   0 30 701c060 18000 603c060 1ff01c0 300f00 3d8000 0 810100 0 630200 10000
  //   contents of rom_20 (hex, n*v repeats v):
  //   0 0 7038060 18000 30660c0 3c200c0 601f00 f18000 0 818300 380700 3e0200 10000
  //   contents of rom_21 (hex, n*v repeats v):
  //   0 0 3ff0060 18000 18c3180 7020040 c03300 1c18000 0 fe00 600f00 0 10000
  //   contents of rom_22 (hex, n*v repeats v):
  //   0 0 1fc0060 0 f81f00 6020040 1806300 3818000 fdf800 0 c01900 0 1fff800
  //   contents of rom_23 (hex, n*v repeats v):
  //   0 0 780060 0 0 6020040 100c300 18000 1020400 0 803100 7fc000 10000
  //   contents of rom_24 (hex, n*v repeats v):
  //   0 0 60 0 0 40200c0 1018300 3ffffc0 1020400 3ffe00 806100 4000 10000
  //   contents of rom_25 (hex, n*v repeats v):
  //   5*0 40301c0 1030300 3ffffc0 1020400 60c300 80c100 4000
  //   contents of rom_26 (hex, n*v repeats v):
  //   5*0 403ff80 1860300 18000 1020400 c08100 c18100 4000
  //   contents of rom_27 (hex, n*v repeats v):
  //   5*0 1ff00 cc0300 18000 1020400 808100 630100 7ffe00 fdf000
  //   contents of rom_28 (hex, n*v repeats v):
  //   6*0 780300 18000 fdf800 808100 3e0100 4000 1020800
  //   contents of rom_29 (hex, n*v repeats v):
  //   7*0 18000 0 808100 0 4000 1020800
  //   contents of rom_30 (hex, n*v repeats v):
  //   9*0 c0c300 0 0 1020800
  //   contents of rom_31 (hex, n*v repeats v):
  //   9*0 7e00 0 0 fdf000
endmodule

module input_to_addr (
  input  [31:0] in_1,
  output [7:0] out_2
);

  wire comparator_1_eq;

  // Probe on in_1
  Comparator #(.width(32), .mode("twosComplement")) comparator_1 (
    .a(in_1), .b({32{1'b0}}), .eq(comparator_1_eq));  // open: gt, lt
  assign out_2 = comparator_1_eq ? {8{1'b0}} : 8'bz;  // Controlled_Buffer controlled_buffer_1
  assign out_2 = in_1[0] ? 8'h1 : 8'bz;  // Controlled_Buffer controlled_buffer_2
  assign out_2 = in_1[1] ? 8'h2 : 8'bz;  // Controlled_Buffer controlled_buffer_3
  assign out_2 = in_1[2] ? 8'h3 : 8'bz;  // Controlled_Buffer controlled_buffer_4
  assign out_2 = in_1[3] ? 8'h4 : 8'bz;  // Controlled_Buffer controlled_buffer_5
  assign out_2 = in_1[4] ? 8'h5 : 8'bz;  // Controlled_Buffer controlled_buffer_6
  assign out_2 = in_1[5] ? 8'h6 : 8'bz;  // Controlled_Buffer controlled_buffer_7
  assign out_2 = in_1[6] ? 8'h7 : 8'bz;  // Controlled_Buffer controlled_buffer_8
  assign out_2 = in_1[7] ? 8'h8 : 8'bz;  // Controlled_Buffer controlled_buffer_9
  assign out_2 = in_1[8] ? 8'h9 : 8'bz;  // Controlled_Buffer controlled_buffer_10
  assign out_2 = in_1[9] ? 8'ha : 8'bz;  // Controlled_Buffer controlled_buffer_11
  assign out_2 = in_1[10] ? 8'hb : 8'bz;  // Controlled_Buffer controlled_buffer_12
  assign out_2 = in_1[11] ? 8'hc : 8'bz;  // Controlled_Buffer controlled_buffer_13
  assign out_2 = in_1[12] ? 8'hd : 8'bz;  // Controlled_Buffer controlled_buffer_14
endmodule

module ram (
  input  clr,
  input  CLK,
  input  str,
  input  [31:0] data,
  input  [9:0] in_5,
  input  [9:0] in_6,
  input  [9:0] in_7,
  input  [9:0] in_8,
  input  [9:0] in_9,
  input  [9:0] in_10,
  input  [9:0] in_11,
  input  [9:0] in_12,
  input  [9:0] in_13,
  input  [9:0] in_14,
  input  [9:0] in_15,
  input  [9:0] in_16,
  input  [9:0] in_17,
  input  [9:0] in_18,
  input  [9:0] in_19,
  input  [9:0] in_20,
  input  [9:0] in_21,
  input  [9:0] in_22,
  input  [9:0] in_23,
  input  [9:0] in_24,
  output [31:0] out_25,
  output [31:0] out_26,
  output [31:0] out_27,
  output [31:0] out_28,
  output [31:0] out_29,
  output [31:0] out_30,
  output [31:0] out_31,
  output [31:0] out_32,
  output [31:0] out_33,
  output [31:0] out_34,
  output [31:0] out_35,
  output [31:0] out_36,
  output [31:0] out_37,
  output [31:0] out_38,
  output [31:0] out_39,
  output [31:0] out_40,
  output [31:0] out_41,
  output [31:0] out_42,
  output [31:0] out_43,
  output [31:0] out_44
);

  RAM ram_1 (
    .ADDR(in_9), .in_5(data), .in_7(CLK), .in_8(str), .in_9(data), .in_10(str), .in_11(str), .in_12(str),
    .in_13(str), .in_14(data), .in_16(data), .in_17(data), .in_23(data), .in_24(str), .in_25(str),
    .in_26(str), .in_27(data), .in_28(str), .in_29(str), .in_30(data), .in_31(data), .in_32(data),
    .in_37(data), .in_39(str), .in_40(str), .in_41(data), .in_42(str), .in_43(str), .in_44(str),
    .in_45(data), .in_46(data), .in_51(data), .in_53(data), .in_54(str), .in_55(str), .in_56(str),
    .in_57(str), .in_58(str), .in_59(data), .in_60(data), .in_61(data), .in_62(data), .out_63(out_25),
    .out_64(out_26), .out_65(out_27), .out_66(out_28), .out_67(out_29), .out_68(out_30), .out_69(out_31),
    .out_70(out_32), .out_71(out_33), .out_72(out_34), .out_73(out_35), .out_74(out_36), .out_75(out_37),
    .out_76(out_38), .out_77(out_39), .out_78(out_40), .out_79(out_41), .out_80(out_42), .out_81(out_43),
    .out_82(out_44), .ADDR_2(in_8), .ADDR_3(in_7), .ADDR_4(in_6), .ADDR_5(in_5), .ADDR_6(in_14),
    .ADDR_7(in_13), .ADDR_8(in_12), .ADDR_9(in_11), .ADDR_10(in_10), .ADDR_11(in_19), .ADDR_12(in_18),
    .ADDR_13(in_17), .ADDR_14(in_16), .ADDR_15(in_15), .ADDR_16(in_24), .ADDR_17(in_23), .ADDR_18(in_22),
    .ADDR_19(in_21), .ADDR_20(in_20), .in_15(clr));
endmodule
