// Logisim project 中断.circ as structural Verilog: 1 circuit, main circuit 中断按键
module \中断按键  (
  input  [31:0] epc_next,
  input  CLK,
  input  IR1,
  input  IR2,
  input  ERET,
  input  IR3,
  input  IR4,
  input  [31:0] IR1_Addr,
  input  [31:0] IR2_Addr,
  input  [31:0] IR3_Addr,
  input  [31:0] IR4_Addr,
  output W1,
  output W2,
  output [31:0] addr,
  output W3,
  output W4
);

  wire and_1_out, and_2_out, and_3_out, and_4_out, and_5_out, and_6_out, d_ff_1_q, d_ff_2_q, d_ff_3_q,
       d_ff_4_q, d_ff_5_q, d_ff_6_q, d_ff_7_q, d_ff_8_q, d_ff_9_qn, or_1_out, or_2_out, or_3_out, or_4_out,
       priority_encoder_1_gs;
  wire [1:0] priority_encoder_1_out;
  wire [31:0] epc_out, multiplexer_1_out, multiplexer_2_out;

  D_Flip_Flop #(.trigger("rising"), .Pre_Clr_Positions("LEGACY"), .NegatePresetClear("false"), .enable("true"), .NewFFLayout("false")) d_ff_1 (
    .clk(IR1), .D(1'b1), .Q(d_ff_1_q), .reset(d_ff_5_q));  // open: Qn, preset, en
  D_Flip_Flop #(.trigger("rising"), .Pre_Clr_Positions("LEGACY"), .NegatePresetClear("false"), .enable("true"), .NewFFLayout("false")) d_ff_2 (
    .clk(IR2), .D(1'b1), .Q(d_ff_2_q), .reset(d_ff_6_q));  // open: Qn, preset, en
  D_Flip_Flop #(.trigger("rising"), .Pre_Clr_Positions("LEGACY"), .NegatePresetClear("false"), .enable("true"), .NewFFLayout("false")) d_ff_3 (
    .clk(IR3), .D(1'b1), .Q(d_ff_3_q), .reset(d_ff_7_q));  // open: Qn, preset, en
  D_Flip_Flop #(.trigger("rising"), .Pre_Clr_Positions("LEGACY"), .NegatePresetClear("false"), .enable("true"), .NewFFLayout("false")) d_ff_4 (
    .clk(IR4), .D(1'b1), .Q(d_ff_4_q), .reset(d_ff_8_q));  // open: Qn, preset, en
  or or_1 (or_1_out, d_ff_1_q, d_ff_5_q);
  or or_2 (or_2_out, d_ff_2_q, d_ff_6_q);
  or or_3 (or_3_out, d_ff_3_q, d_ff_7_q);
  or or_4 (or_4_out, d_ff_4_q, d_ff_8_q);
  and and_1 (and_1_out, ~ERET, or_1_out);  // AND_Gate
  and and_2 (and_2_out, ~ERET, or_2_out);  // AND_Gate
  and and_3 (and_3_out, ~ERET, or_3_out);  // AND_Gate
  and and_4 (and_4_out, ~ERET, or_4_out);  // AND_Gate
  D_Flip_Flop #(.trigger("rising"), .Pre_Clr_Positions("LEGACY"), .NegatePresetClear("false"), .enable("true"), .NewFFLayout("false")) d_ff_5 (
    .clk(CLK), .D(and_1_out), .Q(d_ff_5_q));  // open: Qn, preset, en, reset
  D_Flip_Flop #(.trigger("rising"), .Pre_Clr_Positions("LEGACY"), .NegatePresetClear("false"), .enable("true"), .NewFFLayout("false")) d_ff_6 (
    .clk(CLK), .D(and_2_out), .Q(d_ff_6_q));  // open: Qn, preset, en, reset
  D_Flip_Flop #(.trigger("rising"), .Pre_Clr_Positions("LEGACY"), .NegatePresetClear("false"), .enable("true"), .NewFFLayout("false")) d_ff_7 (
    .clk(CLK), .D(and_3_out), .Q(d_ff_7_q));  // open: Qn, preset, en, reset
  D_Flip_Flop #(.trigger("rising"), .Pre_Clr_Positions("LEGACY"), .NegatePresetClear("false"), .enable("true"), .NewFFLayout("false")) d_ff_8 (
    .clk(CLK), .D(and_4_out), .Q(d_ff_8_q));  // open: Qn, preset, en, reset
  or or_5 (W1, d_ff_5_q, d_ff_1_q);
  or or_6 (W2, d_ff_6_q, d_ff_2_q);
  or or_7 (W3, d_ff_7_q, d_ff_3_q);
  or or_8 (W4, d_ff_8_q, d_ff_4_q);
  Priority_Encoder #(.select(2), .disabled("Z")) priority_encoder_1 (
    .in0(d_ff_5_q), .in1(d_ff_6_q), .in2(d_ff_7_q), .in3(d_ff_8_q), .out(priority_encoder_1_out),
    .gs(priority_encoder_1_gs));  // open: en_out, en_in
  Multiplexer #(.select(2), .width(32), .disabled("Z"), .enable("false")) multiplexer_1 (
    .in0(IR1_Addr), .in1(IR2_Addr), .in2(IR3_Addr), .in3(IR4_Addr), .out(multiplexer_1_out),
    .sel(priority_encoder_1_out));
  and and_5 (and_5_out, priority_encoder_1_gs, ~ERET);  // AND_Gate
  D_Flip_Flop #(.trigger("rising"), .Pre_Clr_Positions("LEGACY"), .NegatePresetClear("false"), .enable("true"), .NewFFLayout("false")) d_ff_9 (
    .clk(CLK), .D(and_5_out), .Qn(d_ff_9_qn));  // open: Q, preset, en, reset
  and and_6 (and_6_out, d_ff_9_qn, priority_encoder_1_gs);
  Multiplexer #(.select(1), .width(32), .disabled("Z"), .enable("false")) multiplexer_2 (
    .in0(epc_next), .in1(epc_out), .out(multiplexer_2_out), .sel(ERET));
  Multiplexer #(.select(1), .width(32), .disabled("Z"), .enable("false")) multiplexer_3 (
    .in0(multiplexer_2_out), .in1(multiplexer_1_out), .out(addr), .sel(and_6_out));
  Register #(.width(32), .trigger("rising"), .Select("low")) register_1 (
    .D(multiplexer_2_out), .en(and_6_out), .Q(epc_out), .clk(CLK));  // open: clr

  // Other names for the same wires on the sheet: Clr1 = ERET; Clr2 = ERET; Clr3 = ERET; Clr4 = ERET
endmodule
