// Logisim project 随机数生成.circ as structural Verilog: 2 circuits, main circuit 自定义随机数电路
module \自定义随机数电路  (
  input  in_1,
  input  in_2,
  input  in_3,
  output [7:0] out_4
);

  wire clock_1_out, comparator_1_eq, multiplexer_1_out, not_1_out;
  wire [0:0] shifter_1_out;
  wire [7:0] multiplexer_2_out, register_1_q;

  Clock #(.highDuration(1), .lowDuration(1)) clock_1 (.out(clock_1_out));
  not not_1 (not_1_out, in_2);
  Multiplexer #(.select(1), .width(1), .disabled("Z"), .enable("false")) multiplexer_1 (
    .in0(clock_1_out), .in1(in_3), .out(multiplexer_1_out), .sel(1'b1));
  Comparator #(.width(8), .mode("twosComplement")) comparator_1 (
    .a({8{1'b0}}), .b(register_1_q), .eq(comparator_1_eq));  // open: gt, lt
  Register #(.width(8), .trigger("rising"), .Select("low")) register_1 (
    .D(out_4), .en(not_1_out), .Q(register_1_q), .clk(multiplexer_1_out), .preset(in_1));  // open: clr, cs
  Multiplexer #(.select(1), .width(8), .disabled("Z"), .enable("false")) multiplexer_2 (
    .in0(register_1_q), .in1({8{1'b1}}), .out(multiplexer_2_out), .sel(comparator_1_eq));
  Shifter #(.width(8), .shift("ll")) shifter_1 (
    .in(multiplexer_2_out), .\dist (3'b001), .out({out_4[7:1], shifter_1_out[0]}));
  xor xor_1 (out_4[0], out_4[1], out_4[2], out_4[3], out_4[7]);
endmodule

module \随机数电路  (
  input  in_1,
  input  Reset,
  output [7:0] out_3
);

  wire clock_1_out, multiplexer_1_out;

  Clock #(.highDuration(1), .lowDuration(1)) clock_1 (.out(clock_1_out));
  Multiplexer #(.select(1), .width(1), .disabled("Z"), .enable("false")) multiplexer_1 (
    .in0(clock_1_out), .in1(in_1), .out(multiplexer_1_out), .sel(1'b1));
  Random #(.width(8), .seed(0), .trigger("rising")) random_1 (
    .clk(multiplexer_1_out), .next(1'b1), .out(out_3), .clr(Reset));
endmodule
